// Logisim project Z80_ProcessorV3.circ as structural Verilog: 19 circuits, main circuit main
module main (
  input  [7:0] in_1,
  input  [7:0] in_2,
  input  INT,
  input  NMI,
  input  BUSRQ,
  output IORQ,
  output [7:0] out_7,
  output BUSACK
);

  // Probe on in_1
  // Probe on in_2
  Adder adder_1 (.a(in_1), .b(in_2), .out(out_7));  // open: cin, cout
  // Probe on out_7
endmodule

module FPGA (
  input  Reset,
  input  OnB,
  input  Off
);

  wire and_5_out, and_7_out, and_8_out, and_10_out, clock_1_out, decoder_1_out0, decoder_1_out1,
       decoder_1_out2, keyboard_1_avail, not_1_out, Processor_1_err, Processor_1_exe, Processor_1_halt,
       Processor_1_iorq, Processor_1_mreq, Processor_1_rd, Processor_1_wr, s_r_ff_1_q, W_out;
  wire [3:0] shift_register_1_out, shift_register_1_out_2, shift_register_1_q0, shift_register_1_q0_2,
       shift_register_1_q1, shift_register_1_q1_2;
  wire [6:0] bit_extender_2_out, keyboard_1_data;
  wire [7:0] and_1_out, and_6_out, bit_extender_1_out, or_1_out, Processor_1_dataout, RAM_1_dout;
  wire [7:7] and_2_out, and_9_out;
  wire [15:0] Processor_1_adress;

  Clock clock_1 (.out(clock_1_out));
  RAM #(.addrWidth(16), .\type ("nonvolatile")) RAM_1 (
    .addr(Processor_1_adress), .we(and_10_out), .oe(Processor_1_mreq), .clk(clock_1_out),
    .din(Processor_1_dataout), .dout(RAM_1_dout));
  Decoder #(.select(5)) decoder_1 (
    .out0(decoder_1_out0), .out1(decoder_1_out1), .out2(decoder_1_out2), .sel(Processor_1_adress[4:0]),
    .en(Processor_1_iorq));  // open: out3, out4, out5, out6, out7, out8, out9, out10, out11, out12, out13, out14, out15, out16, out17, out18, out19, out20, out21, out22, out23, out24, out25, out26, out27, out28, out29, out30, out31
  S_R_Flip_Flop s_r_ff_1 (.S(OnB), .clk(clock_1_out), .R(Off), .Q(s_r_ff_1_q));  // open: Qn, preset, reset
  assign and_1_out = RAM_1_dout & {8{and_9_out[7]}};  // AND_Gate and_1, 8 bits wide
  // AND_Gate R has open pins: in0=decoder_1_out0, in1=Processor_1_rd, out=open
  and W (W_out, Processor_1_wr, decoder_1_out0);
  and and_2 (and_2_out[7], decoder_1_out1, Processor_1_rd);
  // AND_Gate and_3 has open pins: in0=Processor_1_wr, in1=decoder_1_out1, out=open
  // AND_Gate and_4 has open pins: in0=decoder_1_out2, in1=Processor_1_rd, out=open
  and and_5 (and_5_out, Processor_1_wr, decoder_1_out2);
  assign or_1_out = and_1_out | and_6_out;  // OR_Gate or_1, 8 bits wide
  assign and_6_out = {8{and_2_out[7]}} & bit_extender_1_out;  // AND_Gate and_6, 8 bits wide
  and and_7 (and_7_out, and_2_out[7], not_1_out);
  Shift_Register #(.length(3), .width(8)) shift_register_1 (
    .shift(W_out), .in(Processor_1_dataout), .clk(W_out),
    .out({shift_register_1_out_2, shift_register_1_out}), .clr(Reset),
    .q0({shift_register_1_q0, shift_register_1_q0_2}), .q1({shift_register_1_q1, shift_register_1_q1_2}));  // open: load, d0, d1, d2, q2
  LED HALT (.in(Processor_1_halt));
  LED ERR (.in(Processor_1_err));
  Hex_Digit_Display Hex_Digit_Display_1 (.value(shift_register_1_out_2));  // open: dp
  Hex_Digit_Display Hex_Digit_Display_2 (.value(shift_register_1_out));  // open: dp
  not not_1 (not_1_out, keyboard_1_avail);
  Processor Processor_1 (
    .WaitT(and_7_out), .RESET(Reset), .Power(s_r_ff_1_q), .DATAIN(or_1_out), .MREQ(Processor_1_mreq),
    .IORQ(Processor_1_iorq), .RD(Processor_1_rd), .WR(Processor_1_wr), .HALT(Processor_1_halt),
    .ADRESS(Processor_1_adress), .DATAOUT(Processor_1_dataout), .Exe(Processor_1_exe), .ERR(Processor_1_err));  // open: INT, NMI, BUSRQ, M1, BUSACK
  LED EX (.in(Processor_1_exe));
  Hex_Digit_Display Hex_Digit_Display_3 (.value(shift_register_1_q1));  // open: dp
  Keyboard keyboard_1 (
    .clk(clock_1_out), .re(and_8_out), .clr(Reset), .avail(keyboard_1_avail), .data(keyboard_1_data));
  and and_8 (and_8_out, and_2_out[7], keyboard_1_avail);
  and and_9 (and_9_out[7], Processor_1_rd, ~Processor_1_iorq);  // AND_Gate
  and and_10 (and_10_out, Processor_1_wr, ~Processor_1_iorq);  // AND_Gate
  Hex_Digit_Display Hex_Digit_Display_4 (.value(shift_register_1_q1_2));  // open: dp
  Hex_Digit_Display Hex_Digit_Display_5 (.value(shift_register_1_q0));  // open: dp
  assign bit_extender_1_out = {{1{1'b0}}, keyboard_1_data};  // Bit_Extender bit_extender_1
  Bit_Extender #(.out_width(7), .\type ("zero")) bit_extender_2 (.in(Processor_1_dataout), .out(bit_extender_2_out));
  Hex_Digit_Display Hex_Digit_Display_6 (.value(shift_register_1_q0_2));  // open: dp
  TTY #(.cols(40), .rows(20)) tty_1 (.data(bit_extender_2_out), .clk(clock_1_out), .we(and_5_out), .clr(Reset));
endmodule

module Processor (
  input  WaitT,
  input  INT,
  input  NMI,
  input  RESET,
  input  BUSRQ,
  input  Power,
  input  [7:0] DATAIN,
  output M1,
  output MREQ,
  output IORQ,
  output RD,
  output WR,
  output HALT,
  output BUSACK,
  output [15:0] ADRESS,
  output [7:0] DATAOUT,
  output Exe,
  output ERR
);

  wire adder_2_cout, adder_3_cout, and_1_out, and_3_out, and_4_out, and_5_out, and_6_out, and_7_out,
       and_8_out, and_9_out, and_10_out, and_11_out, and_12_out, and_13_out, and_14_out, and_15_out,
       and_16_out, and_17_out, and_18_out, and_19_out, and_20_out, and_22_out, and_24_out, and_30_out,
       and_31_out, clock_1_out, comparator_1_eq, comparator_2_eq, comparator_3_eq, comparator_4_eq,
       comparator_6_eq, comparator_7_eq, comparator_8_eq, counter_3_carry, decoder_1_out0, decoder_1_out1,
       decoder_1_out2, decoder_1_out3, decoder_1_out4, decoder_1_out5, decoder_1_out6, decoder_1_out7,
       decoder_1_out8, decoder_1_out9, decoder_1_out10, decoder_1_out11, decoder_1_out12, decoder_1_out13,
       decoder_1_out14, decoder_1_out15, decoder_2_out0, decoder_2_out1, decoder_2_out2, decoder_2_out3,
       decoder_2_out4, decoder_2_out5, decoder_2_out6, decoder_2_out7, decoder_2_out8, decoder_2_out9,
       decoder_2_out10, decoder_2_out11, decoder_2_out12, decoder_2_out13, decoder_2_out14, decoder_2_out15,
       decoder_3_out0, decoder_3_out1, decoder_3_out2, decoder_3_out3, decoder_3_out4, decoder_3_out5,
       decoder_3_out6, decoder_3_out7, decoder_3_out8, decoder_3_out9, decoder_3_out10, decoder_3_out11,
       decoder_3_out12, decoder_3_out13, decoder_3_out14, decoder_3_out15, decoder_4_out0, decoder_4_out1,
       decoder_4_out2, decoder_4_out3, decoder_4_out4, decoder_4_out5, decoder_4_out6, decoder_4_out7,
       decoder_4_out8, decoder_4_out9, decoder_4_out10, decoder_4_out11, decoder_4_out12, decoder_4_out13,
       decoder_4_out14, decoder_4_out15, decoder_5_out0, decoder_5_out1, decoder_5_out2, decoder_5_out3,
       decoder_5_out4, decoder_5_out5, decoder_5_out6, decoder_5_out7, decoder_6_out0, decoder_6_out1,
       decoder_6_out2, decoder_6_out3, decoder_6_out4, decoder_6_out5, decoder_6_out6, decoder_6_out7,
       decoder_6_out8, decoder_6_out9, decoder_6_out10, decoder_6_out11, decoder_6_out12, decoder_6_out13,
       decoder_6_out14, decoder_6_out15, decoder_7_out0, decoder_7_out1, decoder_7_out2, decoder_7_out3,
       decoder_7_out4, decoder_7_out5, decoder_7_out6, decoder_7_out7, decoder_7_out8, decoder_7_out9,
       decoder_7_out10, decoder_7_out11, decoder_7_out12, decoder_7_out13, decoder_7_out14, decoder_7_out15,
       decoder_8_out0, decoder_8_out1, decoder_8_out2, decoder_8_out3, decoder_8_out4, decoder_8_out5,
       decoder_8_out6, decoder_8_out7, decoder_8_out8, decoder_8_out9, decoder_8_out10, decoder_8_out11,
       decoder_8_out12, decoder_8_out13, decoder_8_out14, decoder_8_out15, decoder_9_out0, decoder_9_out1,
       decoder_9_out2, decoder_9_out3, decoder_9_out4, decoder_9_out5, decoder_9_out6, decoder_9_out7,
       decoder_9_out8, decoder_9_out9, decoder_9_out10, decoder_9_out11, decoder_9_out12, decoder_9_out13,
       decoder_9_out14, decoder_9_out15, decoder_10_out0, decoder_10_out1, decoder_10_out2, decoder_10_out3,
       decoder_10_out4, decoder_10_out5, decoder_10_out6, decoder_10_out7, decoder_10_out8, decoder_10_out9,
       decoder_10_out10, decoder_10_out11, decoder_10_out12, decoder_10_out13, decoder_10_out14,
       decoder_10_out15, decoder_11_out0, decoder_11_out1, decoder_11_out2, decoder_11_out3, decoder_11_out4,
       decoder_11_out5, decoder_11_out6, decoder_11_out7, decoder_11_out8, decoder_11_out9, decoder_11_out10,
       decoder_11_out11, decoder_11_out12, decoder_11_out13, decoder_11_out14, decoder_11_out15,
       decoder_12_out0, decoder_12_out1, decoder_12_out2, decoder_12_out3, decoder_12_out4, decoder_12_out5,
       decoder_12_out6, decoder_12_out7, decoder_12_out8, decoder_12_out9, decoder_12_out10,
       decoder_12_out11, decoder_12_out12, decoder_12_out13, decoder_12_out14, decoder_12_out15,
       decoder_13_out0, decoder_13_out1, decoder_13_out2, decoder_13_out3, decoder_13_out4, decoder_13_out5,
       decoder_13_out6, decoder_13_out7, decoder_13_out8, decoder_13_out9, decoder_13_out10,
       decoder_13_out11, decoder_13_out12, decoder_13_out13, decoder_13_out14, decoder_13_out15,
       decoder_14_out0, decoder_14_out1, decoder_14_out2, decoder_14_out3, decoder_14_out4, decoder_14_out5,
       decoder_14_out6, decoder_14_out7, decoder_14_out8, decoder_14_out9, decoder_14_out10,
       decoder_14_out11, decoder_14_out12, decoder_14_out13, decoder_14_out14, decoder_14_out15,
       decoder_15_out0, decoder_15_out1, decoder_15_out2, decoder_15_out3, decoder_15_out4, decoder_15_out5,
       decoder_15_out6, decoder_15_out7, decoder_15_out8, decoder_15_out9, decoder_15_out10,
       decoder_15_out11, decoder_15_out12, decoder_15_out13, decoder_15_out14, decoder_15_out15,
       decoder_16_out0, decoder_16_out1, decoder_16_out2, decoder_16_out3, decoder_16_out4, decoder_16_out5,
       decoder_16_out6, decoder_16_out7, decoder_16_out8, decoder_16_out9, decoder_16_out10,
       decoder_16_out11, decoder_16_out12, decoder_16_out13, decoder_16_out14, decoder_16_out15,
       decoder_17_out0, decoder_17_out1, decoder_17_out2, decoder_17_out3, decoder_17_out4, decoder_17_out5,
       decoder_17_out6, decoder_17_out7, decoder_17_out8, decoder_17_out9, decoder_17_out10,
       decoder_17_out11, decoder_17_out12, decoder_17_out13, decoder_17_out14, decoder_17_out15,
       decoder_18_out0, decoder_18_out1, decoder_18_out2, decoder_18_out3, decoder_18_out4, decoder_18_out5,
       decoder_18_out6, decoder_18_out7, decoder_18_out8, decoder_18_out9, decoder_18_out10,
       decoder_18_out11, decoder_18_out12, decoder_18_out13, decoder_18_out14, decoder_18_out15,
       decoder_19_out0, decoder_19_out1, decoder_19_out2, decoder_20_out0, decoder_20_out1, decoder_20_out2,
       decoder_20_out3, decoder_20_out4, decoder_20_out5, decoder_21_out0, decoder_21_out1, decoder_21_out2,
       decoder_21_out3, decoder_21_out4, decoder_21_out5, decoder_21_out6, decoder_21_out7, decoder_22_out0,
       decoder_22_out1, decoder_22_out2, decoder_23_out0, decoder_23_out1, decoder_23_out2, decoder_23_out3,
       decoder_23_out4, decoder_23_out5, decoder_24_out0, decoder_24_out1, decoder_24_out2,
       multiplexer_13_out, multiplexer_14_out, multiplexer_16_out, multiplexer_20_out, not_1_out, not_2_out,
       not_3_out, not_4_out, not_5_out, not_6_out, not_7_out, not_8_out, or_1_out, or_3_out, or_6_out,
       or_7_out, or_9_out, or_10_out, or_14_out, or_15_out, or_16_out, or_19_out, or_20_out, or_21_out,
       or_22_out, or_23_out, or_24_out, or_25_out, or_26_out, or_27_out, or_29_out, or_30_out, or_31_out,
       or_32_out, or_33_out, or_34_out, or_35_out, or_36_out, or_37_out, or_38_out, or_39_out, or_40_out,
       or_41_out, Overflow_out, subtractor_1_bout, subtractor_2_bout, xor_1_out, xor_2_out, xor_3_out,
       xor_5_out, xor_6_out, xor_7_out, xor_8_out;
  wire [0:0] Carry_q;
  wire [2:0] counter_2_q;
  wire [4:0] counter_1_q;
  wire [5:0] or_42_out;
  wire [7:0] A_q, adder_2_out, adder_3_out, adder_5_out, and_21_out, and_23_out, and_25_out, and_26_out,
       and_28_out, and_29_out, and_32_out, and_34_out, and_36_out, B_q, C_q, D_q, demultiplexer_2_out0,
       demultiplexer_2_out1, demultiplexer_2_out2, demultiplexer_2_out3, demultiplexer_2_out4,
       demultiplexer_2_out5, demultiplexer_4_out0, demultiplexer_4_out1, demultiplexer_4_out2,
       demultiplexer_4_out3, demultiplexer_4_out4, demultiplexer_4_out5, E_q, F_q, H_q, IR_q, L_q,
       multiplexer_3_out, multiplexer_4_out, multiplexer_5_out, multiplexer_6_out, multiplexer_7_out,
       multiplexer_8_out, multiplexer_9_out, multiplexer_10_out, multiplexer_15_out, multiplexer_17_out,
       multiplexer_18_out, multiplexer_19_out, multiplexer_21_out, multiplexer_22_out, multiplexer_23_out,
       multiplexer_24_out, or_8_out, or_17_out, or_28_out, register_1_q, register_2_q, register_3_q,
       register_4_q, register_5_q, register_6_q, subtractor_1_out, subtractor_2_out, Temp_q, xor_4_out;
  wire [7:1] N_q;
  wire [8:0] shifter_1_out, shifter_2_out, shifter_3_out, shifter_4_out;
  wire [13:0] or_12_out;
  wire [15:0] adder_1_out, adder_4_out, and_27_out, and_33_out, and_35_out, demultiplexer_1_out0,
       demultiplexer_1_out1, demultiplexer_1_out2, demultiplexer_3_out0, demultiplexer_3_out1,
       demultiplexer_3_out2, demultiplexer_5_out0, demultiplexer_5_out1, demultiplexer_5_out2, IX_q, IY_q,
       multiplexer_1_out, multiplexer_2_out, multiplexer_11_out, multiplexer_12_out, multiplexer_25_out,
       multiplexer_26_out, or_18_out, PC_q, SP_q, subtractor_3_out;
  wire [17:0] or_12_out_2;
  wire [31:0] Instructions0x_2_lines, Instructions0x_2_linesa, Instructions0x_2_linesb,
       Instructions1x_1_lines, Instructions1x_1_linesa, Instructions1x_1_linesb, Instructions2x_1_lines,
       Instructions2x_1_linesa, Instructions2x_1_linesb, Instructions3x_1_lines, Instructions3x_1_linesa,
       Instructions3x_1_linesb, Instructions4x_1_lines, Instructions4x_1_linesa, Instructions4x_1_linesb,
       Instructions5x_1_lines, Instructions5x_1_linesa, Instructions5x_1_linesb, Instructions6x_1_lines,
       Instructions6x_1_linesa, Instructions6x_1_linesb, Instructions7x_1_lines, Instructions7x_1_linesa,
       Instructions7x_1_linesb, Instructions8x_1_lines, Instructions8x_1_linesa, Instructions8x_1_linesb,
       Instructions9x_1_lines, Instructions9x_1_linesa, Instructions9x_1_linesb, Instructions10x_1_lines,
       Instructions10x_1_linesa, Instructions10x_1_linesb, Instructions11x_1_lines, Instructions11x_1_linesa,
       Instructions11x_1_linesb, Instructions12x_1_lines, Instructions12x_1_linesa, Instructions12x_1_linesb,
       Instructions13x_1_lines, Instructions13x_1_linesa, Instructions13x_1_linesb, Instructions14x_1_lines,
       Instructions14x_1_linesa, Instructions14x_1_linesb, Instructions15x_1_lines, Instructions15x_1_linesa,
       Instructions15x_1_linesb, or_11_out, or_13_out;

  or or_1 (or_1_out, RESET, or_7_out);
  and and_1 (and_1_out, decoder_5_out5, ~WaitT, ~and_6_out);  // AND_Gate
  and and_2 (Exe, ~HALT, ~ERR, decoder_5_out5);  // AND_Gate
  Register IR (.D(DATAOUT), .en(decoder_5_out3), .Q(IR_q), .clk(clock_1_out), .clr(RESET));
  Counter #(.max('h1f), .ongoal("stay"), .width(5)) counter_1 (
    .count(and_1_out), .Q(counter_1_q), .carry(ERR), .clk(clock_1_out), .clr(or_1_out));  // open: load, D, up
  Clock clock_1 (.out(clock_1_out));
  T_Flip_Flop t_ff_1 (.clk(clock_1_out), .T(or_13_out[0]), .Q(HALT), .reset(RESET));  // open: Qn, preset
  Decoder #(.select(4)) decoder_1 (
    .out0(decoder_1_out0), .out1(decoder_1_out1), .out2(decoder_1_out2), .out3(decoder_1_out3),
    .out4(decoder_1_out4), .out5(decoder_1_out5), .out6(decoder_1_out6), .out7(decoder_1_out7),
    .out8(decoder_1_out8), .out9(decoder_1_out9), .out10(decoder_1_out10), .out11(decoder_1_out11),
    .out12(decoder_1_out12), .out13(decoder_1_out13), .out14(decoder_1_out14), .out15(decoder_1_out15),
    .sel(IR_q[7:4]), .en(decoder_5_out5));
  Decoder #(.select(4)) decoder_2 (
    .out0(decoder_2_out0), .out1(decoder_2_out1), .out2(decoder_2_out2), .out3(decoder_2_out3),
    .out4(decoder_2_out4), .out5(decoder_2_out5), .out6(decoder_2_out6), .out7(decoder_2_out7),
    .out8(decoder_2_out8), .out9(decoder_2_out9), .out10(decoder_2_out10), .out11(decoder_2_out11),
    .out12(decoder_2_out12), .out13(decoder_2_out13), .out14(decoder_2_out14), .out15(decoder_2_out15),
    .sel(IR_q[3:0]), .en(decoder_1_out0));
  and and_3 (and_3_out, ~HALT, Power);  // AND_Gate
  and and_4 (and_4_out, and_3_out, ~WaitT, ~and_5_out);  // AND_Gate
  Decoder #(.select(4)) decoder_3 (
    .out0(decoder_3_out0), .out1(decoder_3_out1), .out2(decoder_3_out2), .out3(decoder_3_out3),
    .out4(decoder_3_out4), .out5(decoder_3_out5), .out6(decoder_3_out6), .out7(decoder_3_out7),
    .out8(decoder_3_out8), .out9(decoder_3_out9), .out10(decoder_3_out10), .out11(decoder_3_out11),
    .out12(decoder_3_out12), .out13(decoder_3_out13), .out14(decoder_3_out14), .out15(decoder_3_out15),
    .sel(IR_q[3:0]), .en(decoder_1_out1));
  Instructions0x Instructions0x_2 (
    .Lines(Instructions0x_2_lines), .Linesa(Instructions0x_2_linesa), .Linesb(Instructions0x_2_linesb),
    .Sel_b(decoder_2_out1), .Sel_c(decoder_2_out2), .Sel_d(decoder_2_out3), .Sel_e(decoder_2_out4),
    .Sel_f(decoder_2_out5), .Sel_g(decoder_2_out6), .Sel_h(decoder_2_out7), .Sel_i(decoder_2_out8),
    .Sel_j(decoder_2_out9), .Sel_k(decoder_2_out10), .Sel_l(decoder_2_out11), .Sel_m(decoder_2_out12),
    .Sel_n(decoder_2_out13), .Sel_o(decoder_2_out14), .Sel_p(decoder_2_out15), .Address(counter_1_q),
    .Sel_a(decoder_2_out0));
  Counter #(.max('h7), .width(3)) counter_2 (
    .count(and_4_out), .Q(counter_2_q), .clk(clock_1_out), .clr(or_3_out));  // open: load, D, carry, up
  Decoder #(.select(4)) decoder_4 (
    .out0(decoder_4_out0), .out1(decoder_4_out1), .out2(decoder_4_out2), .out3(decoder_4_out3),
    .out4(decoder_4_out4), .out5(decoder_4_out5), .out6(decoder_4_out6), .out7(decoder_4_out7),
    .out8(decoder_4_out8), .out9(decoder_4_out9), .out10(decoder_4_out10), .out11(decoder_4_out11),
    .out12(decoder_4_out12), .out13(decoder_4_out13), .out14(decoder_4_out14), .out15(decoder_4_out15),
    .sel(IR_q[3:0]), .en(decoder_1_out2));
  Instructions1x Instructions1x_1 (
    .Lines(Instructions1x_1_lines), .Linesa(Instructions1x_1_linesa), .Linesb(Instructions1x_1_linesb),
    .Sel_b(decoder_3_out1), .Sel_c(decoder_3_out2), .Sel_d(decoder_3_out3), .Sel_e(decoder_3_out4),
    .Sel_f(decoder_3_out5), .Sel_g(decoder_3_out6), .Sel_h(decoder_3_out7), .Sel_i(decoder_3_out8),
    .Sel_j(decoder_3_out9), .Sel_k(decoder_3_out10), .Sel_l(decoder_3_out11), .Sel_m(decoder_3_out12),
    .Sel_n(decoder_3_out13), .Sel_o(decoder_3_out14), .Sel_p(decoder_3_out15), .Address(counter_1_q),
    .Sel_a(decoder_3_out0));
  or or_2 (M1, decoder_5_out1, decoder_5_out2, decoder_5_out0);
  Decoder #(.select(3)) decoder_5 (
    .out0(decoder_5_out0), .out1(decoder_5_out1), .out2(decoder_5_out2), .out3(decoder_5_out3),
    .out4(decoder_5_out4), .out5(decoder_5_out5), .out6(decoder_5_out6), .out7(decoder_5_out7),
    .sel(counter_2_q), .en(and_3_out));
  or or_3 (or_3_out, decoder_5_out7, RESET, or_11_out[30]);
  Instructions2x Instructions2x_1 (
    .Lines(Instructions2x_1_lines), .Linesa(Instructions2x_1_linesa), .Linesb(Instructions2x_1_linesb),
    .Sel_b(decoder_4_out1), .Sel_c(decoder_4_out2), .Sel_d(decoder_4_out3), .Sel_e(decoder_4_out4),
    .Sel_f(decoder_4_out5), .Sel_g(decoder_4_out6), .Sel_h(decoder_4_out7), .Sel_i(decoder_4_out8),
    .Sel_j(decoder_4_out9), .Sel_k(decoder_4_out10), .Sel_l(decoder_4_out11), .Sel_m(decoder_4_out12),
    .Sel_n(decoder_4_out13), .Sel_o(decoder_4_out14), .Sel_p(decoder_4_out15), .Address(counter_1_q),
    .Sel_a(decoder_4_out0));
  or or_4 (RD, or_13_out[24], or_6_out);
  or or_5 (MREQ, decoder_5_out1, decoder_5_out4, decoder_5_out2, decoder_5_out5);
  or or_6 (or_6_out, decoder_5_out1, decoder_5_out2);
  or or_7 (or_7_out, decoder_5_out0, decoder_5_out6);
  Decoder #(.select(4)) decoder_6 (
    .out0(decoder_6_out0), .out1(decoder_6_out1), .out2(decoder_6_out2), .out3(decoder_6_out3),
    .out4(decoder_6_out4), .out5(decoder_6_out5), .out6(decoder_6_out6), .out7(decoder_6_out7),
    .out8(decoder_6_out8), .out9(decoder_6_out9), .out10(decoder_6_out10), .out11(decoder_6_out11),
    .out12(decoder_6_out12), .out13(decoder_6_out13), .out14(decoder_6_out14), .out15(decoder_6_out15),
    .sel(IR_q[3:0]), .en(decoder_1_out3));
  and and_5 (and_5_out, decoder_5_out5, ~or_10_out);  // AND_Gate
  Decoder #(.select(4)) decoder_7 (
    .out0(decoder_7_out0), .out1(decoder_7_out1), .out2(decoder_7_out2), .out3(decoder_7_out3),
    .out4(decoder_7_out4), .out5(decoder_7_out5), .out6(decoder_7_out6), .out7(decoder_7_out7),
    .out8(decoder_7_out8), .out9(decoder_7_out9), .out10(decoder_7_out10), .out11(decoder_7_out11),
    .out12(decoder_7_out12), .out13(decoder_7_out13), .out14(decoder_7_out14), .out15(decoder_7_out15),
    .sel(IR_q[3:0]), .en(decoder_1_out4));
  Instructions3x Instructions3x_1 (
    .Lines(Instructions3x_1_lines), .Linesa(Instructions3x_1_linesa), .Linesb(Instructions3x_1_linesb),
    .Sel_b(decoder_6_out1), .Sel_c(decoder_6_out2), .Sel_d(decoder_6_out3), .Sel_e(decoder_6_out4),
    .Sel_f(decoder_6_out5), .Sel_g(decoder_6_out6), .Sel_h(decoder_6_out7), .Sel_i(decoder_6_out8),
    .Sel_j(decoder_6_out9), .Sel_k(decoder_6_out10), .Sel_l(decoder_6_out11), .Sel_m(decoder_6_out12),
    .Sel_n(decoder_6_out13), .Sel_o(decoder_6_out14), .Sel_p(decoder_6_out15), .Address(counter_1_q),
    .Sel_a(decoder_6_out0));
  assign or_8_out = or_17_out | DATAIN;  // OR_Gate or_8, 8 bits wide
  Register DataBuss (.D(or_8_out), .en(or_9_out), .Q(DATAOUT), .clk(clock_1_out), .clr(RESET));
  or or_9 (or_9_out, decoder_5_out2, or_11_out[27]);
  Decoder #(.select(4)) decoder_8 (
    .out0(decoder_8_out0), .out1(decoder_8_out1), .out2(decoder_8_out2), .out3(decoder_8_out3),
    .out4(decoder_8_out4), .out5(decoder_8_out5), .out6(decoder_8_out6), .out7(decoder_8_out7),
    .out8(decoder_8_out8), .out9(decoder_8_out9), .out10(decoder_8_out10), .out11(decoder_8_out11),
    .out12(decoder_8_out12), .out13(decoder_8_out13), .out14(decoder_8_out14), .out15(decoder_8_out15),
    .sel(IR_q[3:0]), .en(decoder_1_out5));
  Instructions4x Instructions4x_1 (
    .Lines(Instructions4x_1_lines), .Linesa(Instructions4x_1_linesa), .Linesb(Instructions4x_1_linesb),
    .Sel_b(decoder_7_out1), .Sel_c(decoder_7_out2), .Sel_d(decoder_7_out3), .Sel_e(decoder_7_out4),
    .Sel_f(decoder_7_out5), .Sel_g(decoder_7_out6), .Sel_h(decoder_7_out7), .Sel_i(decoder_7_out8),
    .Sel_j(decoder_7_out9), .Sel_k(decoder_7_out10), .Sel_l(decoder_7_out11), .Sel_m(decoder_7_out12),
    .Sel_n(decoder_7_out13), .Sel_o(decoder_7_out14), .Sel_p(decoder_7_out15), .Address(counter_1_q),
    .Sel_a(decoder_7_out0));
  or or_10 (or_10_out, counter_3_carry, or_11_out[31]);
  Counter #(.max('h2), .width(2)) counter_3 (
    .count(and_6_out), .carry(counter_3_carry), .clk(clock_1_out));  // open: load, D, Q, up, clr
  Decoder #(.select(4)) decoder_9 (
    .out0(decoder_9_out0), .out1(decoder_9_out1), .out2(decoder_9_out2), .out3(decoder_9_out3),
    .out4(decoder_9_out4), .out5(decoder_9_out5), .out6(decoder_9_out6), .out7(decoder_9_out7),
    .out8(decoder_9_out8), .out9(decoder_9_out9), .out10(decoder_9_out10), .out11(decoder_9_out11),
    .out12(decoder_9_out12), .out13(decoder_9_out13), .out14(decoder_9_out14), .out15(decoder_9_out15),
    .sel(IR_q[3:0]), .en(decoder_1_out6));
  Instructions5x Instructions5x_1 (
    .Lines(Instructions5x_1_lines), .Linesa(Instructions5x_1_linesa), .Linesb(Instructions5x_1_linesb),
    .Sel_b(decoder_8_out1), .Sel_c(decoder_8_out2), .Sel_d(decoder_8_out3), .Sel_e(decoder_8_out4),
    .Sel_f(decoder_8_out5), .Sel_g(decoder_8_out6), .Sel_h(decoder_8_out7), .Sel_i(decoder_8_out8),
    .Sel_j(decoder_8_out9), .Sel_k(decoder_8_out10), .Sel_l(decoder_8_out11), .Sel_m(decoder_8_out12),
    .Sel_n(decoder_8_out13), .Sel_o(decoder_8_out14), .Sel_p(decoder_8_out15), .Address(counter_1_q),
    .Sel_a(decoder_8_out0));
  Instructions6x Instructions6x_1 (
    .Lines(Instructions6x_1_lines), .Linesa(Instructions6x_1_linesa), .Linesb(Instructions6x_1_linesb),
    .Sel_b(decoder_9_out1), .Sel_c(decoder_9_out2), .Sel_d(decoder_9_out3), .Sel_e(decoder_9_out4),
    .Sel_f(decoder_9_out5), .Sel_g(decoder_9_out6), .Sel_h(decoder_9_out7), .Sel_i(decoder_9_out8),
    .Sel_j(decoder_9_out9), .Sel_k(decoder_9_out10), .Sel_l(decoder_9_out11), .Sel_m(decoder_9_out12),
    .Sel_n(decoder_9_out13), .Sel_o(decoder_9_out14), .Sel_p(decoder_9_out15), .Address(counter_1_q),
    .Sel_a(decoder_9_out0));
  Decoder #(.select(4)) decoder_10 (
    .out0(decoder_10_out0), .out1(decoder_10_out1), .out2(decoder_10_out2), .out3(decoder_10_out3),
    .out4(decoder_10_out4), .out5(decoder_10_out5), .out6(decoder_10_out6), .out7(decoder_10_out7),
    .out8(decoder_10_out8), .out9(decoder_10_out9), .out10(decoder_10_out10), .out11(decoder_10_out11),
    .out12(decoder_10_out12), .out13(decoder_10_out13), .out14(decoder_10_out14), .out15(decoder_10_out15),
    .sel(IR_q[3:0]), .en(decoder_1_out7));
  assign or_11_out = Instructions0x_2_lines | Instructions1x_1_lines | Instructions2x_1_lines | Instructions3x_1_lines | Instructions4x_1_lines | Instructions5x_1_lines | Instructions6x_1_lines | Instructions7x_1_lines | Instructions8x_1_lines | Instructions9x_1_lines | Instructions10x_1_lines | Instructions11x_1_lines | Instructions12x_1_lines | Instructions13x_1_lines | Instructions14x_1_lines | Instructions15x_1_lines;  // OR_Gate or_11, 32 bits wide
  Decoder #(.select(4)) decoder_11 (
    .out0(decoder_11_out0), .out1(decoder_11_out1), .out2(decoder_11_out2), .out3(decoder_11_out3),
    .out4(decoder_11_out4), .out5(decoder_11_out5), .out6(decoder_11_out6), .out7(decoder_11_out7),
    .out8(decoder_11_out8), .out9(decoder_11_out9), .out10(decoder_11_out10), .out11(decoder_11_out11),
    .out12(decoder_11_out12), .out13(decoder_11_out13), .out14(decoder_11_out14), .out15(decoder_11_out15),
    .sel(IR_q[3:0]), .en(decoder_1_out8));
  Instructions7x Instructions7x_1 (
    .Lines(Instructions7x_1_lines), .Linesa(Instructions7x_1_linesa), .Linesb(Instructions7x_1_linesb),
    .Sel_b(decoder_10_out1), .Sel_c(decoder_10_out2), .Sel_d(decoder_10_out3), .Sel_e(decoder_10_out4),
    .Sel_f(decoder_10_out5), .Sel_g(decoder_10_out6), .Sel_h(decoder_10_out7), .Sel_i(decoder_10_out8),
    .Sel_j(decoder_10_out9), .Sel_k(decoder_10_out10), .Sel_l(decoder_10_out11), .Sel_m(decoder_10_out12),
    .Sel_n(decoder_10_out13), .Sel_o(decoder_10_out14), .Sel_p(decoder_10_out15), .Address(counter_1_q),
    .Sel_a(decoder_10_out0));
  assign {or_12_out_2, or_12_out} = Instructions0x_2_linesa | Instructions1x_1_linesa | Instructions2x_1_linesa | Instructions3x_1_linesa | Instructions4x_1_linesa | Instructions5x_1_linesa | Instructions6x_1_linesa | Instructions7x_1_linesa | Instructions8x_1_linesa | Instructions9x_1_linesa | Instructions10x_1_linesa | Instructions11x_1_linesa | Instructions12x_1_linesa | Instructions13x_1_linesa | Instructions14x_1_linesa | Instructions15x_1_linesa;  // OR_Gate or_12, 32 bits wide
  and and_6 (and_6_out, not_4_out, or_13_out[23]);
  and and_7 (and_7_out, ~counter_3_carry, and_6_out);  // AND_Gate
  Decoder #(.select(4)) decoder_12 (
    .out0(decoder_12_out0), .out1(decoder_12_out1), .out2(decoder_12_out2), .out3(decoder_12_out3),
    .out4(decoder_12_out4), .out5(decoder_12_out5), .out6(decoder_12_out6), .out7(decoder_12_out7),
    .out8(decoder_12_out8), .out9(decoder_12_out9), .out10(decoder_12_out10), .out11(decoder_12_out11),
    .out12(decoder_12_out12), .out13(decoder_12_out13), .out14(decoder_12_out14), .out15(decoder_12_out15),
    .sel(IR_q[3:0]), .en(decoder_1_out9));
  Instructions9x Instructions9x_1 (
    .Lines(Instructions9x_1_lines), .Linesa(Instructions9x_1_linesa), .Linesb(Instructions9x_1_linesb),
    .Sel_b(decoder_12_out1), .Sel_c(decoder_12_out2), .Sel_d(decoder_12_out3), .Sel_e(decoder_12_out4),
    .Sel_f(decoder_12_out5), .Sel_g(decoder_12_out6), .Sel_h(decoder_12_out7), .Sel_i(decoder_12_out8),
    .Sel_j(decoder_12_out9), .Sel_k(decoder_12_out10), .Sel_l(decoder_12_out11), .Sel_m(decoder_12_out12),
    .Sel_n(decoder_12_out13), .Sel_o(decoder_12_out14), .Sel_p(decoder_12_out15), .Address(counter_1_q),
    .Sel_a(decoder_12_out0));
  Instructions8x Instructions8x_1 (
    .Lines(Instructions8x_1_lines), .Linesa(Instructions8x_1_linesa), .Linesb(Instructions8x_1_linesb),
    .Sel_b(decoder_11_out1), .Sel_c(decoder_11_out2), .Sel_d(decoder_11_out3), .Sel_e(decoder_11_out4),
    .Sel_f(decoder_11_out5), .Sel_g(decoder_11_out6), .Sel_h(decoder_11_out7), .Sel_i(decoder_11_out8),
    .Sel_j(decoder_11_out9), .Sel_k(decoder_11_out10), .Sel_l(decoder_11_out11), .Sel_m(decoder_11_out12),
    .Sel_n(decoder_11_out13), .Sel_o(decoder_11_out14), .Sel_p(decoder_11_out15), .Address(counter_1_q),
    .Sel_a(decoder_11_out0));
  assign {or_13_out[31:28], WR, or_13_out[26:21], IORQ, or_13_out[19:0]} = Instructions0x_2_linesb | Instructions1x_1_linesb | Instructions2x_1_linesb | Instructions3x_1_linesb | Instructions4x_1_linesb | Instructions5x_1_linesb | Instructions6x_1_linesb | Instructions7x_1_linesb | Instructions8x_1_linesb | Instructions9x_1_linesb | Instructions10x_1_linesb | Instructions11x_1_linesb | Instructions12x_1_linesb | Instructions13x_1_linesb | Instructions14x_1_linesb | Instructions15x_1_linesb;  // OR_Gate or_13, 32 bits wide
  Adder #(.width(16)) adder_1 (.a(PC_q), .b(16'h1), .out(adder_1_out));  // open: cin, cout
  Decoder #(.select(4)) decoder_13 (
    .out0(decoder_13_out0), .out1(decoder_13_out1), .out2(decoder_13_out2), .out3(decoder_13_out3),
    .out4(decoder_13_out4), .out5(decoder_13_out5), .out6(decoder_13_out6), .out7(decoder_13_out7),
    .out8(decoder_13_out8), .out9(decoder_13_out9), .out10(decoder_13_out10), .out11(decoder_13_out11),
    .out12(decoder_13_out12), .out13(decoder_13_out13), .out14(decoder_13_out14), .out15(decoder_13_out15),
    .sel(IR_q[3:0]), .en(decoder_1_out10));
  Instructions10x Instructions10x_1 (
    .Lines(Instructions10x_1_lines), .Linesa(Instructions10x_1_linesa), .Linesb(Instructions10x_1_linesb),
    .Sel_b(decoder_13_out1), .Sel_c(decoder_13_out2), .Sel_d(decoder_13_out3), .Sel_e(decoder_13_out4),
    .Sel_f(decoder_13_out5), .Sel_g(decoder_13_out6), .Sel_h(decoder_13_out7), .Sel_i(decoder_13_out8),
    .Sel_j(decoder_13_out9), .Sel_k(decoder_13_out10), .Sel_l(decoder_13_out11), .Sel_m(decoder_13_out12),
    .Sel_n(decoder_13_out13), .Sel_o(decoder_13_out14), .Sel_p(decoder_13_out15), .Address(counter_1_q),
    .Sel_a(decoder_13_out0));
  Multiplexer #(.enable("false"), .width(16)) multiplexer_1 (
    .in0(adder_1_out), .in1(or_18_out), .out(multiplexer_1_out), .sel(not_1_out));
  not not_1 (not_1_out, or_14_out);
  or or_14 (or_14_out, decoder_5_out6, and_7_out, or_13_out[25]);
  or or_15 (or_15_out, decoder_5_out6, and_7_out, or_11_out[28]);
  Register #(.width(16)) PC (.D(multiplexer_1_out), .en(or_15_out), .Q(PC_q), .clk(clock_1_out), .clr(RESET));
  Register #(.width(16)) AddressBuss (
    .D(multiplexer_2_out), .en(or_16_out), .Q(ADRESS), .clk(clock_1_out), .clr(RESET));
  Multiplexer #(.enable("false"), .width(16)) multiplexer_2 (
    .in0(PC_q), .in1(or_18_out), .out(multiplexer_2_out), .sel(or_11_out[4]));
  or or_16 (or_16_out, decoder_5_out0, or_11_out[29]);
  Decoder #(.select(4)) decoder_14 (
    .out0(decoder_14_out0), .out1(decoder_14_out1), .out2(decoder_14_out2), .out3(decoder_14_out3),
    .out4(decoder_14_out4), .out5(decoder_14_out5), .out6(decoder_14_out6), .out7(decoder_14_out7),
    .out8(decoder_14_out8), .out9(decoder_14_out9), .out10(decoder_14_out10), .out11(decoder_14_out11),
    .out12(decoder_14_out12), .out13(decoder_14_out13), .out14(decoder_14_out14), .out15(decoder_14_out15),
    .sel(IR_q[3:0]), .en(decoder_1_out11));
  Instructions11x Instructions11x_1 (
    .Lines(Instructions11x_1_lines), .Linesa(Instructions11x_1_linesa), .Linesb(Instructions11x_1_linesb),
    .Sel_b(decoder_14_out1), .Sel_c(decoder_14_out2), .Sel_d(decoder_14_out3), .Sel_e(decoder_14_out4),
    .Sel_f(decoder_14_out5), .Sel_g(decoder_14_out6), .Sel_h(decoder_14_out7), .Sel_i(decoder_14_out8),
    .Sel_j(decoder_14_out9), .Sel_k(decoder_14_out10), .Sel_l(decoder_14_out11), .Sel_m(decoder_14_out12),
    .Sel_n(decoder_14_out13), .Sel_o(decoder_14_out14), .Sel_p(decoder_14_out15), .Address(counter_1_q),
    .Sel_a(decoder_14_out0));
  Decoder #(.select(4)) decoder_15 (
    .out0(decoder_15_out0), .out1(decoder_15_out1), .out2(decoder_15_out2), .out3(decoder_15_out3),
    .out4(decoder_15_out4), .out5(decoder_15_out5), .out6(decoder_15_out6), .out7(decoder_15_out7),
    .out8(decoder_15_out8), .out9(decoder_15_out9), .out10(decoder_15_out10), .out11(decoder_15_out11),
    .out12(decoder_15_out12), .out13(decoder_15_out13), .out14(decoder_15_out14), .out15(decoder_15_out15),
    .sel(IR_q[3:0]), .en(decoder_1_out12));
  Instructions12x Instructions12x_1 (
    .Lines(Instructions12x_1_lines), .Linesa(Instructions12x_1_linesa), .Linesb(Instructions12x_1_linesb),
    .Sel_b(decoder_15_out1), .Sel_c(decoder_15_out2), .Sel_d(decoder_15_out3), .Sel_e(decoder_15_out4),
    .Sel_f(decoder_15_out5), .Sel_g(decoder_15_out6), .Sel_h(decoder_15_out7), .Sel_i(decoder_15_out8),
    .Sel_j(decoder_15_out9), .Sel_k(decoder_15_out10), .Sel_l(decoder_15_out11), .Sel_m(decoder_15_out12),
    .Sel_n(decoder_15_out13), .Sel_o(decoder_15_out14), .Sel_p(decoder_15_out15), .Address(counter_1_q),
    .Sel_a(decoder_15_out0));
  Decoder #(.select(4)) decoder_16 (
    .out0(decoder_16_out0), .out1(decoder_16_out1), .out2(decoder_16_out2), .out3(decoder_16_out3),
    .out4(decoder_16_out4), .out5(decoder_16_out5), .out6(decoder_16_out6), .out7(decoder_16_out7),
    .out8(decoder_16_out8), .out9(decoder_16_out9), .out10(decoder_16_out10), .out11(decoder_16_out11),
    .out12(decoder_16_out12), .out13(decoder_16_out13), .out14(decoder_16_out14), .out15(decoder_16_out15),
    .sel(IR_q[3:0]), .en(decoder_1_out13));
  Instructions13x Instructions13x_1 (
    .Lines(Instructions13x_1_lines), .Linesa(Instructions13x_1_linesa), .Linesb(Instructions13x_1_linesb),
    .Sel_b(decoder_16_out1), .Sel_c(decoder_16_out2), .Sel_d(decoder_16_out3), .Sel_e(decoder_16_out4),
    .Sel_f(decoder_16_out5), .Sel_g(decoder_16_out6), .Sel_h(decoder_16_out7), .Sel_i(decoder_16_out8),
    .Sel_j(decoder_16_out9), .Sel_k(decoder_16_out10), .Sel_l(decoder_16_out11), .Sel_m(decoder_16_out12),
    .Sel_n(decoder_16_out13), .Sel_o(decoder_16_out14), .Sel_p(decoder_16_out15), .Address(counter_1_q),
    .Sel_a(decoder_16_out0));
  Decoder #(.select(4)) decoder_17 (
    .out0(decoder_17_out0), .out1(decoder_17_out1), .out2(decoder_17_out2), .out3(decoder_17_out3),
    .out4(decoder_17_out4), .out5(decoder_17_out5), .out6(decoder_17_out6), .out7(decoder_17_out7),
    .out8(decoder_17_out8), .out9(decoder_17_out9), .out10(decoder_17_out10), .out11(decoder_17_out11),
    .out12(decoder_17_out12), .out13(decoder_17_out13), .out14(decoder_17_out14), .out15(decoder_17_out15),
    .sel(IR_q[3:0]), .en(decoder_1_out14));
  Instructions14x Instructions14x_1 (
    .Lines(Instructions14x_1_lines), .Linesa(Instructions14x_1_linesa), .Linesb(Instructions14x_1_linesb),
    .Sel_b(decoder_17_out1), .Sel_c(decoder_17_out2), .Sel_d(decoder_17_out3), .Sel_e(decoder_17_out4),
    .Sel_f(decoder_17_out5), .Sel_g(decoder_17_out6), .Sel_h(decoder_17_out7), .Sel_i(decoder_17_out8),
    .Sel_j(decoder_17_out9), .Sel_k(decoder_17_out10), .Sel_l(decoder_17_out11), .Sel_m(decoder_17_out12),
    .Sel_n(decoder_17_out13), .Sel_o(decoder_17_out14), .Sel_p(decoder_17_out15), .Address(counter_1_q),
    .Sel_a(decoder_17_out0));
  assign or_17_out = and_21_out | and_28_out | and_32_out | and_34_out | and_36_out;  // OR_Gate or_17, 8 bits wide
  assign or_18_out = and_35_out | and_27_out | and_33_out | multiplexer_12_out;  // OR_Gate or_18, 16 bits wide
  Decoder #(.select(4)) decoder_18 (
    .out0(decoder_18_out0), .out1(decoder_18_out1), .out2(decoder_18_out2), .out3(decoder_18_out3),
    .out4(decoder_18_out4), .out5(decoder_18_out5), .out6(decoder_18_out6), .out7(decoder_18_out7),
    .out8(decoder_18_out8), .out9(decoder_18_out9), .out10(decoder_18_out10), .out11(decoder_18_out11),
    .out12(decoder_18_out12), .out13(decoder_18_out13), .out14(decoder_18_out14), .out15(decoder_18_out15),
    .sel(IR_q[3:0]), .en(decoder_1_out15));
  Instructions15x Instructions15x_1 (
    .Lines(Instructions15x_1_lines), .Linesa(Instructions15x_1_linesa), .Linesb(Instructions15x_1_linesb),
    .Sel_b(decoder_18_out1), .Sel_c(decoder_18_out2), .Sel_d(decoder_18_out3), .Sel_e(decoder_18_out4),
    .Sel_f(decoder_18_out5), .Sel_g(decoder_18_out6), .Sel_h(decoder_18_out7), .Sel_i(decoder_18_out8),
    .Sel_j(decoder_18_out9), .Sel_k(decoder_18_out10), .Sel_l(decoder_18_out11), .Sel_m(decoder_18_out12),
    .Sel_n(decoder_18_out13), .Sel_o(decoder_18_out14), .Sel_p(decoder_18_out15), .Address(counter_1_q),
    .Sel_a(decoder_18_out0));
  Demultiplexer #(.enable("false"), .select(2), .width(16)) demultiplexer_1 (
    .out0(demultiplexer_1_out0), .out1(demultiplexer_1_out1), .out2(demultiplexer_1_out2), .in(ADRESS),
    .sel(or_11_out[15:14]));  // open: out3
  Decoder #(.select(2)) decoder_19 (
    .out0(decoder_19_out0), .out1(decoder_19_out1), .out2(decoder_19_out2), .sel(or_11_out[15:14]),
    .en(and_8_out));  // open: out3
  Decoder #(.select(3)) decoder_20 (
    .out0(decoder_20_out0), .out1(decoder_20_out1), .out2(decoder_20_out2), .out3(decoder_20_out3),
    .out4(decoder_20_out4), .out5(decoder_20_out5), .sel(or_11_out[18:16]), .en(and_9_out));  // open: out6, out7
  and and_8 (and_8_out, or_11_out[26], or_11_out[25]);
  and and_9 (and_9_out, not_2_out, or_11_out[26]);
  not not_2 (not_2_out, or_11_out[25]);
  Demultiplexer #(.enable("false"), .select(3), .width(8)) demultiplexer_2 (
    .out0(demultiplexer_2_out0), .out1(demultiplexer_2_out1), .out2(demultiplexer_2_out2),
    .out3(demultiplexer_2_out3), .out4(demultiplexer_2_out4), .out5(demultiplexer_2_out5), .in(DATAOUT),
    .sel(or_11_out[18:16]));  // open: out6, out7
  Multiplexer #(.enable("false"), .width(8)) multiplexer_3 (
    .in0(demultiplexer_2_out0), .in1(demultiplexer_1_out0[15:8]), .out(multiplexer_3_out), .sel(or_11_out[25]));
  Multiplexer #(.enable("false"), .width(8)) multiplexer_4 (
    .in0(demultiplexer_2_out2), .in1(demultiplexer_1_out1[15:8]), .out(multiplexer_4_out), .sel(or_11_out[25]));
  Multiplexer #(.enable("false"), .width(8)) multiplexer_5 (
    .in0(demultiplexer_2_out4), .in1(demultiplexer_1_out2[15:8]), .out(multiplexer_5_out), .sel(or_11_out[25]));
  Decoder #(.select(3)) decoder_21 (
    .out0(decoder_21_out0), .out1(decoder_21_out1), .out2(decoder_21_out2), .out3(decoder_21_out3),
    .out4(decoder_21_out4), .out5(decoder_21_out5), .out6(decoder_21_out6), .out7(decoder_21_out7),
    .sel(or_12_out[13:11]));  // open: en
  or or_19 (or_19_out, decoder_19_out0, decoder_20_out0);
  or or_20 (or_20_out, decoder_19_out0, decoder_20_out1);
  or or_21 (or_21_out, decoder_19_out1, decoder_20_out2);
  or or_22 (or_22_out, decoder_19_out1, decoder_20_out3);
  or or_23 (or_23_out, decoder_19_out2, decoder_20_out4);
  or or_24 (or_24_out, decoder_19_out2, decoder_20_out5);
  // Probe on A_q
  Register B (.D(multiplexer_3_out), .en(or_19_out), .Q(B_q), .clk(clock_1_out), .clr(RESET));
  Register D (.D(multiplexer_4_out), .en(or_21_out), .Q(D_q), .clk(clock_1_out), .clr(RESET));
  Register H (.D(multiplexer_5_out), .en(or_23_out), .Q(H_q), .clk(clock_1_out), .clr(RESET));
  // Probe on Temp_q
  and and_10 (and_10_out, subtractor_2_bout, comparator_1_eq);
  Comparator #(.mode("unsigned"), .width(4)) comparator_1 (
    .a(or_13_out[31:28]), .b(4'b0001), .eq(comparator_1_eq));  // open: gt, lt
  Comparator #(.mode("unsigned"), .width(4)) comparator_2 (
    .a(or_13_out[31:28]), .b(4'b0111), .eq(comparator_2_eq));  // open: gt, lt
  Comparator #(.mode("unsigned"), .width(4)) comparator_3 (
    .a(or_13_out[31:28]), .b(4'b1000), .eq(comparator_3_eq));  // open: gt, lt
  Multiplexer #(.enable("false"), .width(8)) multiplexer_6 (
    .in0(A_q), .in1(Temp_q), .out(multiplexer_6_out), .sel(or_11_out[5]));
  not not_3 (not_3_out, comparator_4_eq);
  Comparator #(.mode("unsigned")) comparator_4 (.a(A_q), .b({8{1'b0}}), .eq(comparator_4_eq));  // open: gt, lt
  and and_11 (and_11_out, A_q[0], decoder_21_out0);
  and and_12 (and_12_out, A_q[1], decoder_21_out1);
  and and_13 (and_13_out, A_q[2], decoder_21_out2);
  and and_14 (and_14_out, A_q[3], decoder_21_out3);
  and and_15 (and_15_out, A_q[4], decoder_21_out4);
  and and_16 (and_16_out, A_q[5], decoder_21_out5);
  and and_17 (and_17_out, A_q[6], decoder_21_out6);
  and and_18 (and_18_out, A_q[7], decoder_21_out7);
  Register Temp (.D(DATAOUT), .en(or_12_out[1]), .Q(Temp_q), .clk(clock_1_out), .clr(RESET));
  // Probe on Temp_q
  Adder adder_2 (.a(multiplexer_6_out), .b(8'h1), .out(adder_2_out), .cout(adder_2_cout));  // open: cin
  and and_19 (and_19_out, adder_2_cout, comparator_2_eq);
  Subtractor subtractor_1 (
    .a(multiplexer_6_out), .b(8'h1), .out(subtractor_1_out), .bout(subtractor_1_bout));  // open: bin
  and and_20 (and_20_out, subtractor_1_bout, comparator_3_eq);
  xor xor_1 (xor_1_out, A_q[0], A_q[1]);
  or or_25 (or_25_out, and_11_out, and_12_out, and_13_out, and_14_out, and_15_out, and_16_out, and_17_out, and_18_out);
  Multiplexer #(.enable("false"), .width(8)) multiplexer_7 (
    .in0(demultiplexer_2_out1), .in1(demultiplexer_1_out0[7:0]), .out(multiplexer_7_out), .sel(or_11_out[25]));
  Multiplexer #(.enable("false"), .width(8)) multiplexer_8 (
    .in0(demultiplexer_2_out3), .in1(demultiplexer_1_out1[7:0]), .out(multiplexer_8_out), .sel(or_11_out[25]));
  Multiplexer #(.enable("false"), .width(8)) multiplexer_9 (
    .in0(demultiplexer_2_out5), .in1(demultiplexer_1_out2[7:0]), .out(multiplexer_9_out), .sel(or_11_out[25]));
  assign and_21_out = {8{or_13_out[26]}} & A_q;  // AND_Gate and_21, 8 bits wide
  Register A (.D(DATAOUT), .en(or_11_out[0]), .Q(A_q), .clk(clock_1_out), .clr(RESET));
  // Probe on A_q
  or or_26 (or_26_out, and_10_out, adder_3_cout);
  or or_27 (or_27_out, and_20_out, and_19_out, or_26_out);
  xor xor_2 (xor_2_out, xor_1_out, A_q[2]);
  xor xor_3 (xor_3_out, xor_2_out, A_q[3]);
  not not_4 (not_4_out, or_25_out);
  Register C (.D(multiplexer_7_out), .en(or_20_out), .Q(C_q), .clk(clock_1_out), .clr(RESET));
  Register E (.D(multiplexer_8_out), .en(or_22_out), .Q(E_q), .clk(clock_1_out), .clr(RESET));
  Register L (.D(multiplexer_9_out), .en(or_24_out), .Q(L_q), .clk(clock_1_out), .clr(RESET));
  and and_22 (and_22_out, or_11_out[8], Carry_q[0]);
  Adder adder_3 (.a(A_q), .b(Temp_q), .out(adder_3_out), .cin(and_22_out), .cout(adder_3_cout));
  Subtractor subtractor_2 (.a(A_q), .b(Temp_q), .out(subtractor_2_out), .bout(subtractor_2_bout));  // open: bin
  assign and_23_out = A_q & Temp_q;  // AND_Gate and_23, 8 bits wide
  assign or_28_out = A_q | Temp_q;  // OR_Gate or_28, 8 bits wide
  assign xor_4_out = A_q ^ Temp_q;  // XOR_Gate xor_4, 8 bits wide
  Comparator #(.mode("unsigned")) comparator_5 (.a(A_q), .b(Temp_q));  // open: gt, eq, lt
  xor xor_5 (xor_5_out, xor_3_out, A_q[4]);
  xor xor_6 (xor_6_out, xor_5_out, A_q[5]);
  Shifter #(.width(9)) shifter_1 (.in({1'b0, A_q}), .\dist (4'b0001), .out(shifter_1_out));
  Shifter #(.shift("lr"), .width(9)) shifter_2 (.in({A_q, 1'b0}), .\dist (4'b0001), .out(shifter_2_out));
  Shifter #(.shift("rl"), .width(9)) shifter_3 (.in({1'b0, A_q}), .\dist (4'b0001), .out(shifter_3_out));
  Shifter #(.shift("rr"), .width(9)) shifter_4 (.in({A_q, 1'b0}), .\dist (4'b0001), .out(shifter_4_out));
  xor xor_7 (xor_7_out, xor_6_out, A_q[6]);
  xor xor_8 (xor_8_out, xor_7_out, A_q[7]);
  not not_5 (not_5_out, xor_8_out);
  Multiplexer #(.enable("false"), .select(3), .width(8)) multiplexer_10 (
    .in0(B_q), .in1(C_q), .in2(D_q), .in3(E_q), .in4(H_q), .in5(L_q), .out(multiplexer_10_out),
    .sel(or_11_out[18:16]));  // open: in6, in7
  and and_24 (and_24_out, not_5_out, not_3_out);
  Multiplexer #(.enable("false"), .select(2), .width(16)) multiplexer_11 (
    .in0({B_q, C_q}), .in1({D_q, E_q}), .in2({H_q, L_q}), .out(multiplexer_11_out), .sel(or_11_out[15:14]));  // open: in3
  xor Overflow (Overflow_out, or_27_out, multiplexer_15_out[7]);
  assign and_25_out = A_q & 8'hf;  // AND_Gate and_25, 8 bits wide
  assign and_26_out = Temp_q & 8'hf;  // AND_Gate and_26, 8 bits wide
  Adder #(.width(16)) adder_4 (.a(multiplexer_11_out), .b(16'h1), .out(adder_4_out));  // open: cin, cout
  Subtractor #(.width(16)) subtractor_3 (.a(multiplexer_11_out), .b(16'h1), .out(subtractor_3_out));  // open: bin, bout
  assign and_27_out = multiplexer_11_out & {16{or_11_out[24]}};  // AND_Gate and_27, 16 bits wide
  assign and_28_out = multiplexer_10_out & {8{or_11_out[24]}};  // AND_Gate and_28, 8 bits wide
  not not_6 (not_6_out, Carry_q[0]);
  or or_29 (or_29_out, and_24_out, Overflow_out);
  Adder adder_5 (.a(and_25_out), .b(and_26_out), .out(adder_5_out));  // open: cin, cout
  assign and_29_out = adder_5_out & 8'h10;  // AND_Gate and_29, 8 bits wide
  Multiplexer #(.enable("false"), .select(2), .width(16)) multiplexer_12 (
    .in0({16{1'b0}}), .in1(adder_4_out), .in2(subtractor_3_out), .out(multiplexer_12_out),
    .sel(or_13_out[22:21]));  // open: in3
  Multiplexer #(.enable("false"), .select(3)) multiplexer_13 (
    .in0(or_27_out), .in1(shifter_1_out[8]), .in2(shifter_2_out[0]), .in3(not_6_out), .in4(shifter_3_out[8]),
    .in5(shifter_4_out[0]), .out(multiplexer_13_out), .sel(or_12_out[7:5]));  // open: in6, in7
  Multiplexer #(.enable("false"), .select(3)) multiplexer_14 (
    .in0(or_29_out), .in1(Overflow_out), .in2(and_24_out), .in3(or_27_out), .out(multiplexer_14_out),
    .sel(or_12_out[10:8]));  // open: in4, in5, in6, in7
  Comparator #(.mode("unsigned")) comparator_6 (.a(and_29_out), .b(8'h10), .eq(comparator_6_eq));  // open: gt, lt
  Demultiplexer #(.enable("false"), .select(2), .width(16)) demultiplexer_3 (
    .out0(demultiplexer_3_out0), .out1(demultiplexer_3_out1), .out2(demultiplexer_3_out2), .in(ADRESS),
    .sel(or_11_out[13:12]));  // open: out3
  and and_30 (and_30_out, or_11_out[23], or_11_out[22]);
  Decoder #(.select(2)) decoder_22 (
    .out0(decoder_22_out0), .out1(decoder_22_out1), .out2(decoder_22_out2), .sel(or_11_out[13:12]),
    .en(and_30_out));  // open: out3
  Decoder #(.select(3)) decoder_23 (
    .out0(decoder_23_out0), .out1(decoder_23_out1), .out2(decoder_23_out2), .out3(decoder_23_out3),
    .out4(decoder_23_out4), .out5(decoder_23_out5), .sel(or_11_out[11:9]), .en(and_31_out));  // open: out6, out7
  and and_31 (and_31_out, not_7_out, or_11_out[23]);
  not not_7 (not_7_out, or_11_out[22]);
  Demultiplexer #(.enable("false"), .select(3), .width(8)) demultiplexer_4 (
    .out0(demultiplexer_4_out0), .out1(demultiplexer_4_out1), .out2(demultiplexer_4_out2),
    .out3(demultiplexer_4_out3), .out4(demultiplexer_4_out4), .out5(demultiplexer_4_out5), .in(DATAOUT),
    .sel(or_11_out[11:9]));  // open: out6, out7
  Multiplexer #(.enable("false"), .select(4), .width(8)) multiplexer_15 (
    .in0(adder_3_out), .in1(subtractor_2_out), .in2(and_23_out), .in3(or_28_out), .in4(xor_4_out),
    .in5({shifter_1_out[7:1], Carry_q[0]}), .in6({Carry_q[0], shifter_2_out[7:1]}), .in7(adder_2_out),
    .in8(subtractor_1_out), .in9({shifter_3_out[7:1], Carry_q[0]}), .in10({Carry_q[0], shifter_4_out[7:1]}),
    .out(multiplexer_15_out), .sel(or_13_out[31:28]));  // open: in11, in12, in13, in14, in15
  Multiplexer #(.enable("false"), .select(3)) multiplexer_16 (
    .in0(comparator_8_eq), .in1(not_4_out), .out(multiplexer_16_out), .sel(or_12_out[4:2]));  // open: in2, in3, in4, in5, in6, in7
  Comparator #(.mode("unsigned"), .width(4)) comparator_7 (
    .a(or_13_out[31:28]), .b(4'b0001), .eq(comparator_7_eq));  // open: gt, lt
  Comparator #(.mode("unsigned")) comparator_8 (
    .a(multiplexer_15_out), .b({8{1'b0}}), .eq(comparator_8_eq));  // open: gt, lt
  Multiplexer #(.enable("false"), .width(8)) multiplexer_17 (
    .in0(demultiplexer_4_out0), .in1(demultiplexer_3_out0[15:8]), .out(multiplexer_17_out),
    .sel(or_11_out[22]));
  Multiplexer #(.enable("false"), .width(8)) multiplexer_18 (
    .in0(demultiplexer_4_out2), .in1(demultiplexer_3_out1[15:8]), .out(multiplexer_18_out),
    .sel(or_11_out[22]));
  Multiplexer #(.enable("false"), .width(8)) multiplexer_19 (
    .in0(demultiplexer_4_out4), .in1(demultiplexer_3_out2[15:8]), .out(multiplexer_19_out),
    .sel(or_11_out[22]));
  assign and_32_out = multiplexer_15_out & {8{or_11_out[1]}};  // AND_Gate and_32, 8 bits wide
  Multiplexer #(.enable("false")) multiplexer_20 (
    .in0(comparator_6_eq), .in1(not_8_out), .out(multiplexer_20_out), .sel(or_11_out[3]));
  not not_8 (not_8_out, N_q[4]);
  or or_30 (or_30_out, decoder_22_out0, decoder_23_out0);
  or or_31 (or_31_out, decoder_22_out0, decoder_23_out1);
  or or_32 (or_32_out, decoder_22_out1, decoder_23_out2);
  or or_33 (or_33_out, decoder_22_out1, decoder_23_out3);
  or or_34 (or_34_out, decoder_22_out2, decoder_23_out4);
  or or_35 (or_35_out, decoder_22_out2, decoder_23_out5);
  or or_36 (or_36_out, multiplexer_13_out, or_12_out_2[5]);
  or or_37 (or_37_out, comparator_7_eq, or_12_out_2[4]);
  or or_38 (or_38_out, multiplexer_14_out, or_12_out_2[3]);
  or or_39 (or_39_out, multiplexer_20_out, or_12_out_2[2]);
  or or_40 (or_40_out, multiplexer_16_out, or_12_out_2[1]);
  or or_41 (or_41_out, multiplexer_15_out[7], or_12_out_2[0]);
  Register register_1 (.D(multiplexer_17_out), .en(or_30_out), .Q(register_1_q), .clk(clock_1_out), .clr(RESET));
  Register register_2 (.D(multiplexer_18_out), .en(or_32_out), .Q(register_2_q), .clk(clock_1_out), .clr(RESET));
  Register register_3 (.D(multiplexer_19_out), .en(or_34_out), .Q(register_3_q), .clk(clock_1_out), .clr(RESET));
  Register #(.width(1)) Carry (
    .D(or_36_out), .en(or_12_out_2[11]), .Q(Carry_q[0]), .clk(clock_1_out), .clr(or_42_out[5]));
  Register #(.width(1)) N (.D(or_37_out), .en(or_12_out_2[10]), .Q(N_q[1]), .clk(clock_1_out), .clr(or_42_out[4]));
  Register #(.width(1)) PV (.D(or_38_out), .en(or_12_out_2[9]), .Q(N_q[2]), .clk(clock_1_out), .clr(or_42_out[3]));
  Register #(.width(1)) H_flag (.D(or_39_out), .en(or_12_out_2[8]), .Q(N_q[4]), .clk(clock_1_out), .clr(or_42_out[2]));
  Register #(.width(1)) Z (.D(or_40_out), .en(or_12_out_2[7]), .Q(N_q[6]), .clk(clock_1_out), .clr(or_42_out[1]));
  Register #(.width(1)) S (.D(or_41_out), .en(or_12_out_2[6]), .Q(N_q[7]), .clk(clock_1_out), .clr(or_42_out[0]));
  assign or_42_out = {6{RESET}} | or_12_out_2[17:12];  // OR_Gate or_42, 6 bits wide
  Multiplexer #(.enable("false"), .width(8)) multiplexer_21 (
    .in0(demultiplexer_4_out1), .in1(demultiplexer_3_out0[7:0]), .out(multiplexer_21_out), .sel(or_11_out[22]));
  Multiplexer #(.enable("false"), .width(8)) multiplexer_22 (
    .in0(demultiplexer_4_out3), .in1(demultiplexer_3_out1[7:0]), .out(multiplexer_22_out), .sel(or_11_out[22]));
  Multiplexer #(.enable("false"), .width(8)) multiplexer_23 (
    .in0(demultiplexer_4_out5), .in1(demultiplexer_3_out2[7:0]), .out(multiplexer_23_out), .sel(or_11_out[22]));
  Register register_4 (.D(multiplexer_21_out), .en(or_31_out), .Q(register_4_q), .clk(clock_1_out), .clr(RESET));
  Register register_5 (.D(multiplexer_22_out), .en(or_33_out), .Q(register_5_q), .clk(clock_1_out), .clr(RESET));
  Register register_6 (.D(multiplexer_23_out), .en(or_35_out), .Q(register_6_q), .clk(clock_1_out), .clr(RESET));
  Decoder #(.select(2)) decoder_24 (
    .out0(decoder_24_out0), .out1(decoder_24_out1), .out2(decoder_24_out2), .sel(or_11_out[7:6]),
    .en(or_11_out[20]));  // open: out3
  Demultiplexer #(.enable("false"), .select(2), .width(16)) demultiplexer_5 (
    .out0(demultiplexer_5_out0), .out1(demultiplexer_5_out1), .out2(demultiplexer_5_out2), .in(ADRESS),
    .sel(or_11_out[7:6]));  // open: out3
  Multiplexer #(.enable("false"), .select(3), .width(8)) multiplexer_24 (
    .in0(register_1_q), .in1(register_4_q), .in2(register_2_q), .in3(register_5_q), .in4(register_3_q),
    .in5(register_6_q), .out(multiplexer_24_out), .sel(or_11_out[11:9]));  // open: in6, in7
  Register #(.width(16)) IX (.D(demultiplexer_5_out0), .en(decoder_24_out0), .Q(IX_q), .clk(clock_1_out), .clr(RESET));
  Register #(.width(16)) IY (.D(demultiplexer_5_out1), .en(decoder_24_out1), .Q(IY_q), .clk(clock_1_out), .clr(RESET));
  Register #(.width(16)) SP (.D(demultiplexer_5_out2), .en(decoder_24_out2), .Q(SP_q), .clk(clock_1_out), .clr(RESET));
  Register F (
    .D({N_q[7:6], 1'b0, N_q[4], 1'b0, N_q[2:1], Carry_q[0]}), .en(or_12_out[0]), .Q(F_q), .clk(clock_1_out),
    .clr(RESET));
  Multiplexer #(.enable("false"), .select(2), .width(16)) multiplexer_25 (
    .in0({register_1_q, register_4_q}), .in1({register_2_q, register_5_q}),
    .in2({register_3_q, register_6_q}), .out(multiplexer_25_out), .sel(or_11_out[13:12]));  // open: in3
  Multiplexer #(.enable("false"), .select(2), .width(16)) multiplexer_26 (
    .in0(IX_q), .in1(IY_q), .in2(SP_q), .out(multiplexer_26_out), .sel(or_11_out[7:6]));  // open: in3
  assign and_33_out = multiplexer_26_out & {16{or_11_out[19]}};  // AND_Gate and_33, 16 bits wide
  assign and_34_out = F_q & {8{or_11_out[2]}};  // AND_Gate and_34, 8 bits wide
  assign and_35_out = multiplexer_25_out & {16{or_11_out[21]}};  // AND_Gate and_35, 16 bits wide
  assign and_36_out = multiplexer_24_out & {8{or_11_out[21]}};  // AND_Gate and_36, 8 bits wide
endmodule

module Instructions0x (
  input  Sel_a,
  input  Sel_b,
  input  Sel_c,
  input  Sel_d,
  input  Sel_e,
  input  Sel_f,
  input  Sel_g,
  input  Sel_h,
  input  Sel_i,
  input  Sel_j,
  input  Sel_k,
  input  Sel_l,
  input  Sel_m,
  input  Sel_n,
  input  Sel_o,
  input  Sel_p,
  input  [4:0] Address,
  output [31:0] Lines,
  output [31:0] Linesa,
  output [31:0] Linesb
);

  wire [4:0] and_1_out, and_2_out, and_3_out, and_4_out, and_5_out, and_6_out, and_7_out, and_8_out,
       and_9_out, and_10_out, and_11_out, and_12_out, and_13_out, and_14_out, and_15_out, and_16_out,
       and_17_out, and_18_out, and_19_out, and_20_out, and_21_out, and_22_out, and_23_out, and_24_out,
       and_25_out, and_26_out, and_27_out, and_28_out, and_29_out, and_30_out, and_31_out, and_32_out,
       and_33_out, and_34_out, and_35_out, and_36_out, and_37_out, and_38_out, and_39_out, and_40_out,
       and_41_out, and_42_out, and_43_out, and_44_out, and_45_out, and_46_out, and_47_out, and_48_out;
  wire [31:0] aROM_a_data, aROM_b_data, aROM_c_data, aROM_d_data, aROM_e_data, aROM_f_data, aROM_g_data,
       aROM_h_data, aROM_i_data, aROM_j_data, aROM_k_data, aROM_l_data, aROM_m_data, aROM_n_data,
       aROM_o_data, aROM_p_data, bROM_a_data, bROM_b_data, bROM_c_data, bROM_d_data, bROM_e_data,
       bROM_f_data, bROM_g_data, bROM_h_data, bROM_i_data, bROM_j_data, bROM_k_data, bROM_l_data,
       bROM_m_data, bROM_n_data, bROM_o_data, bROM_p_data, or_1_out, or_2_out, or_3_out, or_4_out, or_5_out,
       or_6_out, or_7_out, or_8_out, or_9_out, or_10_out, or_11_out, or_12_out, or_13_out, or_14_out,
       or_15_out, or_16_out, or_17_out, or_18_out, or_19_out, or_20_out, or_21_out, or_22_out, or_23_out,
       or_24_out, or_25_out, or_26_out, or_27_out, or_28_out, or_29_out, or_30_out, or_31_out, or_32_out,
       or_33_out, or_34_out, or_35_out, or_36_out, or_37_out, or_38_out, or_39_out, or_40_out, or_41_out,
       or_42_out, ROM_a_data, ROM_b_data, ROM_c_data, ROM_d_data, ROM_e_data, ROM_f_data, ROM_g_data,
       ROM_h_data, ROM_i_data, ROM_j_data, ROM_k_data, ROM_l_data, ROM_m_data, ROM_n_data, ROM_o_data,
       ROM_p_data;

  ROM #(.addrWidth(5), .dataWidth(32)) ROM_a (.addr(and_1_out), .data(ROM_a_data));
  assign and_1_out = Address & {5{Sel_a}};  // AND_Gate and_1, 5 bits wide
  ROM #(.addrWidth(5), .dataWidth(32)) aROM_a (.addr(and_2_out), .data(aROM_a_data));
  assign and_2_out = Address & {5{Sel_a}};  // AND_Gate and_2, 5 bits wide
  ROM #(.addrWidth(5), .dataWidth(32)) bROM_a (.addr(and_3_out), .data(bROM_a_data));
  assign and_3_out = Address & {5{Sel_a}};  // AND_Gate and_3, 5 bits wide
  ROM #(.addrWidth(5), .dataWidth(32)) ROM_b (.addr(and_4_out), .data(ROM_b_data));
  assign and_4_out = Address & {5{Sel_b}};  // AND_Gate and_4, 5 bits wide
  ROM #(.addrWidth(5), .dataWidth(32)) aROM_b (.addr(and_5_out), .data(aROM_b_data));
  assign and_5_out = Address & {5{Sel_b}};  // AND_Gate and_5, 5 bits wide
  ROM #(.addrWidth(5), .dataWidth(32)) bROM_b (.addr(and_6_out), .data(bROM_b_data));
  assign and_6_out = Address & {5{Sel_b}};  // AND_Gate and_6, 5 bits wide
  ROM #(.addrWidth(5), .dataWidth(32)) ROM_c (.addr(and_7_out), .data(ROM_c_data));
  assign and_7_out = Address & {5{Sel_c}};  // AND_Gate and_7, 5 bits wide
  assign or_1_out = ROM_b_data | ROM_a_data;  // OR_Gate or_1, 32 bits wide
  ROM #(.addrWidth(5), .dataWidth(32)) aROM_c (.addr(and_8_out), .data(aROM_c_data));
  assign and_8_out = Address & {5{Sel_c}};  // AND_Gate and_8, 5 bits wide
  assign or_2_out = aROM_b_data | aROM_a_data;  // OR_Gate or_2, 32 bits wide
  ROM #(.addrWidth(5), .dataWidth(32)) bROM_c (.addr(and_9_out), .data(bROM_c_data));
  assign and_9_out = Address & {5{Sel_c}};  // AND_Gate and_9, 5 bits wide
  assign or_3_out = bROM_b_data | bROM_a_data;  // OR_Gate or_3, 32 bits wide
  ROM #(.addrWidth(5), .dataWidth(32)) ROM_d (.addr(and_10_out), .data(ROM_d_data));
  assign and_10_out = Address & {5{Sel_d}};  // AND_Gate and_10, 5 bits wide
  ROM #(.addrWidth(5), .dataWidth(32)) aROM_d (.addr(and_11_out), .data(aROM_d_data));
  assign and_11_out = Address & {5{Sel_d}};  // AND_Gate and_11, 5 bits wide
  ROM #(.addrWidth(5), .dataWidth(32)) bROM_d (.addr(and_12_out), .data(bROM_d_data));
  assign and_12_out = Address & {5{Sel_d}};  // AND_Gate and_12, 5 bits wide
  assign or_4_out = ROM_c_data | or_1_out;  // OR_Gate or_4, 32 bits wide
  assign or_5_out = aROM_c_data | or_2_out;  // OR_Gate or_5, 32 bits wide
  assign or_6_out = bROM_c_data | or_3_out;  // OR_Gate or_6, 32 bits wide
  ROM #(.addrWidth(5), .dataWidth(32)) ROM_e (.addr(and_13_out), .data(ROM_e_data));
  assign and_13_out = Address & {5{Sel_e}};  // AND_Gate and_13, 5 bits wide
  assign or_7_out = ROM_d_data | or_4_out;  // OR_Gate or_7, 32 bits wide
  ROM #(.addrWidth(5), .dataWidth(32)) aROM_e (.addr(and_14_out), .data(aROM_e_data));
  assign and_14_out = Address & {5{Sel_e}};  // AND_Gate and_14, 5 bits wide
  assign or_8_out = aROM_d_data | or_5_out;  // OR_Gate or_8, 32 bits wide
  ROM #(.addrWidth(5), .dataWidth(32)) bROM_e (.addr(and_15_out), .data(bROM_e_data));
  assign and_15_out = Address & {5{Sel_e}};  // AND_Gate and_15, 5 bits wide
  assign or_9_out = bROM_d_data | or_6_out;  // OR_Gate or_9, 32 bits wide
  ROM #(.addrWidth(5), .dataWidth(32)) ROM_f (.addr(and_16_out), .data(ROM_f_data));
  assign and_16_out = Address & {5{Sel_f}};  // AND_Gate and_16, 5 bits wide
  assign or_10_out = ROM_e_data | or_7_out;  // OR_Gate or_10, 32 bits wide
  ROM #(.addrWidth(5), .dataWidth(32)) aROM_f (.addr(and_17_out), .data(aROM_f_data));
  assign and_17_out = Address & {5{Sel_f}};  // AND_Gate and_17, 5 bits wide
  assign or_11_out = aROM_e_data | or_8_out;  // OR_Gate or_11, 32 bits wide
  ROM #(.addrWidth(5), .dataWidth(32)) bROM_f (.addr(and_18_out), .data(bROM_f_data));
  assign and_18_out = Address & {5{Sel_f}};  // AND_Gate and_18, 5 bits wide
  assign or_12_out = bROM_e_data | or_9_out;  // OR_Gate or_12, 32 bits wide
  ROM #(.addrWidth(5), .dataWidth(32)) ROM_g (.addr(and_19_out), .data(ROM_g_data));
  assign and_19_out = Address & {5{Sel_g}};  // AND_Gate and_19, 5 bits wide
  assign or_13_out = ROM_f_data | or_10_out;  // OR_Gate or_13, 32 bits wide
  ROM #(.addrWidth(5), .dataWidth(32)) aROM_g (.addr(and_20_out), .data(aROM_g_data));
  assign and_20_out = Address & {5{Sel_g}};  // AND_Gate and_20, 5 bits wide
  assign or_14_out = aROM_f_data | or_11_out;  // OR_Gate or_14, 32 bits wide
  ROM #(.addrWidth(5), .dataWidth(32)) bROM_g (.addr(and_21_out), .data(bROM_g_data));
  assign and_21_out = Address & {5{Sel_g}};  // AND_Gate and_21, 5 bits wide
  assign or_15_out = bROM_f_data | or_12_out;  // OR_Gate or_15, 32 bits wide
  ROM #(.addrWidth(5), .dataWidth(32)) ROM_h (.addr(and_22_out), .data(ROM_h_data));
  assign and_22_out = Address & {5{Sel_h}};  // AND_Gate and_22, 5 bits wide
  ROM #(.addrWidth(5), .dataWidth(32)) aROM_h (.addr(and_23_out), .data(aROM_h_data));
  assign and_23_out = Address & {5{Sel_h}};  // AND_Gate and_23, 5 bits wide
  ROM #(.addrWidth(5), .dataWidth(32)) bROM_h (.addr(and_24_out), .data(bROM_h_data));
  assign and_24_out = Address & {5{Sel_h}};  // AND_Gate and_24, 5 bits wide
  assign or_16_out = ROM_g_data | or_13_out;  // OR_Gate or_16, 32 bits wide
  assign or_17_out = aROM_g_data | or_14_out;  // OR_Gate or_17, 32 bits wide
  assign or_18_out = bROM_g_data | or_15_out;  // OR_Gate or_18, 32 bits wide
  ROM #(.addrWidth(5), .dataWidth(32)) ROM_i (.addr(and_25_out), .data(ROM_i_data));
  assign and_25_out = Address & {5{Sel_i}};  // AND_Gate and_25, 5 bits wide
  assign or_19_out = ROM_h_data | or_16_out;  // OR_Gate or_19, 32 bits wide
  ROM #(.addrWidth(5), .dataWidth(32)) aROM_i (.addr(and_26_out), .data(aROM_i_data));
  assign and_26_out = Address & {5{Sel_i}};  // AND_Gate and_26, 5 bits wide
  assign or_20_out = aROM_h_data | or_17_out;  // OR_Gate or_20, 32 bits wide
  ROM #(.addrWidth(5), .dataWidth(32)) bROM_i (.addr(and_27_out), .data(bROM_i_data));
  assign and_27_out = Address & {5{Sel_i}};  // AND_Gate and_27, 5 bits wide
  assign or_21_out = bROM_h_data | or_18_out;  // OR_Gate or_21, 32 bits wide
  ROM #(.addrWidth(5), .dataWidth(32)) ROM_j (.addr(and_28_out), .data(ROM_j_data));
  assign and_28_out = Address & {5{Sel_j}};  // AND_Gate and_28, 5 bits wide
  assign or_22_out = ROM_i_data | or_19_out;  // OR_Gate or_22, 32 bits wide
  ROM #(.addrWidth(5), .dataWidth(32)) aROM_j (.addr(and_29_out), .data(aROM_j_data));
  assign and_29_out = Address & {5{Sel_j}};  // AND_Gate and_29, 5 bits wide
  assign or_23_out = aROM_i_data | or_20_out;  // OR_Gate or_23, 32 bits wide
  ROM #(.addrWidth(5), .dataWidth(32)) bROM_j (.addr(and_30_out), .data(bROM_j_data));
  assign and_30_out = Address & {5{Sel_j}};  // AND_Gate and_30, 5 bits wide
  assign or_24_out = bROM_i_data | or_21_out;  // OR_Gate or_24, 32 bits wide
  ROM #(.addrWidth(5), .dataWidth(32)) ROM_k (.addr(and_31_out), .data(ROM_k_data));
  assign and_31_out = Address & {5{Sel_k}};  // AND_Gate and_31, 5 bits wide
  assign or_25_out = ROM_j_data | or_22_out;  // OR_Gate or_25, 32 bits wide
  ROM #(.addrWidth(5), .dataWidth(32)) aROM_k (.addr(and_32_out), .data(aROM_k_data));
  assign and_32_out = Address & {5{Sel_k}};  // AND_Gate and_32, 5 bits wide
  assign or_26_out = aROM_j_data | or_23_out;  // OR_Gate or_26, 32 bits wide
  ROM #(.addrWidth(5), .dataWidth(32)) bROM_k (.addr(and_33_out), .data(bROM_k_data));
  assign and_33_out = Address & {5{Sel_k}};  // AND_Gate and_33, 5 bits wide
  assign or_27_out = bROM_j_data | or_24_out;  // OR_Gate or_27, 32 bits wide
  ROM #(.addrWidth(5), .dataWidth(32)) ROM_l (.addr(and_34_out), .data(ROM_l_data));
  assign and_34_out = Address & {5{Sel_l}};  // AND_Gate and_34, 5 bits wide
  ROM #(.addrWidth(5), .dataWidth(32)) aROM_l (.addr(and_35_out), .data(aROM_l_data));
  assign and_35_out = Address & {5{Sel_l}};  // AND_Gate and_35, 5 bits wide
  ROM #(.addrWidth(5), .dataWidth(32)) bROM_l (.addr(and_36_out), .data(bROM_l_data));
  assign and_36_out = Address & {5{Sel_l}};  // AND_Gate and_36, 5 bits wide
  assign or_28_out = ROM_k_data | or_25_out;  // OR_Gate or_28, 32 bits wide
  assign or_29_out = aROM_k_data | or_26_out;  // OR_Gate or_29, 32 bits wide
  assign or_30_out = bROM_k_data | or_27_out;  // OR_Gate or_30, 32 bits wide
  ROM #(.addrWidth(5), .dataWidth(32)) ROM_m (.addr(and_37_out), .data(ROM_m_data));
  assign and_37_out = Address & {5{Sel_m}};  // AND_Gate and_37, 5 bits wide
  assign or_31_out = ROM_l_data | or_28_out;  // OR_Gate or_31, 32 bits wide
  ROM #(.addrWidth(5), .dataWidth(32)) aROM_m (.addr(and_38_out), .data(aROM_m_data));
  assign and_38_out = Address & {5{Sel_m}};  // AND_Gate and_38, 5 bits wide
  assign or_32_out = aROM_l_data | or_29_out;  // OR_Gate or_32, 32 bits wide
  ROM #(.addrWidth(5), .dataWidth(32)) bROM_m (.addr(and_39_out), .data(bROM_m_data));
  assign and_39_out = Address & {5{Sel_m}};  // AND_Gate and_39, 5 bits wide
  assign or_33_out = bROM_l_data | or_30_out;  // OR_Gate or_33, 32 bits wide
  ROM #(.addrWidth(5), .dataWidth(32)) ROM_n (.addr(and_40_out), .data(ROM_n_data));
  assign and_40_out = Address & {5{Sel_n}};  // AND_Gate and_40, 5 bits wide
  assign or_34_out = ROM_m_data | or_31_out;  // OR_Gate or_34, 32 bits wide
  ROM #(.addrWidth(5), .dataWidth(32)) aROM_n (.addr(and_41_out), .data(aROM_n_data));
  assign and_41_out = Address & {5{Sel_n}};  // AND_Gate and_41, 5 bits wide
  assign or_35_out = aROM_m_data | or_32_out;  // OR_Gate or_35, 32 bits wide
  ROM #(.addrWidth(5), .dataWidth(32)) bROM_n (.addr(and_42_out), .data(bROM_n_data));
  assign and_42_out = Address & {5{Sel_n}};  // AND_Gate and_42, 5 bits wide
  assign or_36_out = bROM_m_data | or_33_out;  // OR_Gate or_36, 32 bits wide
  ROM #(.addrWidth(5), .dataWidth(32)) ROM_o (.addr(and_43_out), .data(ROM_o_data));
  assign and_43_out = Address & {5{Sel_o}};  // AND_Gate and_43, 5 bits wide
  assign or_37_out = ROM_n_data | or_34_out;  // OR_Gate or_37, 32 bits wide
  ROM #(.addrWidth(5), .dataWidth(32)) aROM_o (.addr(and_44_out), .data(aROM_o_data));
  assign and_44_out = Address & {5{Sel_o}};  // AND_Gate and_44, 5 bits wide
  assign or_38_out = aROM_n_data | or_35_out;  // OR_Gate or_38, 32 bits wide
  ROM #(.addrWidth(5), .dataWidth(32)) bROM_o (.addr(and_45_out), .data(bROM_o_data));
  assign and_45_out = Address & {5{Sel_o}};  // AND_Gate and_45, 5 bits wide
  assign or_39_out = bROM_n_data | or_36_out;  // OR_Gate or_39, 32 bits wide
  ROM #(.addrWidth(5), .dataWidth(32)) ROM_p (.addr(and_46_out), .data(ROM_p_data));
  assign and_46_out = Address & {5{Sel_p}};  // AND_Gate and_46, 5 bits wide
  ROM #(.addrWidth(5), .dataWidth(32)) aROM_p (.addr(and_47_out), .data(aROM_p_data));
  assign and_47_out = Address & {5{Sel_p}};  // AND_Gate and_47, 5 bits wide
  ROM #(.addrWidth(5), .dataWidth(32)) bROM_p (.addr(and_48_out), .data(bROM_p_data));
  assign and_48_out = Address & {5{Sel_p}};  // AND_Gate and_48, 5 bits wide
  assign or_40_out = ROM_o_data | or_37_out;  // OR_Gate or_40, 32 bits wide
  assign or_41_out = aROM_o_data | or_38_out;  // OR_Gate or_41, 32 bits wide
  assign or_42_out = bROM_o_data | or_39_out;  // OR_Gate or_42, 32 bits wide
  assign Lines = ROM_p_data | or_40_out;  // OR_Gate or_43, 32 bits wide
  assign Linesa = aROM_p_data | or_41_out;  // OR_Gate or_44, 32 bits wide
  assign Linesb = bROM_p_data | or_42_out;  // OR_Gate or_45, 32 bits wide

  // Notes on the sheet:
  //   contents of ROM_a (hex, n*v repeats v):
  //   0 80000000
  //   contents of ROM_b (hex, n*v repeats v):
  //   0 10000000 20000000 0 8000000 4010000 10000000 20000000 0 8000000 4000000 80000000
  //   contents of bROM_b (hex, n*v repeats v):
  //   0 2000000 0 0 1000000 0 2000000 0 0 1000000
  //   contents of ROM_c (hex, n*v repeats v):
  //   0 23000010 8000000 80000000
  //   contents of bROM_c (hex, n*v repeats v):
  //   0 0 4000000 8000000
  //   contents of ROM_d (hex, n*v repeats v):
  //   0 20000010 86000000
  //   contents of bROM_d (hex, n*v repeats v):
  //   0 200000
  //   contents of ROM_e (hex, n*v repeats v):
  //   0 9000000 1 8000002 84000000
  //   contents of bROM_e (hex, n*v repeats v):
  //   0 0 0 70000000
  //   contents of ROM_f (hex, n*v repeats v):
  //   0 9000000 1 8000002 84000000
  //   contents of bROM_f (hex, n*v repeats v):
  //   0 0 0 80000000
  //   contents of ROM_g (hex, n*v repeats v):
  //   0 10000000 20000000 0 8000000 84000000
  //   contents of bROM_g (hex, n*v repeats v):
  //   0 2000000 0 0 1000000
  //   contents of ROM_h (hex, n*v repeats v):
  //   0 0 8000002 80000001
  //   contents of aROM_h (hex, n*v repeats v):
  //   0 2000080 52000000
  //   contents of bROM_h (hex, n*v repeats v):
  //   0 0 90000000
  //   contents of ROM_o (hex, n*v repeats v):
  //   0 10000000 20000000 0 8000000 84010000
  //   contents of bROM_o (hex, n*v repeats v):
  //   0 2000000 0 0 1000000
endmodule

module Instructions1x (
  input  Sel_a,
  input  Sel_b,
  input  Sel_c,
  input  Sel_d,
  input  Sel_e,
  input  Sel_f,
  input  Sel_g,
  input  Sel_h,
  input  Sel_i,
  input  Sel_j,
  input  Sel_k,
  input  Sel_l,
  input  Sel_m,
  input  Sel_n,
  input  Sel_o,
  input  Sel_p,
  input  [4:0] Address,
  output [31:0] Lines,
  output [31:0] Linesa,
  output [31:0] Linesb
);

  wire [4:0] and_1_out, and_2_out, and_3_out, and_4_out, and_5_out, and_6_out, and_7_out, and_8_out,
       and_9_out, and_10_out, and_11_out, and_12_out, and_13_out, and_14_out, and_15_out, and_16_out,
       and_17_out, and_18_out, and_19_out, and_20_out, and_21_out, and_22_out, and_23_out, and_24_out,
       and_25_out, and_26_out, and_27_out, and_28_out, and_29_out, and_30_out, and_31_out, and_32_out,
       and_33_out, and_34_out, and_35_out, and_36_out, and_37_out, and_38_out, and_39_out, and_40_out,
       and_41_out, and_42_out, and_43_out, and_44_out, and_45_out, and_46_out, and_47_out, and_48_out;
  wire [31:0] aROM_a_data, aROM_b_data, aROM_c_data, aROM_d_data, aROM_e_data, aROM_f_data, aROM_g_data,
       aROM_h_data, aROM_i_data, aROM_j_data, aROM_k_data, aROM_l_data, aROM_m_data, aROM_n_data,
       aROM_o_data, aROM_p_data, bROM_a_data, bROM_b_data, bROM_c_data, bROM_d_data, bROM_e_data,
       bROM_f_data, bROM_g_data, bROM_h_data, bROM_i_data, bROM_j_data, bROM_k_data, bROM_l_data,
       bROM_m_data, bROM_n_data, bROM_o_data, bROM_p_data, or_1_out, or_2_out, or_3_out, or_4_out, or_5_out,
       or_6_out, or_7_out, or_8_out, or_9_out, or_10_out, or_11_out, or_12_out, or_13_out, or_14_out,
       or_15_out, or_16_out, or_17_out, or_18_out, or_19_out, or_20_out, or_21_out, or_22_out, or_23_out,
       or_24_out, or_25_out, or_26_out, or_27_out, or_28_out, or_29_out, or_30_out, or_31_out, or_32_out,
       or_33_out, or_34_out, or_35_out, or_36_out, or_37_out, or_38_out, or_39_out, or_40_out, or_41_out,
       or_42_out, ROM_a_data, ROM_b_data, ROM_c_data, ROM_d_data, ROM_e_data, ROM_f_data, ROM_g_data,
       ROM_h_data, ROM_i_data, ROM_j_data, ROM_k_data, ROM_l_data, ROM_m_data, ROM_n_data, ROM_o_data,
       ROM_p_data;

  ROM #(.addrWidth(5), .dataWidth(32)) ROM_a (.addr(and_1_out), .data(ROM_a_data));
  assign and_1_out = Address & {5{Sel_a}};  // AND_Gate and_1, 5 bits wide
  ROM #(.addrWidth(5), .dataWidth(32)) aROM_a (.addr(and_2_out), .data(aROM_a_data));
  assign and_2_out = Address & {5{Sel_a}};  // AND_Gate and_2, 5 bits wide
  ROM #(.addrWidth(5), .dataWidth(32)) bROM_a (.addr(and_3_out), .data(bROM_a_data));
  assign and_3_out = Address & {5{Sel_a}};  // AND_Gate and_3, 5 bits wide
  ROM #(.addrWidth(5), .dataWidth(32)) ROM_b (.addr(and_4_out), .data(ROM_b_data));
  assign and_4_out = Address & {5{Sel_b}};  // AND_Gate and_4, 5 bits wide
  ROM #(.addrWidth(5), .dataWidth(32)) aROM_b (.addr(and_5_out), .data(aROM_b_data));
  assign and_5_out = Address & {5{Sel_b}};  // AND_Gate and_5, 5 bits wide
  ROM #(.addrWidth(5), .dataWidth(32)) bROM_b (.addr(and_6_out), .data(bROM_b_data));
  assign and_6_out = Address & {5{Sel_b}};  // AND_Gate and_6, 5 bits wide
  ROM #(.addrWidth(5), .dataWidth(32)) ROM_c (.addr(and_7_out), .data(ROM_c_data));
  assign and_7_out = Address & {5{Sel_c}};  // AND_Gate and_7, 5 bits wide
  assign or_1_out = ROM_b_data | ROM_a_data;  // OR_Gate or_1, 32 bits wide
  ROM #(.addrWidth(5), .dataWidth(32)) aROM_c (.addr(and_8_out), .data(aROM_c_data));
  assign and_8_out = Address & {5{Sel_c}};  // AND_Gate and_8, 5 bits wide
  assign or_2_out = aROM_b_data | aROM_a_data;  // OR_Gate or_2, 32 bits wide
  ROM #(.addrWidth(5), .dataWidth(32)) bROM_c (.addr(and_9_out), .data(bROM_c_data));
  assign and_9_out = Address & {5{Sel_c}};  // AND_Gate and_9, 5 bits wide
  assign or_3_out = bROM_b_data | bROM_a_data;  // OR_Gate or_3, 32 bits wide
  ROM #(.addrWidth(5), .dataWidth(32)) ROM_d (.addr(and_10_out), .data(ROM_d_data));
  assign and_10_out = Address & {5{Sel_d}};  // AND_Gate and_10, 5 bits wide
  ROM #(.addrWidth(5), .dataWidth(32)) aROM_d (.addr(and_11_out), .data(aROM_d_data));
  assign and_11_out = Address & {5{Sel_d}};  // AND_Gate and_11, 5 bits wide
  ROM #(.addrWidth(5), .dataWidth(32)) bROM_d (.addr(and_12_out), .data(bROM_d_data));
  assign and_12_out = Address & {5{Sel_d}};  // AND_Gate and_12, 5 bits wide
  assign or_4_out = ROM_c_data | or_1_out;  // OR_Gate or_4, 32 bits wide
  assign or_5_out = aROM_c_data | or_2_out;  // OR_Gate or_5, 32 bits wide
  assign or_6_out = bROM_c_data | or_3_out;  // OR_Gate or_6, 32 bits wide
  ROM #(.addrWidth(5), .dataWidth(32)) ROM_e (.addr(and_13_out), .data(ROM_e_data));
  assign and_13_out = Address & {5{Sel_e}};  // AND_Gate and_13, 5 bits wide
  assign or_7_out = ROM_d_data | or_4_out;  // OR_Gate or_7, 32 bits wide
  ROM #(.addrWidth(5), .dataWidth(32)) aROM_e (.addr(and_14_out), .data(aROM_e_data));
  assign and_14_out = Address & {5{Sel_e}};  // AND_Gate and_14, 5 bits wide
  assign or_8_out = aROM_d_data | or_5_out;  // OR_Gate or_8, 32 bits wide
  ROM #(.addrWidth(5), .dataWidth(32)) bROM_e (.addr(and_15_out), .data(bROM_e_data));
  assign and_15_out = Address & {5{Sel_e}};  // AND_Gate and_15, 5 bits wide
  assign or_9_out = bROM_d_data | or_6_out;  // OR_Gate or_9, 32 bits wide
  ROM #(.addrWidth(5), .dataWidth(32)) ROM_f (.addr(and_16_out), .data(ROM_f_data));
  assign and_16_out = Address & {5{Sel_f}};  // AND_Gate and_16, 5 bits wide
  assign or_10_out = ROM_e_data | or_7_out;  // OR_Gate or_10, 32 bits wide
  ROM #(.addrWidth(5), .dataWidth(32)) aROM_f (.addr(and_17_out), .data(aROM_f_data));
  assign and_17_out = Address & {5{Sel_f}};  // AND_Gate and_17, 5 bits wide
  assign or_11_out = aROM_e_data | or_8_out;  // OR_Gate or_11, 32 bits wide
  ROM #(.addrWidth(5), .dataWidth(32)) bROM_f (.addr(and_18_out), .data(bROM_f_data));
  assign and_18_out = Address & {5{Sel_f}};  // AND_Gate and_18, 5 bits wide
  assign or_12_out = bROM_e_data | or_9_out;  // OR_Gate or_12, 32 bits wide
  ROM #(.addrWidth(5), .dataWidth(32)) ROM_g (.addr(and_19_out), .data(ROM_g_data));
  assign and_19_out = Address & {5{Sel_g}};  // AND_Gate and_19, 5 bits wide
  assign or_13_out = ROM_f_data | or_10_out;  // OR_Gate or_13, 32 bits wide
  ROM #(.addrWidth(5), .dataWidth(32)) aROM_g (.addr(and_20_out), .data(aROM_g_data));
  assign and_20_out = Address & {5{Sel_g}};  // AND_Gate and_20, 5 bits wide
  assign or_14_out = aROM_f_data | or_11_out;  // OR_Gate or_14, 32 bits wide
  ROM #(.addrWidth(5), .dataWidth(32)) bROM_g (.addr(and_21_out), .data(bROM_g_data));
  assign and_21_out = Address & {5{Sel_g}};  // AND_Gate and_21, 5 bits wide
  assign or_15_out = bROM_f_data | or_12_out;  // OR_Gate or_15, 32 bits wide
  ROM #(.addrWidth(5), .dataWidth(32)) ROM_h (.addr(and_22_out), .data(ROM_h_data));
  assign and_22_out = Address & {5{Sel_h}};  // AND_Gate and_22, 5 bits wide
  ROM #(.addrWidth(5), .dataWidth(32)) aROM_h (.addr(and_23_out), .data(aROM_h_data));
  assign and_23_out = Address & {5{Sel_h}};  // AND_Gate and_23, 5 bits wide
  ROM #(.addrWidth(5), .dataWidth(32)) bROM_h (.addr(and_24_out), .data(bROM_h_data));
  assign and_24_out = Address & {5{Sel_h}};  // AND_Gate and_24, 5 bits wide
  assign or_16_out = ROM_g_data | or_13_out;  // OR_Gate or_16, 32 bits wide
  assign or_17_out = aROM_g_data | or_14_out;  // OR_Gate or_17, 32 bits wide
  assign or_18_out = bROM_g_data | or_15_out;  // OR_Gate or_18, 32 bits wide
  ROM #(.addrWidth(5), .dataWidth(32)) ROM_i (.addr(and_25_out), .data(ROM_i_data));
  assign and_25_out = Address & {5{Sel_i}};  // AND_Gate and_25, 5 bits wide
  assign or_19_out = ROM_h_data | or_16_out;  // OR_Gate or_19, 32 bits wide
  ROM #(.addrWidth(5), .dataWidth(32)) aROM_i (.addr(and_26_out), .data(aROM_i_data));
  assign and_26_out = Address & {5{Sel_i}};  // AND_Gate and_26, 5 bits wide
  assign or_20_out = aROM_h_data | or_17_out;  // OR_Gate or_20, 32 bits wide
  ROM #(.addrWidth(5), .dataWidth(32)) bROM_i (.addr(and_27_out), .data(bROM_i_data));
  assign and_27_out = Address & {5{Sel_i}};  // AND_Gate and_27, 5 bits wide
  assign or_21_out = bROM_h_data | or_18_out;  // OR_Gate or_21, 32 bits wide
  ROM #(.addrWidth(5), .dataWidth(32)) ROM_j (.addr(and_28_out), .data(ROM_j_data));
  assign and_28_out = Address & {5{Sel_j}};  // AND_Gate and_28, 5 bits wide
  assign or_22_out = ROM_i_data | or_19_out;  // OR_Gate or_22, 32 bits wide
  ROM #(.addrWidth(5), .dataWidth(32)) aROM_j (.addr(and_29_out), .data(aROM_j_data));
  assign and_29_out = Address & {5{Sel_j}};  // AND_Gate and_29, 5 bits wide
  assign or_23_out = aROM_i_data | or_20_out;  // OR_Gate or_23, 32 bits wide
  ROM #(.addrWidth(5), .dataWidth(32)) bROM_j (.addr(and_30_out), .data(bROM_j_data));
  assign and_30_out = Address & {5{Sel_j}};  // AND_Gate and_30, 5 bits wide
  assign or_24_out = bROM_i_data | or_21_out;  // OR_Gate or_24, 32 bits wide
  ROM #(.addrWidth(5), .dataWidth(32)) ROM_k (.addr(and_31_out), .data(ROM_k_data));
  assign and_31_out = Address & {5{Sel_k}};  // AND_Gate and_31, 5 bits wide
  assign or_25_out = ROM_j_data | or_22_out;  // OR_Gate or_25, 32 bits wide
  ROM #(.addrWidth(5), .dataWidth(32)) aROM_k (.addr(and_32_out), .data(aROM_k_data));
  assign and_32_out = Address & {5{Sel_k}};  // AND_Gate and_32, 5 bits wide
  assign or_26_out = aROM_j_data | or_23_out;  // OR_Gate or_26, 32 bits wide
  ROM #(.addrWidth(5), .dataWidth(32)) bROM_k (.addr(and_33_out), .data(bROM_k_data));
  assign and_33_out = Address & {5{Sel_k}};  // AND_Gate and_33, 5 bits wide
  assign or_27_out = bROM_j_data | or_24_out;  // OR_Gate or_27, 32 bits wide
  ROM #(.addrWidth(5), .dataWidth(32)) ROM_l (.addr(and_34_out), .data(ROM_l_data));
  assign and_34_out = Address & {5{Sel_l}};  // AND_Gate and_34, 5 bits wide
  ROM #(.addrWidth(5), .dataWidth(32)) aROM_l (.addr(and_35_out), .data(aROM_l_data));
  assign and_35_out = Address & {5{Sel_l}};  // AND_Gate and_35, 5 bits wide
  ROM #(.addrWidth(5), .dataWidth(32)) bROM_l (.addr(and_36_out), .data(bROM_l_data));
  assign and_36_out = Address & {5{Sel_l}};  // AND_Gate and_36, 5 bits wide
  assign or_28_out = ROM_k_data | or_25_out;  // OR_Gate or_28, 32 bits wide
  assign or_29_out = aROM_k_data | or_26_out;  // OR_Gate or_29, 32 bits wide
  assign or_30_out = bROM_k_data | or_27_out;  // OR_Gate or_30, 32 bits wide
  ROM #(.addrWidth(5), .dataWidth(32)) ROM_m (.addr(and_37_out), .data(ROM_m_data));
  assign and_37_out = Address & {5{Sel_m}};  // AND_Gate and_37, 5 bits wide
  assign or_31_out = ROM_l_data | or_28_out;  // OR_Gate or_31, 32 bits wide
  ROM #(.addrWidth(5), .dataWidth(32)) aROM_m (.addr(and_38_out), .data(aROM_m_data));
  assign and_38_out = Address & {5{Sel_m}};  // AND_Gate and_38, 5 bits wide
  assign or_32_out = aROM_l_data | or_29_out;  // OR_Gate or_32, 32 bits wide
  ROM #(.addrWidth(5), .dataWidth(32)) bROM_m (.addr(and_39_out), .data(bROM_m_data));
  assign and_39_out = Address & {5{Sel_m}};  // AND_Gate and_39, 5 bits wide
  assign or_33_out = bROM_l_data | or_30_out;  // OR_Gate or_33, 32 bits wide
  ROM #(.addrWidth(5), .dataWidth(32)) ROM_n (.addr(and_40_out), .data(ROM_n_data));
  assign and_40_out = Address & {5{Sel_n}};  // AND_Gate and_40, 5 bits wide
  assign or_34_out = ROM_m_data | or_31_out;  // OR_Gate or_34, 32 bits wide
  ROM #(.addrWidth(5), .dataWidth(32)) aROM_n (.addr(and_41_out), .data(aROM_n_data));
  assign and_41_out = Address & {5{Sel_n}};  // AND_Gate and_41, 5 bits wide
  assign or_35_out = aROM_m_data | or_32_out;  // OR_Gate or_35, 32 bits wide
  ROM #(.addrWidth(5), .dataWidth(32)) bROM_n (.addr(and_42_out), .data(bROM_n_data));
  assign and_42_out = Address & {5{Sel_n}};  // AND_Gate and_42, 5 bits wide
  assign or_36_out = bROM_m_data | or_33_out;  // OR_Gate or_36, 32 bits wide
  ROM #(.addrWidth(5), .dataWidth(32)) ROM_o (.addr(and_43_out), .data(ROM_o_data));
  assign and_43_out = Address & {5{Sel_o}};  // AND_Gate and_43, 5 bits wide
  assign or_37_out = ROM_n_data | or_34_out;  // OR_Gate or_37, 32 bits wide
  ROM #(.addrWidth(5), .dataWidth(32)) aROM_o (.addr(and_44_out), .data(aROM_o_data));
  assign and_44_out = Address & {5{Sel_o}};  // AND_Gate and_44, 5 bits wide
  assign or_38_out = aROM_n_data | or_35_out;  // OR_Gate or_38, 32 bits wide
  ROM #(.addrWidth(5), .dataWidth(32)) bROM_o (.addr(and_45_out), .data(bROM_o_data));
  assign and_45_out = Address & {5{Sel_o}};  // AND_Gate and_45, 5 bits wide
  assign or_39_out = bROM_n_data | or_36_out;  // OR_Gate or_39, 32 bits wide
  ROM #(.addrWidth(5), .dataWidth(32)) ROM_p (.addr(and_46_out), .data(ROM_p_data));
  assign and_46_out = Address & {5{Sel_p}};  // AND_Gate and_46, 5 bits wide
  ROM #(.addrWidth(5), .dataWidth(32)) aROM_p (.addr(and_47_out), .data(aROM_p_data));
  assign and_47_out = Address & {5{Sel_p}};  // AND_Gate and_47, 5 bits wide
  ROM #(.addrWidth(5), .dataWidth(32)) bROM_p (.addr(and_48_out), .data(bROM_p_data));
  assign and_48_out = Address & {5{Sel_p}};  // AND_Gate and_48, 5 bits wide
  assign or_40_out = ROM_o_data | or_37_out;  // OR_Gate or_40, 32 bits wide
  assign or_41_out = aROM_o_data | or_38_out;  // OR_Gate or_41, 32 bits wide
  assign or_42_out = bROM_o_data | or_39_out;  // OR_Gate or_42, 32 bits wide
  assign Lines = ROM_p_data | or_40_out;  // OR_Gate or_43, 32 bits wide
  assign Linesa = aROM_p_data | or_41_out;  // OR_Gate or_44, 32 bits wide
  assign Linesb = bROM_p_data | or_42_out;  // OR_Gate or_45, 32 bits wide

  // Notes on the sheet:
  //   contents of aROM_a (hex, n*v repeats v):
  //   0 10000000
  //   contents of bROM_a (hex, n*v repeats v):
  //   0 10000000
  //   contents of ROM_c (hex, n*v repeats v):
  //   0 23004010 8000000 80000000
  //   contents of bROM_c (hex, n*v repeats v):
  //   0 0 4000000 8000000
  //   contents of ROM_g (hex, n*v repeats v):
  //   0 10000000 20000000 0 8000000 84020000
  //   contents of bROM_g (hex, n*v repeats v):
  //   0 2000000 0 0 1000000
  //   contents of ROM_m (hex, n*v repeats v):
  //   0 9030000 1 8000002 84030000
  //   contents of aROM_m (hex, n*v repeats v):
  //   0 0 0 3f00100
  //   contents of bROM_m (hex, n*v repeats v):
  //   0 0 0 70000000
endmodule

module Instructions2x (
  input  Sel_a,
  input  Sel_b,
  input  Sel_c,
  input  Sel_d,
  input  Sel_e,
  input  Sel_f,
  input  Sel_g,
  input  Sel_h,
  input  Sel_i,
  input  Sel_j,
  input  Sel_k,
  input  Sel_l,
  input  Sel_m,
  input  Sel_n,
  input  Sel_o,
  input  Sel_p,
  input  [4:0] Address,
  output [31:0] Lines,
  output [31:0] Linesa,
  output [31:0] Linesb
);

  wire [4:0] and_1_out, and_2_out, and_3_out, and_4_out, and_5_out, and_6_out, and_7_out, and_8_out,
       and_9_out, and_10_out, and_11_out, and_12_out, and_13_out, and_14_out, and_15_out, and_16_out,
       and_17_out, and_18_out, and_19_out, and_20_out, and_21_out, and_22_out, and_23_out, and_24_out,
       and_25_out, and_26_out, and_27_out, and_28_out, and_29_out, and_30_out, and_31_out, and_32_out,
       and_33_out, and_34_out, and_35_out, and_36_out, and_37_out, and_38_out, and_39_out, and_40_out,
       and_41_out, and_42_out, and_43_out, and_44_out, and_45_out, and_46_out, and_47_out, and_48_out;
  wire [31:0] aROM_a_data, aROM_b_data, aROM_c_data, aROM_d_data, aROM_e_data, aROM_f_data, aROM_g_data,
       aROM_h_data, aROM_i_data, aROM_j_data, aROM_k_data, aROM_l_data, aROM_m_data, aROM_n_data,
       aROM_o_data, aROM_p_data, bROM_a_data, bROM_b_data, bROM_c_data, bROM_d_data, bROM_e_data,
       bROM_f_data, bROM_g_data, bROM_h_data, bROM_i_data, bROM_j_data, bROM_k_data, bROM_l_data,
       bROM_m_data, bROM_n_data, bROM_o_data, bROM_p_data, or_1_out, or_2_out, or_3_out, or_4_out, or_5_out,
       or_6_out, or_7_out, or_8_out, or_9_out, or_10_out, or_11_out, or_12_out, or_13_out, or_14_out,
       or_15_out, or_16_out, or_17_out, or_18_out, or_19_out, or_20_out, or_21_out, or_22_out, or_23_out,
       or_24_out, or_25_out, or_26_out, or_27_out, or_28_out, or_29_out, or_30_out, or_31_out, or_32_out,
       or_33_out, or_34_out, or_35_out, or_36_out, or_37_out, or_38_out, or_39_out, or_40_out, or_41_out,
       or_42_out, ROM_a_data, ROM_b_data, ROM_c_data, ROM_d_data, ROM_e_data, ROM_f_data, ROM_g_data,
       ROM_h_data, ROM_i_data, ROM_j_data, ROM_k_data, ROM_l_data, ROM_m_data, ROM_n_data, ROM_o_data,
       ROM_p_data;

  ROM #(.addrWidth(5), .dataWidth(32)) ROM_a (.addr(and_1_out), .data(ROM_a_data));
  assign and_1_out = Address & {5{Sel_a}};  // AND_Gate and_1, 5 bits wide
  ROM #(.addrWidth(5), .dataWidth(32)) aROM_a (.addr(and_2_out), .data(aROM_a_data));
  assign and_2_out = Address & {5{Sel_a}};  // AND_Gate and_2, 5 bits wide
  ROM #(.addrWidth(5), .dataWidth(32)) bROM_a (.addr(and_3_out), .data(bROM_a_data));
  assign and_3_out = Address & {5{Sel_a}};  // AND_Gate and_3, 5 bits wide
  ROM #(.addrWidth(5), .dataWidth(32)) ROM_b (.addr(and_4_out), .data(ROM_b_data));
  assign and_4_out = Address & {5{Sel_b}};  // AND_Gate and_4, 5 bits wide
  ROM #(.addrWidth(5), .dataWidth(32)) aROM_b (.addr(and_5_out), .data(aROM_b_data));
  assign and_5_out = Address & {5{Sel_b}};  // AND_Gate and_5, 5 bits wide
  ROM #(.addrWidth(5), .dataWidth(32)) bROM_b (.addr(and_6_out), .data(bROM_b_data));
  assign and_6_out = Address & {5{Sel_b}};  // AND_Gate and_6, 5 bits wide
  ROM #(.addrWidth(5), .dataWidth(32)) ROM_c (.addr(and_7_out), .data(ROM_c_data));
  assign and_7_out = Address & {5{Sel_c}};  // AND_Gate and_7, 5 bits wide
  assign or_1_out = ROM_b_data | ROM_a_data;  // OR_Gate or_1, 32 bits wide
  ROM #(.addrWidth(5), .dataWidth(32)) aROM_c (.addr(and_8_out), .data(aROM_c_data));
  assign and_8_out = Address & {5{Sel_c}};  // AND_Gate and_8, 5 bits wide
  assign or_2_out = aROM_b_data | aROM_a_data;  // OR_Gate or_2, 32 bits wide
  ROM #(.addrWidth(5), .dataWidth(32)) bROM_c (.addr(and_9_out), .data(bROM_c_data));
  assign and_9_out = Address & {5{Sel_c}};  // AND_Gate and_9, 5 bits wide
  assign or_3_out = bROM_b_data | bROM_a_data;  // OR_Gate or_3, 32 bits wide
  ROM #(.addrWidth(5), .dataWidth(32)) ROM_d (.addr(and_10_out), .data(ROM_d_data));
  assign and_10_out = Address & {5{Sel_d}};  // AND_Gate and_10, 5 bits wide
  ROM #(.addrWidth(5), .dataWidth(32)) aROM_d (.addr(and_11_out), .data(aROM_d_data));
  assign and_11_out = Address & {5{Sel_d}};  // AND_Gate and_11, 5 bits wide
  ROM #(.addrWidth(5), .dataWidth(32)) bROM_d (.addr(and_12_out), .data(bROM_d_data));
  assign and_12_out = Address & {5{Sel_d}};  // AND_Gate and_12, 5 bits wide
  assign or_4_out = ROM_c_data | or_1_out;  // OR_Gate or_4, 32 bits wide
  assign or_5_out = aROM_c_data | or_2_out;  // OR_Gate or_5, 32 bits wide
  assign or_6_out = bROM_c_data | or_3_out;  // OR_Gate or_6, 32 bits wide
  ROM #(.addrWidth(5), .dataWidth(32)) ROM_e (.addr(and_13_out), .data(ROM_e_data));
  assign and_13_out = Address & {5{Sel_e}};  // AND_Gate and_13, 5 bits wide
  assign or_7_out = ROM_d_data | or_4_out;  // OR_Gate or_7, 32 bits wide
  ROM #(.addrWidth(5), .dataWidth(32)) aROM_e (.addr(and_14_out), .data(aROM_e_data));
  assign and_14_out = Address & {5{Sel_e}};  // AND_Gate and_14, 5 bits wide
  assign or_8_out = aROM_d_data | or_5_out;  // OR_Gate or_8, 32 bits wide
  ROM #(.addrWidth(5), .dataWidth(32)) bROM_e (.addr(and_15_out), .data(bROM_e_data));
  assign and_15_out = Address & {5{Sel_e}};  // AND_Gate and_15, 5 bits wide
  assign or_9_out = bROM_d_data | or_6_out;  // OR_Gate or_9, 32 bits wide
  ROM #(.addrWidth(5), .dataWidth(32)) ROM_f (.addr(and_16_out), .data(ROM_f_data));
  assign and_16_out = Address & {5{Sel_f}};  // AND_Gate and_16, 5 bits wide
  assign or_10_out = ROM_e_data | or_7_out;  // OR_Gate or_10, 32 bits wide
  ROM #(.addrWidth(5), .dataWidth(32)) aROM_f (.addr(and_17_out), .data(aROM_f_data));
  assign and_17_out = Address & {5{Sel_f}};  // AND_Gate and_17, 5 bits wide
  assign or_11_out = aROM_e_data | or_8_out;  // OR_Gate or_11, 32 bits wide
  ROM #(.addrWidth(5), .dataWidth(32)) bROM_f (.addr(and_18_out), .data(bROM_f_data));
  assign and_18_out = Address & {5{Sel_f}};  // AND_Gate and_18, 5 bits wide
  assign or_12_out = bROM_e_data | or_9_out;  // OR_Gate or_12, 32 bits wide
  ROM #(.addrWidth(5), .dataWidth(32)) ROM_g (.addr(and_19_out), .data(ROM_g_data));
  assign and_19_out = Address & {5{Sel_g}};  // AND_Gate and_19, 5 bits wide
  assign or_13_out = ROM_f_data | or_10_out;  // OR_Gate or_13, 32 bits wide
  ROM #(.addrWidth(5), .dataWidth(32)) aROM_g (.addr(and_20_out), .data(aROM_g_data));
  assign and_20_out = Address & {5{Sel_g}};  // AND_Gate and_20, 5 bits wide
  assign or_14_out = aROM_f_data | or_11_out;  // OR_Gate or_14, 32 bits wide
  ROM #(.addrWidth(5), .dataWidth(32)) bROM_g (.addr(and_21_out), .data(bROM_g_data));
  assign and_21_out = Address & {5{Sel_g}};  // AND_Gate and_21, 5 bits wide
  assign or_15_out = bROM_f_data | or_12_out;  // OR_Gate or_15, 32 bits wide
  ROM #(.addrWidth(5), .dataWidth(32)) ROM_h (.addr(and_22_out), .data(ROM_h_data));
  assign and_22_out = Address & {5{Sel_h}};  // AND_Gate and_22, 5 bits wide
  ROM #(.addrWidth(5), .dataWidth(32)) aROM_h (.addr(and_23_out), .data(aROM_h_data));
  assign and_23_out = Address & {5{Sel_h}};  // AND_Gate and_23, 5 bits wide
  ROM #(.addrWidth(5), .dataWidth(32)) bROM_h (.addr(and_24_out), .data(bROM_h_data));
  assign and_24_out = Address & {5{Sel_h}};  // AND_Gate and_24, 5 bits wide
  assign or_16_out = ROM_g_data | or_13_out;  // OR_Gate or_16, 32 bits wide
  assign or_17_out = aROM_g_data | or_14_out;  // OR_Gate or_17, 32 bits wide
  assign or_18_out = bROM_g_data | or_15_out;  // OR_Gate or_18, 32 bits wide
  ROM #(.addrWidth(5), .dataWidth(32)) ROM_i (.addr(and_25_out), .data(ROM_i_data));
  assign and_25_out = Address & {5{Sel_i}};  // AND_Gate and_25, 5 bits wide
  assign or_19_out = ROM_h_data | or_16_out;  // OR_Gate or_19, 32 bits wide
  ROM #(.addrWidth(5), .dataWidth(32)) aROM_i (.addr(and_26_out), .data(aROM_i_data));
  assign and_26_out = Address & {5{Sel_i}};  // AND_Gate and_26, 5 bits wide
  assign or_20_out = aROM_h_data | or_17_out;  // OR_Gate or_20, 32 bits wide
  ROM #(.addrWidth(5), .dataWidth(32)) bROM_i (.addr(and_27_out), .data(bROM_i_data));
  assign and_27_out = Address & {5{Sel_i}};  // AND_Gate and_27, 5 bits wide
  assign or_21_out = bROM_h_data | or_18_out;  // OR_Gate or_21, 32 bits wide
  ROM #(.addrWidth(5), .dataWidth(32)) ROM_j (.addr(and_28_out), .data(ROM_j_data));
  assign and_28_out = Address & {5{Sel_j}};  // AND_Gate and_28, 5 bits wide
  assign or_22_out = ROM_i_data | or_19_out;  // OR_Gate or_22, 32 bits wide
  ROM #(.addrWidth(5), .dataWidth(32)) aROM_j (.addr(and_29_out), .data(aROM_j_data));
  assign and_29_out = Address & {5{Sel_j}};  // AND_Gate and_29, 5 bits wide
  assign or_23_out = aROM_i_data | or_20_out;  // OR_Gate or_23, 32 bits wide
  ROM #(.addrWidth(5), .dataWidth(32)) bROM_j (.addr(and_30_out), .data(bROM_j_data));
  assign and_30_out = Address & {5{Sel_j}};  // AND_Gate and_30, 5 bits wide
  assign or_24_out = bROM_i_data | or_21_out;  // OR_Gate or_24, 32 bits wide
  ROM #(.addrWidth(5), .dataWidth(32)) ROM_k (.addr(and_31_out), .data(ROM_k_data));
  assign and_31_out = Address & {5{Sel_k}};  // AND_Gate and_31, 5 bits wide
  assign or_25_out = ROM_j_data | or_22_out;  // OR_Gate or_25, 32 bits wide
  ROM #(.addrWidth(5), .dataWidth(32)) aROM_k (.addr(and_32_out), .data(aROM_k_data));
  assign and_32_out = Address & {5{Sel_k}};  // AND_Gate and_32, 5 bits wide
  assign or_26_out = aROM_j_data | or_23_out;  // OR_Gate or_26, 32 bits wide
  ROM #(.addrWidth(5), .dataWidth(32)) bROM_k (.addr(and_33_out), .data(bROM_k_data));
  assign and_33_out = Address & {5{Sel_k}};  // AND_Gate and_33, 5 bits wide
  assign or_27_out = bROM_j_data | or_24_out;  // OR_Gate or_27, 32 bits wide
  ROM #(.addrWidth(5), .dataWidth(32)) ROM_l (.addr(and_34_out), .data(ROM_l_data));
  assign and_34_out = Address & {5{Sel_l}};  // AND_Gate and_34, 5 bits wide
  ROM #(.addrWidth(5), .dataWidth(32)) aROM_l (.addr(and_35_out), .data(aROM_l_data));
  assign and_35_out = Address & {5{Sel_l}};  // AND_Gate and_35, 5 bits wide
  ROM #(.addrWidth(5), .dataWidth(32)) bROM_l (.addr(and_36_out), .data(bROM_l_data));
  assign and_36_out = Address & {5{Sel_l}};  // AND_Gate and_36, 5 bits wide
  assign or_28_out = ROM_k_data | or_25_out;  // OR_Gate or_28, 32 bits wide
  assign or_29_out = aROM_k_data | or_26_out;  // OR_Gate or_29, 32 bits wide
  assign or_30_out = bROM_k_data | or_27_out;  // OR_Gate or_30, 32 bits wide
  ROM #(.addrWidth(5), .dataWidth(32)) ROM_m (.addr(and_37_out), .data(ROM_m_data));
  assign and_37_out = Address & {5{Sel_m}};  // AND_Gate and_37, 5 bits wide
  assign or_31_out = ROM_l_data | or_28_out;  // OR_Gate or_31, 32 bits wide
  ROM #(.addrWidth(5), .dataWidth(32)) aROM_m (.addr(and_38_out), .data(aROM_m_data));
  assign and_38_out = Address & {5{Sel_m}};  // AND_Gate and_38, 5 bits wide
  assign or_32_out = aROM_l_data | or_29_out;  // OR_Gate or_32, 32 bits wide
  ROM #(.addrWidth(5), .dataWidth(32)) bROM_m (.addr(and_39_out), .data(bROM_m_data));
  assign and_39_out = Address & {5{Sel_m}};  // AND_Gate and_39, 5 bits wide
  assign or_33_out = bROM_l_data | or_30_out;  // OR_Gate or_33, 32 bits wide
  ROM #(.addrWidth(5), .dataWidth(32)) ROM_n (.addr(and_40_out), .data(ROM_n_data));
  assign and_40_out = Address & {5{Sel_n}};  // AND_Gate and_40, 5 bits wide
  assign or_34_out = ROM_m_data | or_31_out;  // OR_Gate or_34, 32 bits wide
  ROM #(.addrWidth(5), .dataWidth(32)) aROM_n (.addr(and_41_out), .data(aROM_n_data));
  assign and_41_out = Address & {5{Sel_n}};  // AND_Gate and_41, 5 bits wide
  assign or_35_out = aROM_m_data | or_32_out;  // OR_Gate or_35, 32 bits wide
  ROM #(.addrWidth(5), .dataWidth(32)) bROM_n (.addr(and_42_out), .data(bROM_n_data));
  assign and_42_out = Address & {5{Sel_n}};  // AND_Gate and_42, 5 bits wide
  assign or_36_out = bROM_m_data | or_33_out;  // OR_Gate or_36, 32 bits wide
  ROM #(.addrWidth(5), .dataWidth(32)) ROM_o (.addr(and_43_out), .data(ROM_o_data));
  assign and_43_out = Address & {5{Sel_o}};  // AND_Gate and_43, 5 bits wide
  assign or_37_out = ROM_n_data | or_34_out;  // OR_Gate or_37, 32 bits wide
  ROM #(.addrWidth(5), .dataWidth(32)) aROM_o (.addr(and_44_out), .data(aROM_o_data));
  assign and_44_out = Address & {5{Sel_o}};  // AND_Gate and_44, 5 bits wide
  assign or_38_out = aROM_n_data | or_35_out;  // OR_Gate or_38, 32 bits wide
  ROM #(.addrWidth(5), .dataWidth(32)) bROM_o (.addr(and_45_out), .data(bROM_o_data));
  assign and_45_out = Address & {5{Sel_o}};  // AND_Gate and_45, 5 bits wide
  assign or_39_out = bROM_n_data | or_36_out;  // OR_Gate or_39, 32 bits wide
  ROM #(.addrWidth(5), .dataWidth(32)) ROM_p (.addr(and_46_out), .data(ROM_p_data));
  assign and_46_out = Address & {5{Sel_p}};  // AND_Gate and_46, 5 bits wide
  ROM #(.addrWidth(5), .dataWidth(32)) aROM_p (.addr(and_47_out), .data(aROM_p_data));
  assign and_47_out = Address & {5{Sel_p}};  // AND_Gate and_47, 5 bits wide
  ROM #(.addrWidth(5), .dataWidth(32)) bROM_p (.addr(and_48_out), .data(bROM_p_data));
  assign and_48_out = Address & {5{Sel_p}};  // AND_Gate and_48, 5 bits wide
  assign or_40_out = ROM_o_data | or_37_out;  // OR_Gate or_40, 32 bits wide
  assign or_41_out = aROM_o_data | or_38_out;  // OR_Gate or_41, 32 bits wide
  assign or_42_out = bROM_o_data | or_39_out;  // OR_Gate or_42, 32 bits wide
  assign Lines = ROM_p_data | or_40_out;  // OR_Gate or_43, 32 bits wide
  assign Linesa = aROM_p_data | or_41_out;  // OR_Gate or_44, 32 bits wide
  assign Linesb = bROM_p_data | or_42_out;  // OR_Gate or_45, 32 bits wide

  // Notes on the sheet:
  //   contents of aROM_a (hex, n*v repeats v):
  //   0 10000000
  //   contents of bROM_a (hex, n*v repeats v):
  //   0 10000000
endmodule
module Instructions3x (
  input  Sel_a,
  input  Sel_b,
  input  Sel_c,
  input  Sel_d,
  input  Sel_e,
  input  Sel_f,
  input  Sel_g,
  input  Sel_h,
  input  Sel_i,
  input  Sel_j,
  input  Sel_k,
  input  Sel_l,
  input  Sel_m,
  input  Sel_n,
  input  Sel_o,
  input  Sel_p,
  input  [4:0] Address,
  output [31:0] Lines,
  output [31:0] Linesa,
  output [31:0] Linesb
);

  wire [4:0] and_1_out, and_2_out, and_3_out, and_4_out, and_5_out, and_6_out, and_7_out, and_8_out,
       and_9_out, and_10_out, and_11_out, and_12_out, and_13_out, and_14_out, and_15_out, and_16_out,
       and_17_out, and_18_out, and_19_out, and_20_out, and_21_out, and_22_out, and_23_out, and_24_out,
       and_25_out, and_26_out, and_27_out, and_28_out, and_29_out, and_30_out, and_31_out, and_32_out,
       and_33_out, and_34_out, and_35_out, and_36_out, and_37_out, and_38_out, and_39_out, and_40_out,
       and_41_out, and_42_out, and_43_out, and_44_out, and_45_out, and_46_out, and_47_out, and_48_out;
  wire [31:0] aROM_a_data, aROM_b_data, aROM_c_data, aROM_d_data, aROM_e_data, aROM_f_data, aROM_g_data,
       aROM_h_data, aROM_i_data, aROM_j_data, aROM_k_data, aROM_l_data, aROM_m_data, aROM_n_data,
       aROM_o_data, aROM_p_data, bROM_a_data, bROM_b_data, bROM_c_data, bROM_d_data, bROM_e_data,
       bROM_f_data, bROM_g_data, bROM_h_data, bROM_i_data, bROM_j_data, bROM_k_data, bROM_l_data,
       bROM_m_data, bROM_n_data, bROM_o_data, bROM_p_data, or_1_out, or_2_out, or_3_out, or_4_out, or_5_out,
       or_6_out, or_7_out, or_8_out, or_9_out, or_10_out, or_11_out, or_12_out, or_13_out, or_14_out,
       or_15_out, or_16_out, or_17_out, or_18_out, or_19_out, or_20_out, or_21_out, or_22_out, or_23_out,
       or_24_out, or_25_out, or_26_out, or_27_out, or_28_out, or_29_out, or_30_out, or_31_out, or_32_out,
       or_33_out, or_34_out, or_35_out, or_36_out, or_37_out, or_38_out, or_39_out, or_40_out, or_41_out,
       or_42_out, ROM_a_data, ROM_b_data, ROM_c_data, ROM_d_data, ROM_e_data, ROM_f_data, ROM_g_data,
       ROM_h_data, ROM_i_data, ROM_j_data, ROM_k_data, ROM_l_data, ROM_m_data, ROM_n_data, ROM_o_data,
       ROM_p_data;

  ROM #(.addrWidth(5), .dataWidth(32)) ROM_a (.addr(and_1_out), .data(ROM_a_data));
  assign and_1_out = Address & {5{Sel_a}};  // AND_Gate and_1, 5 bits wide
  ROM #(.addrWidth(5), .dataWidth(32)) aROM_a (.addr(and_2_out), .data(aROM_a_data));
  assign and_2_out = Address & {5{Sel_a}};  // AND_Gate and_2, 5 bits wide
  ROM #(.addrWidth(5), .dataWidth(32)) bROM_a (.addr(and_3_out), .data(bROM_a_data));
  assign and_3_out = Address & {5{Sel_a}};  // AND_Gate and_3, 5 bits wide
  ROM #(.addrWidth(5), .dataWidth(32)) ROM_b (.addr(and_4_out), .data(ROM_b_data));
  assign and_4_out = Address & {5{Sel_b}};  // AND_Gate and_4, 5 bits wide
  ROM #(.addrWidth(5), .dataWidth(32)) aROM_b (.addr(and_5_out), .data(aROM_b_data));
  assign and_5_out = Address & {5{Sel_b}};  // AND_Gate and_5, 5 bits wide
  ROM #(.addrWidth(5), .dataWidth(32)) bROM_b (.addr(and_6_out), .data(bROM_b_data));
  assign and_6_out = Address & {5{Sel_b}};  // AND_Gate and_6, 5 bits wide
  ROM #(.addrWidth(5), .dataWidth(32)) ROM_c (.addr(and_7_out), .data(ROM_c_data));
  assign and_7_out = Address & {5{Sel_c}};  // AND_Gate and_7, 5 bits wide
  assign or_1_out = ROM_b_data | ROM_a_data;  // OR_Gate or_1, 32 bits wide
  ROM #(.addrWidth(5), .dataWidth(32)) aROM_c (.addr(and_8_out), .data(aROM_c_data));
  assign and_8_out = Address & {5{Sel_c}};  // AND_Gate and_8, 5 bits wide
  assign or_2_out = aROM_b_data | aROM_a_data;  // OR_Gate or_2, 32 bits wide
  ROM #(.addrWidth(5), .dataWidth(32)) bROM_c (.addr(and_9_out), .data(bROM_c_data));
  assign and_9_out = Address & {5{Sel_c}};  // AND_Gate and_9, 5 bits wide
  assign or_3_out = bROM_b_data | bROM_a_data;  // OR_Gate or_3, 32 bits wide
  ROM #(.addrWidth(5), .dataWidth(32)) ROM_d (.addr(and_10_out), .data(ROM_d_data));
  assign and_10_out = Address & {5{Sel_d}};  // AND_Gate and_10, 5 bits wide
  ROM #(.addrWidth(5), .dataWidth(32)) aROM_d (.addr(and_11_out), .data(aROM_d_data));
  assign and_11_out = Address & {5{Sel_d}};  // AND_Gate and_11, 5 bits wide
  ROM #(.addrWidth(5), .dataWidth(32)) bROM_d (.addr(and_12_out), .data(bROM_d_data));
  assign and_12_out = Address & {5{Sel_d}};  // AND_Gate and_12, 5 bits wide
  assign or_4_out = ROM_c_data | or_1_out;  // OR_Gate or_4, 32 bits wide
  assign or_5_out = aROM_c_data | or_2_out;  // OR_Gate or_5, 32 bits wide
  assign or_6_out = bROM_c_data | or_3_out;  // OR_Gate or_6, 32 bits wide
  ROM #(.addrWidth(5), .dataWidth(32)) ROM_e (.addr(and_13_out), .data(ROM_e_data));
  assign and_13_out = Address & {5{Sel_e}};  // AND_Gate and_13, 5 bits wide
  assign or_7_out = ROM_d_data | or_4_out;  // OR_Gate or_7, 32 bits wide
  ROM #(.addrWidth(5), .dataWidth(32)) aROM_e (.addr(and_14_out), .data(aROM_e_data));
  assign and_14_out = Address & {5{Sel_e}};  // AND_Gate and_14, 5 bits wide
  assign or_8_out = aROM_d_data | or_5_out;  // OR_Gate or_8, 32 bits wide
  ROM #(.addrWidth(5), .dataWidth(32)) bROM_e (.addr(and_15_out), .data(bROM_e_data));
  assign and_15_out = Address & {5{Sel_e}};  // AND_Gate and_15, 5 bits wide
  assign or_9_out = bROM_d_data | or_6_out;  // OR_Gate or_9, 32 bits wide
  ROM #(.addrWidth(5), .dataWidth(32)) ROM_f (.addr(and_16_out), .data(ROM_f_data));
  assign and_16_out = Address & {5{Sel_f}};  // AND_Gate and_16, 5 bits wide
  assign or_10_out = ROM_e_data | or_7_out;  // OR_Gate or_10, 32 bits wide
  ROM #(.addrWidth(5), .dataWidth(32)) aROM_f (.addr(and_17_out), .data(aROM_f_data));
  assign and_17_out = Address & {5{Sel_f}};  // AND_Gate and_17, 5 bits wide
  assign or_11_out = aROM_e_data | or_8_out;  // OR_Gate or_11, 32 bits wide
  ROM #(.addrWidth(5), .dataWidth(32)) bROM_f (.addr(and_18_out), .data(bROM_f_data));
  assign and_18_out = Address & {5{Sel_f}};  // AND_Gate and_18, 5 bits wide
  assign or_12_out = bROM_e_data | or_9_out;  // OR_Gate or_12, 32 bits wide
  ROM #(.addrWidth(5), .dataWidth(32)) ROM_g (.addr(and_19_out), .data(ROM_g_data));
  assign and_19_out = Address & {5{Sel_g}};  // AND_Gate and_19, 5 bits wide
  assign or_13_out = ROM_f_data | or_10_out;  // OR_Gate or_13, 32 bits wide
  ROM #(.addrWidth(5), .dataWidth(32)) aROM_g (.addr(and_20_out), .data(aROM_g_data));
  assign and_20_out = Address & {5{Sel_g}};  // AND_Gate and_20, 5 bits wide
  assign or_14_out = aROM_f_data | or_11_out;  // OR_Gate or_14, 32 bits wide
  ROM #(.addrWidth(5), .dataWidth(32)) bROM_g (.addr(and_21_out), .data(bROM_g_data));
  assign and_21_out = Address & {5{Sel_g}};  // AND_Gate and_21, 5 bits wide
  assign or_15_out = bROM_f_data | or_12_out;  // OR_Gate or_15, 32 bits wide
  ROM #(.addrWidth(5), .dataWidth(32)) ROM_h (.addr(and_22_out), .data(ROM_h_data));
  assign and_22_out = Address & {5{Sel_h}};  // AND_Gate and_22, 5 bits wide
  ROM #(.addrWidth(5), .dataWidth(32)) aROM_h (.addr(and_23_out), .data(aROM_h_data));
  assign and_23_out = Address & {5{Sel_h}};  // AND_Gate and_23, 5 bits wide
  ROM #(.addrWidth(5), .dataWidth(32)) bROM_h (.addr(and_24_out), .data(bROM_h_data));
  assign and_24_out = Address & {5{Sel_h}};  // AND_Gate and_24, 5 bits wide
  assign or_16_out = ROM_g_data | or_13_out;  // OR_Gate or_16, 32 bits wide
  assign or_17_out = aROM_g_data | or_14_out;  // OR_Gate or_17, 32 bits wide
  assign or_18_out = bROM_g_data | or_15_out;  // OR_Gate or_18, 32 bits wide
  ROM #(.addrWidth(5), .dataWidth(32)) ROM_i (.addr(and_25_out), .data(ROM_i_data));
  assign and_25_out = Address & {5{Sel_i}};  // AND_Gate and_25, 5 bits wide
  assign or_19_out = ROM_h_data | or_16_out;  // OR_Gate or_19, 32 bits wide
  ROM #(.addrWidth(5), .dataWidth(32)) aROM_i (.addr(and_26_out), .data(aROM_i_data));
  assign and_26_out = Address & {5{Sel_i}};  // AND_Gate and_26, 5 bits wide
  assign or_20_out = aROM_h_data | or_17_out;  // OR_Gate or_20, 32 bits wide
  ROM #(.addrWidth(5), .dataWidth(32)) bROM_i (.addr(and_27_out), .data(bROM_i_data));
  assign and_27_out = Address & {5{Sel_i}};  // AND_Gate and_27, 5 bits wide
  assign or_21_out = bROM_h_data | or_18_out;  // OR_Gate or_21, 32 bits wide
  ROM #(.addrWidth(5), .dataWidth(32)) ROM_j (.addr(and_28_out), .data(ROM_j_data));
  assign and_28_out = Address & {5{Sel_j}};  // AND_Gate and_28, 5 bits wide
  assign or_22_out = ROM_i_data | or_19_out;  // OR_Gate or_22, 32 bits wide
  ROM #(.addrWidth(5), .dataWidth(32)) aROM_j (.addr(and_29_out), .data(aROM_j_data));
  assign and_29_out = Address & {5{Sel_j}};  // AND_Gate and_29, 5 bits wide
  assign or_23_out = aROM_i_data | or_20_out;  // OR_Gate or_23, 32 bits wide
  ROM #(.addrWidth(5), .dataWidth(32)) bROM_j (.addr(and_30_out), .data(bROM_j_data));
  assign and_30_out = Address & {5{Sel_j}};  // AND_Gate and_30, 5 bits wide
  assign or_24_out = bROM_i_data | or_21_out;  // OR_Gate or_24, 32 bits wide
  ROM #(.addrWidth(5), .dataWidth(32)) ROM_k (.addr(and_31_out), .data(ROM_k_data));
  assign and_31_out = Address & {5{Sel_k}};  // AND_Gate and_31, 5 bits wide
  assign or_25_out = ROM_j_data | or_22_out;  // OR_Gate or_25, 32 bits wide
  ROM #(.addrWidth(5), .dataWidth(32)) aROM_k (.addr(and_32_out), .data(aROM_k_data));
  assign and_32_out = Address & {5{Sel_k}};  // AND_Gate and_32, 5 bits wide
  assign or_26_out = aROM_j_data | or_23_out;  // OR_Gate or_26, 32 bits wide
  ROM #(.addrWidth(5), .dataWidth(32)) bROM_k (.addr(and_33_out), .data(bROM_k_data));
  assign and_33_out = Address & {5{Sel_k}};  // AND_Gate and_33, 5 bits wide
  assign or_27_out = bROM_j_data | or_24_out;  // OR_Gate or_27, 32 bits wide
  ROM #(.addrWidth(5), .dataWidth(32)) ROM_l (.addr(and_34_out), .data(ROM_l_data));
  assign and_34_out = Address & {5{Sel_l}};  // AND_Gate and_34, 5 bits wide
  ROM #(.addrWidth(5), .dataWidth(32)) aROM_l (.addr(and_35_out), .data(aROM_l_data));
  assign and_35_out = Address & {5{Sel_l}};  // AND_Gate and_35, 5 bits wide
  ROM #(.addrWidth(5), .dataWidth(32)) bROM_l (.addr(and_36_out), .data(bROM_l_data));
  assign and_36_out = Address & {5{Sel_l}};  // AND_Gate and_36, 5 bits wide
  assign or_28_out = ROM_k_data | or_25_out;  // OR_Gate or_28, 32 bits wide
  assign or_29_out = aROM_k_data | or_26_out;  // OR_Gate or_29, 32 bits wide
  assign or_30_out = bROM_k_data | or_27_out;  // OR_Gate or_30, 32 bits wide
  ROM #(.addrWidth(5), .dataWidth(32)) ROM_m (.addr(and_37_out), .data(ROM_m_data));
  assign and_37_out = Address & {5{Sel_m}};  // AND_Gate and_37, 5 bits wide
  assign or_31_out = ROM_l_data | or_28_out;  // OR_Gate or_31, 32 bits wide
  ROM #(.addrWidth(5), .dataWidth(32)) aROM_m (.addr(and_38_out), .data(aROM_m_data));
  assign and_38_out = Address & {5{Sel_m}};  // AND_Gate and_38, 5 bits wide
  assign or_32_out = aROM_l_data | or_29_out;  // OR_Gate or_32, 32 bits wide
  ROM #(.addrWidth(5), .dataWidth(32)) bROM_m (.addr(and_39_out), .data(bROM_m_data));
  assign and_39_out = Address & {5{Sel_m}};  // AND_Gate and_39, 5 bits wide
  assign or_33_out = bROM_l_data | or_30_out;  // OR_Gate or_33, 32 bits wide
  ROM #(.addrWidth(5), .dataWidth(32)) ROM_n (.addr(and_40_out), .data(ROM_n_data));
  assign and_40_out = Address & {5{Sel_n}};  // AND_Gate and_40, 5 bits wide
  assign or_34_out = ROM_m_data | or_31_out;  // OR_Gate or_34, 32 bits wide
  ROM #(.addrWidth(5), .dataWidth(32)) aROM_n (.addr(and_41_out), .data(aROM_n_data));
  assign and_41_out = Address & {5{Sel_n}};  // AND_Gate and_41, 5 bits wide
  assign or_35_out = aROM_m_data | or_32_out;  // OR_Gate or_35, 32 bits wide
  ROM #(.addrWidth(5), .dataWidth(32)) bROM_n (.addr(and_42_out), .data(bROM_n_data));
  assign and_42_out = Address & {5{Sel_n}};  // AND_Gate and_42, 5 bits wide
  assign or_36_out = bROM_m_data | or_33_out;  // OR_Gate or_36, 32 bits wide
  ROM #(.addrWidth(5), .dataWidth(32)) ROM_o (.addr(and_43_out), .data(ROM_o_data));
  assign and_43_out = Address & {5{Sel_o}};  // AND_Gate and_43, 5 bits wide
  assign or_37_out = ROM_n_data | or_34_out;  // OR_Gate or_37, 32 bits wide
  ROM #(.addrWidth(5), .dataWidth(32)) aROM_o (.addr(and_44_out), .data(aROM_o_data));
  assign and_44_out = Address & {5{Sel_o}};  // AND_Gate and_44, 5 bits wide
  assign or_38_out = aROM_n_data | or_35_out;  // OR_Gate or_38, 32 bits wide
  ROM #(.addrWidth(5), .dataWidth(32)) bROM_o (.addr(and_45_out), .data(bROM_o_data));
  assign and_45_out = Address & {5{Sel_o}};  // AND_Gate and_45, 5 bits wide
  assign or_39_out = bROM_n_data | or_36_out;  // OR_Gate or_39, 32 bits wide
  ROM #(.addrWidth(5), .dataWidth(32)) ROM_p (.addr(and_46_out), .data(ROM_p_data));
  assign and_46_out = Address & {5{Sel_p}};  // AND_Gate and_46, 5 bits wide
  ROM #(.addrWidth(5), .dataWidth(32)) aROM_p (.addr(and_47_out), .data(aROM_p_data));
  assign and_47_out = Address & {5{Sel_p}};  // AND_Gate and_47, 5 bits wide
  ROM #(.addrWidth(5), .dataWidth(32)) bROM_p (.addr(and_48_out), .data(bROM_p_data));
  assign and_48_out = Address & {5{Sel_p}};  // AND_Gate and_48, 5 bits wide
  assign or_40_out = ROM_o_data | or_37_out;  // OR_Gate or_40, 32 bits wide
  assign or_41_out = aROM_o_data | or_38_out;  // OR_Gate or_41, 32 bits wide
  assign or_42_out = bROM_o_data | or_39_out;  // OR_Gate or_42, 32 bits wide
  assign Lines = ROM_p_data | or_40_out;  // OR_Gate or_43, 32 bits wide
  assign Linesa = aROM_p_data | or_41_out;  // OR_Gate or_44, 32 bits wide
  assign Linesb = bROM_p_data | or_42_out;  // OR_Gate or_45, 32 bits wide

  // Notes on the sheet:
  //   contents of aROM_a (hex, n*v repeats v):
  //   0 10000000
  //   contents of bROM_a (hex, n*v repeats v):
  //   0 10000000
endmodule

module Instructions4x (
  input  Sel_a,
  input  Sel_b,
  input  Sel_c,
  input  Sel_d,
  input  Sel_e,
  input  Sel_f,
  input  Sel_g,
  input  Sel_h,
  input  Sel_i,
  input  Sel_j,
  input  Sel_k,
  input  Sel_l,
  input  Sel_m,
  input  Sel_n,
  input  Sel_o,
  input  Sel_p,
  input  [4:0] Address,
  output [31:0] Lines,
  output [31:0] Linesa,
  output [31:0] Linesb
);

  wire [4:0] and_1_out, and_2_out, and_3_out, and_4_out, and_5_out, and_6_out, and_7_out, and_8_out,
       and_9_out, and_10_out, and_11_out, and_12_out, and_13_out, and_14_out, and_15_out, and_16_out,
       and_17_out, and_18_out, and_19_out, and_20_out, and_21_out, and_22_out, and_23_out, and_24_out,
       and_25_out, and_26_out, and_27_out, and_28_out, and_29_out, and_30_out, and_31_out, and_32_out,
       and_33_out, and_34_out, and_35_out, and_36_out, and_37_out, and_38_out, and_39_out, and_40_out,
       and_41_out, and_42_out, and_43_out, and_44_out, and_45_out, and_46_out, and_47_out, and_48_out;
  wire [31:0] aROM_a_data, aROM_b_data, aROM_c_data, aROM_d_data, aROM_e_data, aROM_f_data, aROM_g_data,
       aROM_h_data, aROM_i_data, aROM_j_data, aROM_k_data, aROM_l_data, aROM_m_data, aROM_n_data,
       aROM_o_data, aROM_p_data, bROM_a_data, bROM_b_data, bROM_c_data, bROM_d_data, bROM_e_data,
       bROM_f_data, bROM_g_data, bROM_h_data, bROM_i_data, bROM_j_data, bROM_k_data, bROM_l_data,
       bROM_m_data, bROM_n_data, bROM_o_data, bROM_p_data, or_1_out, or_2_out, or_3_out, or_4_out, or_5_out,
       or_6_out, or_7_out, or_8_out, or_9_out, or_10_out, or_11_out, or_12_out, or_13_out, or_14_out,
       or_15_out, or_16_out, or_17_out, or_18_out, or_19_out, or_20_out, or_21_out, or_22_out, or_23_out,
       or_24_out, or_25_out, or_26_out, or_27_out, or_28_out, or_29_out, or_30_out, or_31_out, or_32_out,
       or_33_out, or_34_out, or_35_out, or_36_out, or_37_out, or_38_out, or_39_out, or_40_out, or_41_out,
       or_42_out, ROM_a_data, ROM_b_data, ROM_c_data, ROM_d_data, ROM_e_data, ROM_f_data, ROM_g_data,
       ROM_h_data, ROM_i_data, ROM_j_data, ROM_k_data, ROM_l_data, ROM_m_data, ROM_n_data, ROM_o_data,
       ROM_p_data;

  ROM #(.addrWidth(5), .dataWidth(32)) ROM_a (.addr(and_1_out), .data(ROM_a_data));
  assign and_1_out = Address & {5{Sel_a}};  // AND_Gate and_1, 5 bits wide
  ROM #(.addrWidth(5), .dataWidth(32)) aROM_a (.addr(and_2_out), .data(aROM_a_data));
  assign and_2_out = Address & {5{Sel_a}};  // AND_Gate and_2, 5 bits wide
  ROM #(.addrWidth(5), .dataWidth(32)) bROM_a (.addr(and_3_out), .data(bROM_a_data));
  assign and_3_out = Address & {5{Sel_a}};  // AND_Gate and_3, 5 bits wide
  ROM #(.addrWidth(5), .dataWidth(32)) ROM_b (.addr(and_4_out), .data(ROM_b_data));
  assign and_4_out = Address & {5{Sel_b}};  // AND_Gate and_4, 5 bits wide
  ROM #(.addrWidth(5), .dataWidth(32)) aROM_b (.addr(and_5_out), .data(aROM_b_data));
  assign and_5_out = Address & {5{Sel_b}};  // AND_Gate and_5, 5 bits wide
  ROM #(.addrWidth(5), .dataWidth(32)) bROM_b (.addr(and_6_out), .data(bROM_b_data));
  assign and_6_out = Address & {5{Sel_b}};  // AND_Gate and_6, 5 bits wide
  ROM #(.addrWidth(5), .dataWidth(32)) ROM_c (.addr(and_7_out), .data(ROM_c_data));
  assign and_7_out = Address & {5{Sel_c}};  // AND_Gate and_7, 5 bits wide
  assign or_1_out = ROM_b_data | ROM_a_data;  // OR_Gate or_1, 32 bits wide
  ROM #(.addrWidth(5), .dataWidth(32)) aROM_c (.addr(and_8_out), .data(aROM_c_data));
  assign and_8_out = Address & {5{Sel_c}};  // AND_Gate and_8, 5 bits wide
  assign or_2_out = aROM_b_data | aROM_a_data;  // OR_Gate or_2, 32 bits wide
  ROM #(.addrWidth(5), .dataWidth(32)) bROM_c (.addr(and_9_out), .data(bROM_c_data));
  assign and_9_out = Address & {5{Sel_c}};  // AND_Gate and_9, 5 bits wide
  assign or_3_out = bROM_b_data | bROM_a_data;  // OR_Gate or_3, 32 bits wide
  ROM #(.addrWidth(5), .dataWidth(32)) ROM_d (.addr(and_10_out), .data(ROM_d_data));
  assign and_10_out = Address & {5{Sel_d}};  // AND_Gate and_10, 5 bits wide
  ROM #(.addrWidth(5), .dataWidth(32)) aROM_d (.addr(and_11_out), .data(aROM_d_data));
  assign and_11_out = Address & {5{Sel_d}};  // AND_Gate and_11, 5 bits wide
  ROM #(.addrWidth(5), .dataWidth(32)) bROM_d (.addr(and_12_out), .data(bROM_d_data));
  assign and_12_out = Address & {5{Sel_d}};  // AND_Gate and_12, 5 bits wide
  assign or_4_out = ROM_c_data | or_1_out;  // OR_Gate or_4, 32 bits wide
  assign or_5_out = aROM_c_data | or_2_out;  // OR_Gate or_5, 32 bits wide
  assign or_6_out = bROM_c_data | or_3_out;  // OR_Gate or_6, 32 bits wide
  ROM #(.addrWidth(5), .dataWidth(32)) ROM_e (.addr(and_13_out), .data(ROM_e_data));
  assign and_13_out = Address & {5{Sel_e}};  // AND_Gate and_13, 5 bits wide
  assign or_7_out = ROM_d_data | or_4_out;  // OR_Gate or_7, 32 bits wide
  ROM #(.addrWidth(5), .dataWidth(32)) aROM_e (.addr(and_14_out), .data(aROM_e_data));
  assign and_14_out = Address & {5{Sel_e}};  // AND_Gate and_14, 5 bits wide
  assign or_8_out = aROM_d_data | or_5_out;  // OR_Gate or_8, 32 bits wide
  ROM #(.addrWidth(5), .dataWidth(32)) bROM_e (.addr(and_15_out), .data(bROM_e_data));
  assign and_15_out = Address & {5{Sel_e}};  // AND_Gate and_15, 5 bits wide
  assign or_9_out = bROM_d_data | or_6_out;  // OR_Gate or_9, 32 bits wide
  ROM #(.addrWidth(5), .dataWidth(32)) ROM_f (.addr(and_16_out), .data(ROM_f_data));
  assign and_16_out = Address & {5{Sel_f}};  // AND_Gate and_16, 5 bits wide
  assign or_10_out = ROM_e_data | or_7_out;  // OR_Gate or_10, 32 bits wide
  ROM #(.addrWidth(5), .dataWidth(32)) aROM_f (.addr(and_17_out), .data(aROM_f_data));
  assign and_17_out = Address & {5{Sel_f}};  // AND_Gate and_17, 5 bits wide
  assign or_11_out = aROM_e_data | or_8_out;  // OR_Gate or_11, 32 bits wide
  ROM #(.addrWidth(5), .dataWidth(32)) bROM_f (.addr(and_18_out), .data(bROM_f_data));
  assign and_18_out = Address & {5{Sel_f}};  // AND_Gate and_18, 5 bits wide
  assign or_12_out = bROM_e_data | or_9_out;  // OR_Gate or_12, 32 bits wide
  ROM #(.addrWidth(5), .dataWidth(32)) ROM_g (.addr(and_19_out), .data(ROM_g_data));
  assign and_19_out = Address & {5{Sel_g}};  // AND_Gate and_19, 5 bits wide
  assign or_13_out = ROM_f_data | or_10_out;  // OR_Gate or_13, 32 bits wide
  ROM #(.addrWidth(5), .dataWidth(32)) aROM_g (.addr(and_20_out), .data(aROM_g_data));
  assign and_20_out = Address & {5{Sel_g}};  // AND_Gate and_20, 5 bits wide
  assign or_14_out = aROM_f_data | or_11_out;  // OR_Gate or_14, 32 bits wide
  ROM #(.addrWidth(5), .dataWidth(32)) bROM_g (.addr(and_21_out), .data(bROM_g_data));
  assign and_21_out = Address & {5{Sel_g}};  // AND_Gate and_21, 5 bits wide
  assign or_15_out = bROM_f_data | or_12_out;  // OR_Gate or_15, 32 bits wide
  ROM #(.addrWidth(5), .dataWidth(32)) ROM_h (.addr(and_22_out), .data(ROM_h_data));
  assign and_22_out = Address & {5{Sel_h}};  // AND_Gate and_22, 5 bits wide
  ROM #(.addrWidth(5), .dataWidth(32)) aROM_h (.addr(and_23_out), .data(aROM_h_data));
  assign and_23_out = Address & {5{Sel_h}};  // AND_Gate and_23, 5 bits wide
  ROM #(.addrWidth(5), .dataWidth(32)) bROM_h (.addr(and_24_out), .data(bROM_h_data));
  assign and_24_out = Address & {5{Sel_h}};  // AND_Gate and_24, 5 bits wide
  assign or_16_out = ROM_g_data | or_13_out;  // OR_Gate or_16, 32 bits wide
  assign or_17_out = aROM_g_data | or_14_out;  // OR_Gate or_17, 32 bits wide
  assign or_18_out = bROM_g_data | or_15_out;  // OR_Gate or_18, 32 bits wide
  ROM #(.addrWidth(5), .dataWidth(32)) ROM_i (.addr(and_25_out), .data(ROM_i_data));
  assign and_25_out = Address & {5{Sel_i}};  // AND_Gate and_25, 5 bits wide
  assign or_19_out = ROM_h_data | or_16_out;  // OR_Gate or_19, 32 bits wide
  ROM #(.addrWidth(5), .dataWidth(32)) aROM_i (.addr(and_26_out), .data(aROM_i_data));
  assign and_26_out = Address & {5{Sel_i}};  // AND_Gate and_26, 5 bits wide
  assign or_20_out = aROM_h_data | or_17_out;  // OR_Gate or_20, 32 bits wide
  ROM #(.addrWidth(5), .dataWidth(32)) bROM_i (.addr(and_27_out), .data(bROM_i_data));
  assign and_27_out = Address & {5{Sel_i}};  // AND_Gate and_27, 5 bits wide
  assign or_21_out = bROM_h_data | or_18_out;  // OR_Gate or_21, 32 bits wide
  ROM #(.addrWidth(5), .dataWidth(32)) ROM_j (.addr(and_28_out), .data(ROM_j_data));
  assign and_28_out = Address & {5{Sel_j}};  // AND_Gate and_28, 5 bits wide
  assign or_22_out = ROM_i_data | or_19_out;  // OR_Gate or_22, 32 bits wide
  ROM #(.addrWidth(5), .dataWidth(32)) aROM_j (.addr(and_29_out), .data(aROM_j_data));
  assign and_29_out = Address & {5{Sel_j}};  // AND_Gate and_29, 5 bits wide
  assign or_23_out = aROM_i_data | or_20_out;  // OR_Gate or_23, 32 bits wide
  ROM #(.addrWidth(5), .dataWidth(32)) bROM_j (.addr(and_30_out), .data(bROM_j_data));
  assign and_30_out = Address & {5{Sel_j}};  // AND_Gate and_30, 5 bits wide
  assign or_24_out = bROM_i_data | or_21_out;  // OR_Gate or_24, 32 bits wide
  ROM #(.addrWidth(5), .dataWidth(32)) ROM_k (.addr(and_31_out), .data(ROM_k_data));
  assign and_31_out = Address & {5{Sel_k}};  // AND_Gate and_31, 5 bits wide
  assign or_25_out = ROM_j_data | or_22_out;  // OR_Gate or_25, 32 bits wide
  ROM #(.addrWidth(5), .dataWidth(32)) aROM_k (.addr(and_32_out), .data(aROM_k_data));
  assign and_32_out = Address & {5{Sel_k}};  // AND_Gate and_32, 5 bits wide
  assign or_26_out = aROM_j_data | or_23_out;  // OR_Gate or_26, 32 bits wide
  ROM #(.addrWidth(5), .dataWidth(32)) bROM_k (.addr(and_33_out), .data(bROM_k_data));
  assign and_33_out = Address & {5{Sel_k}};  // AND_Gate and_33, 5 bits wide
  assign or_27_out = bROM_j_data | or_24_out;  // OR_Gate or_27, 32 bits wide
  ROM #(.addrWidth(5), .dataWidth(32)) ROM_l (.addr(and_34_out), .data(ROM_l_data));
  assign and_34_out = Address & {5{Sel_l}};  // AND_Gate and_34, 5 bits wide
  ROM #(.addrWidth(5), .dataWidth(32)) aROM_l (.addr(and_35_out), .data(aROM_l_data));
  assign and_35_out = Address & {5{Sel_l}};  // AND_Gate and_35, 5 bits wide
  ROM #(.addrWidth(5), .dataWidth(32)) bROM_l (.addr(and_36_out), .data(bROM_l_data));
  assign and_36_out = Address & {5{Sel_l}};  // AND_Gate and_36, 5 bits wide
  assign or_28_out = ROM_k_data | or_25_out;  // OR_Gate or_28, 32 bits wide
  assign or_29_out = aROM_k_data | or_26_out;  // OR_Gate or_29, 32 bits wide
  assign or_30_out = bROM_k_data | or_27_out;  // OR_Gate or_30, 32 bits wide
  ROM #(.addrWidth(5), .dataWidth(32)) ROM_m (.addr(and_37_out), .data(ROM_m_data));
  assign and_37_out = Address & {5{Sel_m}};  // AND_Gate and_37, 5 bits wide
  assign or_31_out = ROM_l_data | or_28_out;  // OR_Gate or_31, 32 bits wide
  ROM #(.addrWidth(5), .dataWidth(32)) aROM_m (.addr(and_38_out), .data(aROM_m_data));
  assign and_38_out = Address & {5{Sel_m}};  // AND_Gate and_38, 5 bits wide
  assign or_32_out = aROM_l_data | or_29_out;  // OR_Gate or_32, 32 bits wide
  ROM #(.addrWidth(5), .dataWidth(32)) bROM_m (.addr(and_39_out), .data(bROM_m_data));
  assign and_39_out = Address & {5{Sel_m}};  // AND_Gate and_39, 5 bits wide
  assign or_33_out = bROM_l_data | or_30_out;  // OR_Gate or_33, 32 bits wide
  ROM #(.addrWidth(5), .dataWidth(32)) ROM_n (.addr(and_40_out), .data(ROM_n_data));
  assign and_40_out = Address & {5{Sel_n}};  // AND_Gate and_40, 5 bits wide
  assign or_34_out = ROM_m_data | or_31_out;  // OR_Gate or_34, 32 bits wide
  ROM #(.addrWidth(5), .dataWidth(32)) aROM_n (.addr(and_41_out), .data(aROM_n_data));
  assign and_41_out = Address & {5{Sel_n}};  // AND_Gate and_41, 5 bits wide
  assign or_35_out = aROM_m_data | or_32_out;  // OR_Gate or_35, 32 bits wide
  ROM #(.addrWidth(5), .dataWidth(32)) bROM_n (.addr(and_42_out), .data(bROM_n_data));
  assign and_42_out = Address & {5{Sel_n}};  // AND_Gate and_42, 5 bits wide
  assign or_36_out = bROM_m_data | or_33_out;  // OR_Gate or_36, 32 bits wide
  ROM #(.addrWidth(5), .dataWidth(32)) ROM_o (.addr(and_43_out), .data(ROM_o_data));
  assign and_43_out = Address & {5{Sel_o}};  // AND_Gate and_43, 5 bits wide
  assign or_37_out = ROM_n_data | or_34_out;  // OR_Gate or_37, 32 bits wide
  ROM #(.addrWidth(5), .dataWidth(32)) aROM_o (.addr(and_44_out), .data(aROM_o_data));
  assign and_44_out = Address & {5{Sel_o}};  // AND_Gate and_44, 5 bits wide
  assign or_38_out = aROM_n_data | or_35_out;  // OR_Gate or_38, 32 bits wide
  ROM #(.addrWidth(5), .dataWidth(32)) bROM_o (.addr(and_45_out), .data(bROM_o_data));
  assign and_45_out = Address & {5{Sel_o}};  // AND_Gate and_45, 5 bits wide
  assign or_39_out = bROM_n_data | or_36_out;  // OR_Gate or_39, 32 bits wide
  ROM #(.addrWidth(5), .dataWidth(32)) ROM_p (.addr(and_46_out), .data(ROM_p_data));
  assign and_46_out = Address & {5{Sel_p}};  // AND_Gate and_46, 5 bits wide
  ROM #(.addrWidth(5), .dataWidth(32)) aROM_p (.addr(and_47_out), .data(aROM_p_data));
  assign and_47_out = Address & {5{Sel_p}};  // AND_Gate and_47, 5 bits wide
  ROM #(.addrWidth(5), .dataWidth(32)) bROM_p (.addr(and_48_out), .data(bROM_p_data));
  assign and_48_out = Address & {5{Sel_p}};  // AND_Gate and_48, 5 bits wide
  assign or_40_out = ROM_o_data | or_37_out;  // OR_Gate or_40, 32 bits wide
  assign or_41_out = aROM_o_data | or_38_out;  // OR_Gate or_41, 32 bits wide
  assign or_42_out = bROM_o_data | or_39_out;  // OR_Gate or_42, 32 bits wide
  assign Lines = ROM_p_data | or_40_out;  // OR_Gate or_43, 32 bits wide
  assign Linesa = aROM_p_data | or_41_out;  // OR_Gate or_44, 32 bits wide
  assign Linesb = bROM_p_data | or_42_out;  // OR_Gate or_45, 32 bits wide

  // Notes on the sheet:
  //   contents of aROM_a (hex, n*v repeats v):
  //   0 10000000
  //   contents of ROM_b (hex, n*v repeats v):
  //   0 9010000 84000000
  //   contents of ROM_p (hex, n*v repeats v):
  //   0 8000000 84010000
  //   contents of bROM_p (hex, n*v repeats v):
  //   0 4000000
endmodule

module Instructions5x (
  input  Sel_a,
  input  Sel_b,
  input  Sel_c,
  input  Sel_d,
  input  Sel_e,
  input  Sel_f,
  input  Sel_g,
  input  Sel_h,
  input  Sel_i,
  input  Sel_j,
  input  Sel_k,
  input  Sel_l,
  input  Sel_m,
  input  Sel_n,
  input  Sel_o,
  input  Sel_p,
  input  [4:0] Address,
  output [31:0] Lines,
  output [31:0] Linesa,
  output [31:0] Linesb
);

  wire [4:0] and_1_out, and_2_out, and_3_out, and_4_out, and_5_out, and_6_out, and_7_out, and_8_out,
       and_9_out, and_10_out, and_11_out, and_12_out, and_13_out, and_14_out, and_15_out, and_16_out,
       and_17_out, and_18_out, and_19_out, and_20_out, and_21_out, and_22_out, and_23_out, and_24_out,
       and_25_out, and_26_out, and_27_out, and_28_out, and_29_out, and_30_out, and_31_out, and_32_out,
       and_33_out, and_34_out, and_35_out, and_36_out, and_37_out, and_38_out, and_39_out, and_40_out,
       and_41_out, and_42_out, and_43_out, and_44_out, and_45_out, and_46_out, and_47_out, and_48_out;
  wire [31:0] aROM_a_data, aROM_b_data, aROM_c_data, aROM_d_data, aROM_e_data, aROM_f_data, aROM_g_data,
       aROM_h_data, aROM_i_data, aROM_j_data, aROM_k_data, aROM_l_data, aROM_m_data, aROM_n_data,
       aROM_o_data, aROM_p_data, bROM_a_data, bROM_b_data, bROM_c_data, bROM_d_data, bROM_e_data,
       bROM_f_data, bROM_g_data, bROM_h_data, bROM_i_data, bROM_j_data, bROM_k_data, bROM_l_data,
       bROM_m_data, bROM_n_data, bROM_o_data, bROM_p_data, or_1_out, or_2_out, or_3_out, or_4_out, or_5_out,
       or_6_out, or_7_out, or_8_out, or_9_out, or_10_out, or_11_out, or_12_out, or_13_out, or_14_out,
       or_15_out, or_16_out, or_17_out, or_18_out, or_19_out, or_20_out, or_21_out, or_22_out, or_23_out,
       or_24_out, or_25_out, or_26_out, or_27_out, or_28_out, or_29_out, or_30_out, or_31_out, or_32_out,
       or_33_out, or_34_out, or_35_out, or_36_out, or_37_out, or_38_out, or_39_out, or_40_out, or_41_out,
       or_42_out, ROM_a_data, ROM_b_data, ROM_c_data, ROM_d_data, ROM_e_data, ROM_f_data, ROM_g_data,
       ROM_h_data, ROM_i_data, ROM_j_data, ROM_k_data, ROM_l_data, ROM_m_data, ROM_n_data, ROM_o_data,
       ROM_p_data;

  ROM #(.addrWidth(5), .dataWidth(32)) ROM_a (.addr(and_1_out), .data(ROM_a_data));
  assign and_1_out = Address & {5{Sel_a}};  // AND_Gate and_1, 5 bits wide
  ROM #(.addrWidth(5), .dataWidth(32)) aROM_a (.addr(and_2_out), .data(aROM_a_data));
  assign and_2_out = Address & {5{Sel_a}};  // AND_Gate and_2, 5 bits wide
  ROM #(.addrWidth(5), .dataWidth(32)) bROM_a (.addr(and_3_out), .data(bROM_a_data));
  assign and_3_out = Address & {5{Sel_a}};  // AND_Gate and_3, 5 bits wide
  ROM #(.addrWidth(5), .dataWidth(32)) ROM_b (.addr(and_4_out), .data(ROM_b_data));
  assign and_4_out = Address & {5{Sel_b}};  // AND_Gate and_4, 5 bits wide
  ROM #(.addrWidth(5), .dataWidth(32)) aROM_b (.addr(and_5_out), .data(aROM_b_data));
  assign and_5_out = Address & {5{Sel_b}};  // AND_Gate and_5, 5 bits wide
  ROM #(.addrWidth(5), .dataWidth(32)) bROM_b (.addr(and_6_out), .data(bROM_b_data));
  assign and_6_out = Address & {5{Sel_b}};  // AND_Gate and_6, 5 bits wide
  ROM #(.addrWidth(5), .dataWidth(32)) ROM_c (.addr(and_7_out), .data(ROM_c_data));
  assign and_7_out = Address & {5{Sel_c}};  // AND_Gate and_7, 5 bits wide
  assign or_1_out = ROM_b_data | ROM_a_data;  // OR_Gate or_1, 32 bits wide
  ROM #(.addrWidth(5), .dataWidth(32)) aROM_c (.addr(and_8_out), .data(aROM_c_data));
  assign and_8_out = Address & {5{Sel_c}};  // AND_Gate and_8, 5 bits wide
  assign or_2_out = aROM_b_data | aROM_a_data;  // OR_Gate or_2, 32 bits wide
  ROM #(.addrWidth(5), .dataWidth(32)) bROM_c (.addr(and_9_out), .data(bROM_c_data));
  assign and_9_out = Address & {5{Sel_c}};  // AND_Gate and_9, 5 bits wide
  assign or_3_out = bROM_b_data | bROM_a_data;  // OR_Gate or_3, 32 bits wide
  ROM #(.addrWidth(5), .dataWidth(32)) ROM_d (.addr(and_10_out), .data(ROM_d_data));
  assign and_10_out = Address & {5{Sel_d}};  // AND_Gate and_10, 5 bits wide
  ROM #(.addrWidth(5), .dataWidth(32)) aROM_d (.addr(and_11_out), .data(aROM_d_data));
  assign and_11_out = Address & {5{Sel_d}};  // AND_Gate and_11, 5 bits wide
  ROM #(.addrWidth(5), .dataWidth(32)) bROM_d (.addr(and_12_out), .data(bROM_d_data));
  assign and_12_out = Address & {5{Sel_d}};  // AND_Gate and_12, 5 bits wide
  assign or_4_out = ROM_c_data | or_1_out;  // OR_Gate or_4, 32 bits wide
  assign or_5_out = aROM_c_data | or_2_out;  // OR_Gate or_5, 32 bits wide
  assign or_6_out = bROM_c_data | or_3_out;  // OR_Gate or_6, 32 bits wide
  ROM #(.addrWidth(5), .dataWidth(32)) ROM_e (.addr(and_13_out), .data(ROM_e_data));
  assign and_13_out = Address & {5{Sel_e}};  // AND_Gate and_13, 5 bits wide
  assign or_7_out = ROM_d_data | or_4_out;  // OR_Gate or_7, 32 bits wide
  ROM #(.addrWidth(5), .dataWidth(32)) aROM_e (.addr(and_14_out), .data(aROM_e_data));
  assign and_14_out = Address & {5{Sel_e}};  // AND_Gate and_14, 5 bits wide
  assign or_8_out = aROM_d_data | or_5_out;  // OR_Gate or_8, 32 bits wide
  ROM #(.addrWidth(5), .dataWidth(32)) bROM_e (.addr(and_15_out), .data(bROM_e_data));
  assign and_15_out = Address & {5{Sel_e}};  // AND_Gate and_15, 5 bits wide
  assign or_9_out = bROM_d_data | or_6_out;  // OR_Gate or_9, 32 bits wide
  ROM #(.addrWidth(5), .dataWidth(32)) ROM_f (.addr(and_16_out), .data(ROM_f_data));
  assign and_16_out = Address & {5{Sel_f}};  // AND_Gate and_16, 5 bits wide
  assign or_10_out = ROM_e_data | or_7_out;  // OR_Gate or_10, 32 bits wide
  ROM #(.addrWidth(5), .dataWidth(32)) aROM_f (.addr(and_17_out), .data(aROM_f_data));
  assign and_17_out = Address & {5{Sel_f}};  // AND_Gate and_17, 5 bits wide
  assign or_11_out = aROM_e_data | or_8_out;  // OR_Gate or_11, 32 bits wide
  ROM #(.addrWidth(5), .dataWidth(32)) bROM_f (.addr(and_18_out), .data(bROM_f_data));
  assign and_18_out = Address & {5{Sel_f}};  // AND_Gate and_18, 5 bits wide
  assign or_12_out = bROM_e_data | or_9_out;  // OR_Gate or_12, 32 bits wide
  ROM #(.addrWidth(5), .dataWidth(32)) ROM_g (.addr(and_19_out), .data(ROM_g_data));
  assign and_19_out = Address & {5{Sel_g}};  // AND_Gate and_19, 5 bits wide
  assign or_13_out = ROM_f_data | or_10_out;  // OR_Gate or_13, 32 bits wide
  ROM #(.addrWidth(5), .dataWidth(32)) aROM_g (.addr(and_20_out), .data(aROM_g_data));
  assign and_20_out = Address & {5{Sel_g}};  // AND_Gate and_20, 5 bits wide
  assign or_14_out = aROM_f_data | or_11_out;  // OR_Gate or_14, 32 bits wide
  ROM #(.addrWidth(5), .dataWidth(32)) bROM_g (.addr(and_21_out), .data(bROM_g_data));
  assign and_21_out = Address & {5{Sel_g}};  // AND_Gate and_21, 5 bits wide
  assign or_15_out = bROM_f_data | or_12_out;  // OR_Gate or_15, 32 bits wide
  ROM #(.addrWidth(5), .dataWidth(32)) ROM_h (.addr(and_22_out), .data(ROM_h_data));
  assign and_22_out = Address & {5{Sel_h}};  // AND_Gate and_22, 5 bits wide
  ROM #(.addrWidth(5), .dataWidth(32)) aROM_h (.addr(and_23_out), .data(aROM_h_data));
  assign and_23_out = Address & {5{Sel_h}};  // AND_Gate and_23, 5 bits wide
  ROM #(.addrWidth(5), .dataWidth(32)) bROM_h (.addr(and_24_out), .data(bROM_h_data));
  assign and_24_out = Address & {5{Sel_h}};  // AND_Gate and_24, 5 bits wide
  assign or_16_out = ROM_g_data | or_13_out;  // OR_Gate or_16, 32 bits wide
  assign or_17_out = aROM_g_data | or_14_out;  // OR_Gate or_17, 32 bits wide
  assign or_18_out = bROM_g_data | or_15_out;  // OR_Gate or_18, 32 bits wide
  ROM #(.addrWidth(5), .dataWidth(32)) ROM_i (.addr(and_25_out), .data(ROM_i_data));
  assign and_25_out = Address & {5{Sel_i}};  // AND_Gate and_25, 5 bits wide
  assign or_19_out = ROM_h_data | or_16_out;  // OR_Gate or_19, 32 bits wide
  ROM #(.addrWidth(5), .dataWidth(32)) aROM_i (.addr(and_26_out), .data(aROM_i_data));
  assign and_26_out = Address & {5{Sel_i}};  // AND_Gate and_26, 5 bits wide
  assign or_20_out = aROM_h_data | or_17_out;  // OR_Gate or_20, 32 bits wide
  ROM #(.addrWidth(5), .dataWidth(32)) bROM_i (.addr(and_27_out), .data(bROM_i_data));
  assign and_27_out = Address & {5{Sel_i}};  // AND_Gate and_27, 5 bits wide
  assign or_21_out = bROM_h_data | or_18_out;  // OR_Gate or_21, 32 bits wide
  ROM #(.addrWidth(5), .dataWidth(32)) ROM_j (.addr(and_28_out), .data(ROM_j_data));
  assign and_28_out = Address & {5{Sel_j}};  // AND_Gate and_28, 5 bits wide
  assign or_22_out = ROM_i_data | or_19_out;  // OR_Gate or_22, 32 bits wide
  ROM #(.addrWidth(5), .dataWidth(32)) aROM_j (.addr(and_29_out), .data(aROM_j_data));
  assign and_29_out = Address & {5{Sel_j}};  // AND_Gate and_29, 5 bits wide
  assign or_23_out = aROM_i_data | or_20_out;  // OR_Gate or_23, 32 bits wide
  ROM #(.addrWidth(5), .dataWidth(32)) bROM_j (.addr(and_30_out), .data(bROM_j_data));
  assign and_30_out = Address & {5{Sel_j}};  // AND_Gate and_30, 5 bits wide
  assign or_24_out = bROM_i_data | or_21_out;  // OR_Gate or_24, 32 bits wide
  ROM #(.addrWidth(5), .dataWidth(32)) ROM_k (.addr(and_31_out), .data(ROM_k_data));
  assign and_31_out = Address & {5{Sel_k}};  // AND_Gate and_31, 5 bits wide
  assign or_25_out = ROM_j_data | or_22_out;  // OR_Gate or_25, 32 bits wide
  ROM #(.addrWidth(5), .dataWidth(32)) aROM_k (.addr(and_32_out), .data(aROM_k_data));
  assign and_32_out = Address & {5{Sel_k}};  // AND_Gate and_32, 5 bits wide
  assign or_26_out = aROM_j_data | or_23_out;  // OR_Gate or_26, 32 bits wide
  ROM #(.addrWidth(5), .dataWidth(32)) bROM_k (.addr(and_33_out), .data(bROM_k_data));
  assign and_33_out = Address & {5{Sel_k}};  // AND_Gate and_33, 5 bits wide
  assign or_27_out = bROM_j_data | or_24_out;  // OR_Gate or_27, 32 bits wide
  ROM #(.addrWidth(5), .dataWidth(32)) ROM_l (.addr(and_34_out), .data(ROM_l_data));
  assign and_34_out = Address & {5{Sel_l}};  // AND_Gate and_34, 5 bits wide
  ROM #(.addrWidth(5), .dataWidth(32)) aROM_l (.addr(and_35_out), .data(aROM_l_data));
  assign and_35_out = Address & {5{Sel_l}};  // AND_Gate and_35, 5 bits wide
  ROM #(.addrWidth(5), .dataWidth(32)) bROM_l (.addr(and_36_out), .data(bROM_l_data));
  assign and_36_out = Address & {5{Sel_l}};  // AND_Gate and_36, 5 bits wide
  assign or_28_out = ROM_k_data | or_25_out;  // OR_Gate or_28, 32 bits wide
  assign or_29_out = aROM_k_data | or_26_out;  // OR_Gate or_29, 32 bits wide
  assign or_30_out = bROM_k_data | or_27_out;  // OR_Gate or_30, 32 bits wide
  ROM #(.addrWidth(5), .dataWidth(32)) ROM_m (.addr(and_37_out), .data(ROM_m_data));
  assign and_37_out = Address & {5{Sel_m}};  // AND_Gate and_37, 5 bits wide
  assign or_31_out = ROM_l_data | or_28_out;  // OR_Gate or_31, 32 bits wide
  ROM #(.addrWidth(5), .dataWidth(32)) aROM_m (.addr(and_38_out), .data(aROM_m_data));
  assign and_38_out = Address & {5{Sel_m}};  // AND_Gate and_38, 5 bits wide
  assign or_32_out = aROM_l_data | or_29_out;  // OR_Gate or_32, 32 bits wide
  ROM #(.addrWidth(5), .dataWidth(32)) bROM_m (.addr(and_39_out), .data(bROM_m_data));
  assign and_39_out = Address & {5{Sel_m}};  // AND_Gate and_39, 5 bits wide
  assign or_33_out = bROM_l_data | or_30_out;  // OR_Gate or_33, 32 bits wide
  ROM #(.addrWidth(5), .dataWidth(32)) ROM_n (.addr(and_40_out), .data(ROM_n_data));
  assign and_40_out = Address & {5{Sel_n}};  // AND_Gate and_40, 5 bits wide
  assign or_34_out = ROM_m_data | or_31_out;  // OR_Gate or_34, 32 bits wide
  ROM #(.addrWidth(5), .dataWidth(32)) aROM_n (.addr(and_41_out), .data(aROM_n_data));
  assign and_41_out = Address & {5{Sel_n}};  // AND_Gate and_41, 5 bits wide
  assign or_35_out = aROM_m_data | or_32_out;  // OR_Gate or_35, 32 bits wide
  ROM #(.addrWidth(5), .dataWidth(32)) bROM_n (.addr(and_42_out), .data(bROM_n_data));
  assign and_42_out = Address & {5{Sel_n}};  // AND_Gate and_42, 5 bits wide
  assign or_36_out = bROM_m_data | or_33_out;  // OR_Gate or_36, 32 bits wide
  ROM #(.addrWidth(5), .dataWidth(32)) ROM_o (.addr(and_43_out), .data(ROM_o_data));
  assign and_43_out = Address & {5{Sel_o}};  // AND_Gate and_43, 5 bits wide
  assign or_37_out = ROM_n_data | or_34_out;  // OR_Gate or_37, 32 bits wide
  ROM #(.addrWidth(5), .dataWidth(32)) aROM_o (.addr(and_44_out), .data(aROM_o_data));
  assign and_44_out = Address & {5{Sel_o}};  // AND_Gate and_44, 5 bits wide
  assign or_38_out = aROM_n_data | or_35_out;  // OR_Gate or_38, 32 bits wide
  ROM #(.addrWidth(5), .dataWidth(32)) bROM_o (.addr(and_45_out), .data(bROM_o_data));
  assign and_45_out = Address & {5{Sel_o}};  // AND_Gate and_45, 5 bits wide
  assign or_39_out = bROM_n_data | or_36_out;  // OR_Gate or_39, 32 bits wide
  ROM #(.addrWidth(5), .dataWidth(32)) ROM_p (.addr(and_46_out), .data(ROM_p_data));
  assign and_46_out = Address & {5{Sel_p}};  // AND_Gate and_46, 5 bits wide
  ROM #(.addrWidth(5), .dataWidth(32)) aROM_p (.addr(and_47_out), .data(aROM_p_data));
  assign and_47_out = Address & {5{Sel_p}};  // AND_Gate and_47, 5 bits wide
  ROM #(.addrWidth(5), .dataWidth(32)) bROM_p (.addr(and_48_out), .data(bROM_p_data));
  assign and_48_out = Address & {5{Sel_p}};  // AND_Gate and_48, 5 bits wide
  assign or_40_out = ROM_o_data | or_37_out;  // OR_Gate or_40, 32 bits wide
  assign or_41_out = aROM_o_data | or_38_out;  // OR_Gate or_41, 32 bits wide
  assign or_42_out = bROM_o_data | or_39_out;  // OR_Gate or_42, 32 bits wide
  assign Lines = ROM_p_data | or_40_out;  // OR_Gate or_43, 32 bits wide
  assign Linesa = aROM_p_data | or_41_out;  // OR_Gate or_44, 32 bits wide
  assign Linesb = bROM_p_data | or_42_out;  // OR_Gate or_45, 32 bits wide

  // Notes on the sheet:
  //   contents of aROM_a (hex, n*v repeats v):
  //   0 10000000
  //   contents of bROM_a (hex, n*v repeats v):
  //   0 10000000
endmodule

module Instructions6x (
  input  Sel_a,
  input  Sel_b,
  input  Sel_c,
  input  Sel_d,
  input  Sel_e,
  input  Sel_f,
  input  Sel_g,
  input  Sel_h,
  input  Sel_i,
  input  Sel_j,
  input  Sel_k,
  input  Sel_l,
  input  Sel_m,
  input  Sel_n,
  input  Sel_o,
  input  Sel_p,
  input  [4:0] Address,
  output [31:0] Lines,
  output [31:0] Linesa,
  output [31:0] Linesb
);

  wire [4:0] and_1_out, and_2_out, and_3_out, and_4_out, and_5_out, and_6_out, and_7_out, and_8_out,
       and_9_out, and_10_out, and_11_out, and_12_out, and_13_out, and_14_out, and_15_out, and_16_out,
       and_17_out, and_18_out, and_19_out, and_20_out, and_21_out, and_22_out, and_23_out, and_24_out,
       and_25_out, and_26_out, and_27_out, and_28_out, and_29_out, and_30_out, and_31_out, and_32_out,
       and_33_out, and_34_out, and_35_out, and_36_out, and_37_out, and_38_out, and_39_out, and_40_out,
       and_41_out, and_42_out, and_43_out, and_44_out, and_45_out, and_46_out, and_47_out, and_48_out;
  wire [31:0] aROM_a_data, aROM_b_data, aROM_c_data, aROM_d_data, aROM_e_data, aROM_f_data, aROM_g_data,
       aROM_h_data, aROM_i_data, aROM_j_data, aROM_k_data, aROM_l_data, aROM_m_data, aROM_n_data,
       aROM_o_data, aROM_p_data, bROM_a_data, bROM_b_data, bROM_c_data, bROM_d_data, bROM_e_data,
       bROM_f_data, bROM_g_data, bROM_h_data, bROM_i_data, bROM_j_data, bROM_k_data, bROM_l_data,
       bROM_m_data, bROM_n_data, bROM_o_data, bROM_p_data, or_1_out, or_2_out, or_3_out, or_4_out, or_5_out,
       or_6_out, or_7_out, or_8_out, or_9_out, or_10_out, or_11_out, or_12_out, or_13_out, or_14_out,
       or_15_out, or_16_out, or_17_out, or_18_out, or_19_out, or_20_out, or_21_out, or_22_out, or_23_out,
       or_24_out, or_25_out, or_26_out, or_27_out, or_28_out, or_29_out, or_30_out, or_31_out, or_32_out,
       or_33_out, or_34_out, or_35_out, or_36_out, or_37_out, or_38_out, or_39_out, or_40_out, or_41_out,
       or_42_out, ROM_a_data, ROM_b_data, ROM_c_data, ROM_d_data, ROM_e_data, ROM_f_data, ROM_g_data,
       ROM_h_data, ROM_i_data, ROM_j_data, ROM_k_data, ROM_l_data, ROM_m_data, ROM_n_data, ROM_o_data,
       ROM_p_data;

  ROM #(.addrWidth(5), .dataWidth(32)) ROM_a (.addr(and_1_out), .data(ROM_a_data));
  assign and_1_out = Address & {5{Sel_a}};  // AND_Gate and_1, 5 bits wide
  ROM #(.addrWidth(5), .dataWidth(32)) aROM_a (.addr(and_2_out), .data(aROM_a_data));
  assign and_2_out = Address & {5{Sel_a}};  // AND_Gate and_2, 5 bits wide
  ROM #(.addrWidth(5), .dataWidth(32)) bROM_a (.addr(and_3_out), .data(bROM_a_data));
  assign and_3_out = Address & {5{Sel_a}};  // AND_Gate and_3, 5 bits wide
  ROM #(.addrWidth(5), .dataWidth(32)) ROM_b (.addr(and_4_out), .data(ROM_b_data));
  assign and_4_out = Address & {5{Sel_b}};  // AND_Gate and_4, 5 bits wide
  ROM #(.addrWidth(5), .dataWidth(32)) aROM_b (.addr(and_5_out), .data(aROM_b_data));
  assign and_5_out = Address & {5{Sel_b}};  // AND_Gate and_5, 5 bits wide
  ROM #(.addrWidth(5), .dataWidth(32)) bROM_b (.addr(and_6_out), .data(bROM_b_data));
  assign and_6_out = Address & {5{Sel_b}};  // AND_Gate and_6, 5 bits wide
  ROM #(.addrWidth(5), .dataWidth(32)) ROM_c (.addr(and_7_out), .data(ROM_c_data));
  assign and_7_out = Address & {5{Sel_c}};  // AND_Gate and_7, 5 bits wide
  assign or_1_out = ROM_b_data | ROM_a_data;  // OR_Gate or_1, 32 bits wide
  ROM #(.addrWidth(5), .dataWidth(32)) aROM_c (.addr(and_8_out), .data(aROM_c_data));
  assign and_8_out = Address & {5{Sel_c}};  // AND_Gate and_8, 5 bits wide
  assign or_2_out = aROM_b_data | aROM_a_data;  // OR_Gate or_2, 32 bits wide
  ROM #(.addrWidth(5), .dataWidth(32)) bROM_c (.addr(and_9_out), .data(bROM_c_data));
  assign and_9_out = Address & {5{Sel_c}};  // AND_Gate and_9, 5 bits wide
  assign or_3_out = bROM_b_data | bROM_a_data;  // OR_Gate or_3, 32 bits wide
  ROM #(.addrWidth(5), .dataWidth(32)) ROM_d (.addr(and_10_out), .data(ROM_d_data));
  assign and_10_out = Address & {5{Sel_d}};  // AND_Gate and_10, 5 bits wide
  ROM #(.addrWidth(5), .dataWidth(32)) aROM_d (.addr(and_11_out), .data(aROM_d_data));
  assign and_11_out = Address & {5{Sel_d}};  // AND_Gate and_11, 5 bits wide
  ROM #(.addrWidth(5), .dataWidth(32)) bROM_d (.addr(and_12_out), .data(bROM_d_data));
  assign and_12_out = Address & {5{Sel_d}};  // AND_Gate and_12, 5 bits wide
  assign or_4_out = ROM_c_data | or_1_out;  // OR_Gate or_4, 32 bits wide
  assign or_5_out = aROM_c_data | or_2_out;  // OR_Gate or_5, 32 bits wide
  assign or_6_out = bROM_c_data | or_3_out;  // OR_Gate or_6, 32 bits wide
  ROM #(.addrWidth(5), .dataWidth(32)) ROM_e (.addr(and_13_out), .data(ROM_e_data));
  assign and_13_out = Address & {5{Sel_e}};  // AND_Gate and_13, 5 bits wide
  assign or_7_out = ROM_d_data | or_4_out;  // OR_Gate or_7, 32 bits wide
  ROM #(.addrWidth(5), .dataWidth(32)) aROM_e (.addr(and_14_out), .data(aROM_e_data));
  assign and_14_out = Address & {5{Sel_e}};  // AND_Gate and_14, 5 bits wide
  assign or_8_out = aROM_d_data | or_5_out;  // OR_Gate or_8, 32 bits wide
  ROM #(.addrWidth(5), .dataWidth(32)) bROM_e (.addr(and_15_out), .data(bROM_e_data));
  assign and_15_out = Address & {5{Sel_e}};  // AND_Gate and_15, 5 bits wide
  assign or_9_out = bROM_d_data | or_6_out;  // OR_Gate or_9, 32 bits wide
  ROM #(.addrWidth(5), .dataWidth(32)) ROM_f (.addr(and_16_out), .data(ROM_f_data));
  assign and_16_out = Address & {5{Sel_f}};  // AND_Gate and_16, 5 bits wide
  assign or_10_out = ROM_e_data | or_7_out;  // OR_Gate or_10, 32 bits wide
  ROM #(.addrWidth(5), .dataWidth(32)) aROM_f (.addr(and_17_out), .data(aROM_f_data));
  assign and_17_out = Address & {5{Sel_f}};  // AND_Gate and_17, 5 bits wide
  assign or_11_out = aROM_e_data | or_8_out;  // OR_Gate or_11, 32 bits wide
  ROM #(.addrWidth(5), .dataWidth(32)) bROM_f (.addr(and_18_out), .data(bROM_f_data));
  assign and_18_out = Address & {5{Sel_f}};  // AND_Gate and_18, 5 bits wide
  assign or_12_out = bROM_e_data | or_9_out;  // OR_Gate or_12, 32 bits wide
  ROM #(.addrWidth(5), .dataWidth(32)) ROM_g (.addr(and_19_out), .data(ROM_g_data));
  assign and_19_out = Address & {5{Sel_g}};  // AND_Gate and_19, 5 bits wide
  assign or_13_out = ROM_f_data | or_10_out;  // OR_Gate or_13, 32 bits wide
  ROM #(.addrWidth(5), .dataWidth(32)) aROM_g (.addr(and_20_out), .data(aROM_g_data));
  assign and_20_out = Address & {5{Sel_g}};  // AND_Gate and_20, 5 bits wide
  assign or_14_out = aROM_f_data | or_11_out;  // OR_Gate or_14, 32 bits wide
  ROM #(.addrWidth(5), .dataWidth(32)) bROM_g (.addr(and_21_out), .data(bROM_g_data));
  assign and_21_out = Address & {5{Sel_g}};  // AND_Gate and_21, 5 bits wide
  assign or_15_out = bROM_f_data | or_12_out;  // OR_Gate or_15, 32 bits wide
  ROM #(.addrWidth(5), .dataWidth(32)) ROM_h (.addr(and_22_out), .data(ROM_h_data));
  assign and_22_out = Address & {5{Sel_h}};  // AND_Gate and_22, 5 bits wide
  ROM #(.addrWidth(5), .dataWidth(32)) aROM_h (.addr(and_23_out), .data(aROM_h_data));
  assign and_23_out = Address & {5{Sel_h}};  // AND_Gate and_23, 5 bits wide
  ROM #(.addrWidth(5), .dataWidth(32)) bROM_h (.addr(and_24_out), .data(bROM_h_data));
  assign and_24_out = Address & {5{Sel_h}};  // AND_Gate and_24, 5 bits wide
  assign or_16_out = ROM_g_data | or_13_out;  // OR_Gate or_16, 32 bits wide
  assign or_17_out = aROM_g_data | or_14_out;  // OR_Gate or_17, 32 bits wide
  assign or_18_out = bROM_g_data | or_15_out;  // OR_Gate or_18, 32 bits wide
  ROM #(.addrWidth(5), .dataWidth(32)) ROM_i (.addr(and_25_out), .data(ROM_i_data));
  assign and_25_out = Address & {5{Sel_i}};  // AND_Gate and_25, 5 bits wide
  assign or_19_out = ROM_h_data | or_16_out;  // OR_Gate or_19, 32 bits wide
  ROM #(.addrWidth(5), .dataWidth(32)) aROM_i (.addr(and_26_out), .data(aROM_i_data));
  assign and_26_out = Address & {5{Sel_i}};  // AND_Gate and_26, 5 bits wide
  assign or_20_out = aROM_h_data | or_17_out;  // OR_Gate or_20, 32 bits wide
  ROM #(.addrWidth(5), .dataWidth(32)) bROM_i (.addr(and_27_out), .data(bROM_i_data));
  assign and_27_out = Address & {5{Sel_i}};  // AND_Gate and_27, 5 bits wide
  assign or_21_out = bROM_h_data | or_18_out;  // OR_Gate or_21, 32 bits wide
  ROM #(.addrWidth(5), .dataWidth(32)) ROM_j (.addr(and_28_out), .data(ROM_j_data));
  assign and_28_out = Address & {5{Sel_j}};  // AND_Gate and_28, 5 bits wide
  assign or_22_out = ROM_i_data | or_19_out;  // OR_Gate or_22, 32 bits wide
  ROM #(.addrWidth(5), .dataWidth(32)) aROM_j (.addr(and_29_out), .data(aROM_j_data));
  assign and_29_out = Address & {5{Sel_j}};  // AND_Gate and_29, 5 bits wide
  assign or_23_out = aROM_i_data | or_20_out;  // OR_Gate or_23, 32 bits wide
  ROM #(.addrWidth(5), .dataWidth(32)) bROM_j (.addr(and_30_out), .data(bROM_j_data));
  assign and_30_out = Address & {5{Sel_j}};  // AND_Gate and_30, 5 bits wide
  assign or_24_out = bROM_i_data | or_21_out;  // OR_Gate or_24, 32 bits wide
  ROM #(.addrWidth(5), .dataWidth(32)) ROM_k (.addr(and_31_out), .data(ROM_k_data));
  assign and_31_out = Address & {5{Sel_k}};  // AND_Gate and_31, 5 bits wide
  assign or_25_out = ROM_j_data | or_22_out;  // OR_Gate or_25, 32 bits wide
  ROM #(.addrWidth(5), .dataWidth(32)) aROM_k (.addr(and_32_out), .data(aROM_k_data));
  assign and_32_out = Address & {5{Sel_k}};  // AND_Gate and_32, 5 bits wide
  assign or_26_out = aROM_j_data | or_23_out;  // OR_Gate or_26, 32 bits wide
  ROM #(.addrWidth(5), .dataWidth(32)) bROM_k (.addr(and_33_out), .data(bROM_k_data));
  assign and_33_out = Address & {5{Sel_k}};  // AND_Gate and_33, 5 bits wide
  assign or_27_out = bROM_j_data | or_24_out;  // OR_Gate or_27, 32 bits wide
  ROM #(.addrWidth(5), .dataWidth(32)) ROM_l (.addr(and_34_out), .data(ROM_l_data));
  assign and_34_out = Address & {5{Sel_l}};  // AND_Gate and_34, 5 bits wide
  ROM #(.addrWidth(5), .dataWidth(32)) aROM_l (.addr(and_35_out), .data(aROM_l_data));
  assign and_35_out = Address & {5{Sel_l}};  // AND_Gate and_35, 5 bits wide
  ROM #(.addrWidth(5), .dataWidth(32)) bROM_l (.addr(and_36_out), .data(bROM_l_data));
  assign and_36_out = Address & {5{Sel_l}};  // AND_Gate and_36, 5 bits wide
  assign or_28_out = ROM_k_data | or_25_out;  // OR_Gate or_28, 32 bits wide
  assign or_29_out = aROM_k_data | or_26_out;  // OR_Gate or_29, 32 bits wide
  assign or_30_out = bROM_k_data | or_27_out;  // OR_Gate or_30, 32 bits wide
  ROM #(.addrWidth(5), .dataWidth(32)) ROM_m (.addr(and_37_out), .data(ROM_m_data));
  assign and_37_out = Address & {5{Sel_m}};  // AND_Gate and_37, 5 bits wide
  assign or_31_out = ROM_l_data | or_28_out;  // OR_Gate or_31, 32 bits wide
  ROM #(.addrWidth(5), .dataWidth(32)) aROM_m (.addr(and_38_out), .data(aROM_m_data));
  assign and_38_out = Address & {5{Sel_m}};  // AND_Gate and_38, 5 bits wide
  assign or_32_out = aROM_l_data | or_29_out;  // OR_Gate or_32, 32 bits wide
  ROM #(.addrWidth(5), .dataWidth(32)) bROM_m (.addr(and_39_out), .data(bROM_m_data));
  assign and_39_out = Address & {5{Sel_m}};  // AND_Gate and_39, 5 bits wide
  assign or_33_out = bROM_l_data | or_30_out;  // OR_Gate or_33, 32 bits wide
  ROM #(.addrWidth(5), .dataWidth(32)) ROM_n (.addr(and_40_out), .data(ROM_n_data));
  assign and_40_out = Address & {5{Sel_n}};  // AND_Gate and_40, 5 bits wide
  assign or_34_out = ROM_m_data | or_31_out;  // OR_Gate or_34, 32 bits wide
  ROM #(.addrWidth(5), .dataWidth(32)) aROM_n (.addr(and_41_out), .data(aROM_n_data));
  assign and_41_out = Address & {5{Sel_n}};  // AND_Gate and_41, 5 bits wide
  assign or_35_out = aROM_m_data | or_32_out;  // OR_Gate or_35, 32 bits wide
  ROM #(.addrWidth(5), .dataWidth(32)) bROM_n (.addr(and_42_out), .data(bROM_n_data));
  assign and_42_out = Address & {5{Sel_n}};  // AND_Gate and_42, 5 bits wide
  assign or_36_out = bROM_m_data | or_33_out;  // OR_Gate or_36, 32 bits wide
  ROM #(.addrWidth(5), .dataWidth(32)) ROM_o (.addr(and_43_out), .data(ROM_o_data));
  assign and_43_out = Address & {5{Sel_o}};  // AND_Gate and_43, 5 bits wide
  assign or_37_out = ROM_n_data | or_34_out;  // OR_Gate or_37, 32 bits wide
  ROM #(.addrWidth(5), .dataWidth(32)) aROM_o (.addr(and_44_out), .data(aROM_o_data));
  assign and_44_out = Address & {5{Sel_o}};  // AND_Gate and_44, 5 bits wide
  assign or_38_out = aROM_n_data | or_35_out;  // OR_Gate or_38, 32 bits wide
  ROM #(.addrWidth(5), .dataWidth(32)) bROM_o (.addr(and_45_out), .data(bROM_o_data));
  assign and_45_out = Address & {5{Sel_o}};  // AND_Gate and_45, 5 bits wide
  assign or_39_out = bROM_n_data | or_36_out;  // OR_Gate or_39, 32 bits wide
  ROM #(.addrWidth(5), .dataWidth(32)) ROM_p (.addr(and_46_out), .data(ROM_p_data));
  assign and_46_out = Address & {5{Sel_p}};  // AND_Gate and_46, 5 bits wide
  ROM #(.addrWidth(5), .dataWidth(32)) aROM_p (.addr(and_47_out), .data(aROM_p_data));
  assign and_47_out = Address & {5{Sel_p}};  // AND_Gate and_47, 5 bits wide
  ROM #(.addrWidth(5), .dataWidth(32)) bROM_p (.addr(and_48_out), .data(bROM_p_data));
  assign and_48_out = Address & {5{Sel_p}};  // AND_Gate and_48, 5 bits wide
  assign or_40_out = ROM_o_data | or_37_out;  // OR_Gate or_40, 32 bits wide
  assign or_41_out = aROM_o_data | or_38_out;  // OR_Gate or_41, 32 bits wide
  assign or_42_out = bROM_o_data | or_39_out;  // OR_Gate or_42, 32 bits wide
  assign Lines = ROM_p_data | or_40_out;  // OR_Gate or_43, 32 bits wide
  assign Linesa = aROM_p_data | or_41_out;  // OR_Gate or_44, 32 bits wide
  assign Linesb = bROM_p_data | or_42_out;  // OR_Gate or_45, 32 bits wide

  // Notes on the sheet:
  //   contents of aROM_a (hex, n*v repeats v):
  //   0 10000000
  //   contents of bROM_a (hex, n*v repeats v):
  //   0 10000000
endmodule

module Instructions7x (
  input  Sel_a,
  input  Sel_b,
  input  Sel_c,
  input  Sel_d,
  input  Sel_e,
  input  Sel_f,
  input  Sel_g,
  input  Sel_h,
  input  Sel_i,
  input  Sel_j,
  input  Sel_k,
  input  Sel_l,
  input  Sel_m,
  input  Sel_n,
  input  Sel_o,
  input  Sel_p,
  input  [4:0] Address,
  output [31:0] Lines,
  output [31:0] Linesa,
  output [31:0] Linesb
);

  wire [4:0] and_1_out, and_2_out, and_3_out, and_4_out, and_5_out, and_6_out, and_7_out, and_8_out,
       and_9_out, and_10_out, and_11_out, and_12_out, and_13_out, and_14_out, and_15_out, and_16_out,
       and_17_out, and_18_out, and_19_out, and_20_out, and_21_out, and_22_out, and_23_out, and_24_out,
       and_25_out, and_26_out, and_27_out, and_28_out, and_29_out, and_30_out, and_31_out, and_32_out,
       and_33_out, and_34_out, and_35_out, and_36_out, and_37_out, and_38_out, and_39_out, and_40_out,
       and_41_out, and_42_out, and_43_out, and_44_out, and_45_out, and_46_out, and_47_out, and_48_out;
  wire [31:0] aROM_a_data, aROM_b_data, aROM_c_data, aROM_d_data, aROM_e_data, aROM_f_data, aROM_g_data,
       aROM_h_data, aROM_i_data, aROM_j_data, aROM_k_data, aROM_l_data, aROM_m_data, aROM_n_data,
       aROM_o_data, aROM_p_data, bROM_a_data, bROM_b_data, bROM_c_data, bROM_d_data, bROM_e_data,
       bROM_f_data, bROM_g_data, bROM_h_data, bROM_i_data, bROM_j_data, bROM_k_data, bROM_l_data,
       bROM_m_data, bROM_n_data, bROM_o_data, bROM_p_data, or_1_out, or_2_out, or_3_out, or_4_out, or_5_out,
       or_6_out, or_7_out, or_8_out, or_9_out, or_10_out, or_11_out, or_12_out, or_13_out, or_14_out,
       or_15_out, or_16_out, or_17_out, or_18_out, or_19_out, or_20_out, or_21_out, or_22_out, or_23_out,
       or_24_out, or_25_out, or_26_out, or_27_out, or_28_out, or_29_out, or_30_out, or_31_out, or_32_out,
       or_33_out, or_34_out, or_35_out, or_36_out, or_37_out, or_38_out, or_39_out, or_40_out, or_41_out,
       or_42_out, ROM_a_data, ROM_b_data, ROM_c_data, ROM_d_data, ROM_e_data, ROM_f_data, ROM_g_data,
       ROM_h_data, ROM_i_data, ROM_j_data, ROM_k_data, ROM_l_data, ROM_m_data, ROM_n_data, ROM_o_data,
       ROM_p_data;

  ROM #(.addrWidth(5), .dataWidth(32)) ROM_a (.addr(and_1_out), .data(ROM_a_data));
  assign and_1_out = Address & {5{Sel_a}};  // AND_Gate and_1, 5 bits wide
  ROM #(.addrWidth(5), .dataWidth(32)) aROM_a (.addr(and_2_out), .data(aROM_a_data));
  assign and_2_out = Address & {5{Sel_a}};  // AND_Gate and_2, 5 bits wide
  ROM #(.addrWidth(5), .dataWidth(32)) bROM_a (.addr(and_3_out), .data(bROM_a_data));
  assign and_3_out = Address & {5{Sel_a}};  // AND_Gate and_3, 5 bits wide
  ROM #(.addrWidth(5), .dataWidth(32)) ROM_b (.addr(and_4_out), .data(ROM_b_data));
  assign and_4_out = Address & {5{Sel_b}};  // AND_Gate and_4, 5 bits wide
  ROM #(.addrWidth(5), .dataWidth(32)) aROM_b (.addr(and_5_out), .data(aROM_b_data));
  assign and_5_out = Address & {5{Sel_b}};  // AND_Gate and_5, 5 bits wide
  ROM #(.addrWidth(5), .dataWidth(32)) bROM_b (.addr(and_6_out), .data(bROM_b_data));
  assign and_6_out = Address & {5{Sel_b}};  // AND_Gate and_6, 5 bits wide
  ROM #(.addrWidth(5), .dataWidth(32)) ROM_c (.addr(and_7_out), .data(ROM_c_data));
  assign and_7_out = Address & {5{Sel_c}};  // AND_Gate and_7, 5 bits wide
  assign or_1_out = ROM_b_data | ROM_a_data;  // OR_Gate or_1, 32 bits wide
  ROM #(.addrWidth(5), .dataWidth(32)) aROM_c (.addr(and_8_out), .data(aROM_c_data));
  assign and_8_out = Address & {5{Sel_c}};  // AND_Gate and_8, 5 bits wide
  assign or_2_out = aROM_b_data | aROM_a_data;  // OR_Gate or_2, 32 bits wide
  ROM #(.addrWidth(5), .dataWidth(32)) bROM_c (.addr(and_9_out), .data(bROM_c_data));
  assign and_9_out = Address & {5{Sel_c}};  // AND_Gate and_9, 5 bits wide
  assign or_3_out = bROM_b_data | bROM_a_data;  // OR_Gate or_3, 32 bits wide
  ROM #(.addrWidth(5), .dataWidth(32)) ROM_d (.addr(and_10_out), .data(ROM_d_data));
  assign and_10_out = Address & {5{Sel_d}};  // AND_Gate and_10, 5 bits wide
  ROM #(.addrWidth(5), .dataWidth(32)) aROM_d (.addr(and_11_out), .data(aROM_d_data));
  assign and_11_out = Address & {5{Sel_d}};  // AND_Gate and_11, 5 bits wide
  ROM #(.addrWidth(5), .dataWidth(32)) bROM_d (.addr(and_12_out), .data(bROM_d_data));
  assign and_12_out = Address & {5{Sel_d}};  // AND_Gate and_12, 5 bits wide
  assign or_4_out = ROM_c_data | or_1_out;  // OR_Gate or_4, 32 bits wide
  assign or_5_out = aROM_c_data | or_2_out;  // OR_Gate or_5, 32 bits wide
  assign or_6_out = bROM_c_data | or_3_out;  // OR_Gate or_6, 32 bits wide
  ROM #(.addrWidth(5), .dataWidth(32)) ROM_e (.addr(and_13_out), .data(ROM_e_data));
  assign and_13_out = Address & {5{Sel_e}};  // AND_Gate and_13, 5 bits wide
  assign or_7_out = ROM_d_data | or_4_out;  // OR_Gate or_7, 32 bits wide
  ROM #(.addrWidth(5), .dataWidth(32)) aROM_e (.addr(and_14_out), .data(aROM_e_data));
  assign and_14_out = Address & {5{Sel_e}};  // AND_Gate and_14, 5 bits wide
  assign or_8_out = aROM_d_data | or_5_out;  // OR_Gate or_8, 32 bits wide
  ROM #(.addrWidth(5), .dataWidth(32)) bROM_e (.addr(and_15_out), .data(bROM_e_data));
  assign and_15_out = Address & {5{Sel_e}};  // AND_Gate and_15, 5 bits wide
  assign or_9_out = bROM_d_data | or_6_out;  // OR_Gate or_9, 32 bits wide
  ROM #(.addrWidth(5), .dataWidth(32)) ROM_f (.addr(and_16_out), .data(ROM_f_data));
  assign and_16_out = Address & {5{Sel_f}};  // AND_Gate and_16, 5 bits wide
  assign or_10_out = ROM_e_data | or_7_out;  // OR_Gate or_10, 32 bits wide
  ROM #(.addrWidth(5), .dataWidth(32)) aROM_f (.addr(and_17_out), .data(aROM_f_data));
  assign and_17_out = Address & {5{Sel_f}};  // AND_Gate and_17, 5 bits wide
  assign or_11_out = aROM_e_data | or_8_out;  // OR_Gate or_11, 32 bits wide
  ROM #(.addrWidth(5), .dataWidth(32)) bROM_f (.addr(and_18_out), .data(bROM_f_data));
  assign and_18_out = Address & {5{Sel_f}};  // AND_Gate and_18, 5 bits wide
  assign or_12_out = bROM_e_data | or_9_out;  // OR_Gate or_12, 32 bits wide
  ROM #(.addrWidth(5), .dataWidth(32)) ROM_g (.addr(and_19_out), .data(ROM_g_data));
  assign and_19_out = Address & {5{Sel_g}};  // AND_Gate and_19, 5 bits wide
  assign or_13_out = ROM_f_data | or_10_out;  // OR_Gate or_13, 32 bits wide
  ROM #(.addrWidth(5), .dataWidth(32)) aROM_g (.addr(and_20_out), .data(aROM_g_data));
  assign and_20_out = Address & {5{Sel_g}};  // AND_Gate and_20, 5 bits wide
  assign or_14_out = aROM_f_data | or_11_out;  // OR_Gate or_14, 32 bits wide
  ROM #(.addrWidth(5), .dataWidth(32)) bROM_g (.addr(and_21_out), .data(bROM_g_data));
  assign and_21_out = Address & {5{Sel_g}};  // AND_Gate and_21, 5 bits wide
  assign or_15_out = bROM_f_data | or_12_out;  // OR_Gate or_15, 32 bits wide
  ROM #(.addrWidth(5), .dataWidth(32)) ROM_h (.addr(and_22_out), .data(ROM_h_data));
  assign and_22_out = Address & {5{Sel_h}};  // AND_Gate and_22, 5 bits wide
  ROM #(.addrWidth(5), .dataWidth(32)) aROM_h (.addr(and_23_out), .data(aROM_h_data));
  assign and_23_out = Address & {5{Sel_h}};  // AND_Gate and_23, 5 bits wide
  ROM #(.addrWidth(5), .dataWidth(32)) bROM_h (.addr(and_24_out), .data(bROM_h_data));
  assign and_24_out = Address & {5{Sel_h}};  // AND_Gate and_24, 5 bits wide
  assign or_16_out = ROM_g_data | or_13_out;  // OR_Gate or_16, 32 bits wide
  assign or_17_out = aROM_g_data | or_14_out;  // OR_Gate or_17, 32 bits wide
  assign or_18_out = bROM_g_data | or_15_out;  // OR_Gate or_18, 32 bits wide
  ROM #(.addrWidth(5), .dataWidth(32)) ROM_i (.addr(and_25_out), .data(ROM_i_data));
  assign and_25_out = Address & {5{Sel_i}};  // AND_Gate and_25, 5 bits wide
  assign or_19_out = ROM_h_data | or_16_out;  // OR_Gate or_19, 32 bits wide
  ROM #(.addrWidth(5), .dataWidth(32)) aROM_i (.addr(and_26_out), .data(aROM_i_data));
  assign and_26_out = Address & {5{Sel_i}};  // AND_Gate and_26, 5 bits wide
  assign or_20_out = aROM_h_data | or_17_out;  // OR_Gate or_20, 32 bits wide
  ROM #(.addrWidth(5), .dataWidth(32)) bROM_i (.addr(and_27_out), .data(bROM_i_data));
  assign and_27_out = Address & {5{Sel_i}};  // AND_Gate and_27, 5 bits wide
  assign or_21_out = bROM_h_data | or_18_out;  // OR_Gate or_21, 32 bits wide
  ROM #(.addrWidth(5), .dataWidth(32)) ROM_j (.addr(and_28_out), .data(ROM_j_data));
  assign and_28_out = Address & {5{Sel_j}};  // AND_Gate and_28, 5 bits wide
  assign or_22_out = ROM_i_data | or_19_out;  // OR_Gate or_22, 32 bits wide
  ROM #(.addrWidth(5), .dataWidth(32)) aROM_j (.addr(and_29_out), .data(aROM_j_data));
  assign and_29_out = Address & {5{Sel_j}};  // AND_Gate and_29, 5 bits wide
  assign or_23_out = aROM_i_data | or_20_out;  // OR_Gate or_23, 32 bits wide
  ROM #(.addrWidth(5), .dataWidth(32)) bROM_j (.addr(and_30_out), .data(bROM_j_data));
  assign and_30_out = Address & {5{Sel_j}};  // AND_Gate and_30, 5 bits wide
  assign or_24_out = bROM_i_data | or_21_out;  // OR_Gate or_24, 32 bits wide
  ROM #(.addrWidth(5), .dataWidth(32)) ROM_k (.addr(and_31_out), .data(ROM_k_data));
  assign and_31_out = Address & {5{Sel_k}};  // AND_Gate and_31, 5 bits wide
  assign or_25_out = ROM_j_data | or_22_out;  // OR_Gate or_25, 32 bits wide
  ROM #(.addrWidth(5), .dataWidth(32)) aROM_k (.addr(and_32_out), .data(aROM_k_data));
  assign and_32_out = Address & {5{Sel_k}};  // AND_Gate and_32, 5 bits wide
  assign or_26_out = aROM_j_data | or_23_out;  // OR_Gate or_26, 32 bits wide
  ROM #(.addrWidth(5), .dataWidth(32)) bROM_k (.addr(and_33_out), .data(bROM_k_data));
  assign and_33_out = Address & {5{Sel_k}};  // AND_Gate and_33, 5 bits wide
  assign or_27_out = bROM_j_data | or_24_out;  // OR_Gate or_27, 32 bits wide
  ROM #(.addrWidth(5), .dataWidth(32)) ROM_l (.addr(and_34_out), .data(ROM_l_data));
  assign and_34_out = Address & {5{Sel_l}};  // AND_Gate and_34, 5 bits wide
  ROM #(.addrWidth(5), .dataWidth(32)) aROM_l (.addr(and_35_out), .data(aROM_l_data));
  assign and_35_out = Address & {5{Sel_l}};  // AND_Gate and_35, 5 bits wide
  ROM #(.addrWidth(5), .dataWidth(32)) bROM_l (.addr(and_36_out), .data(bROM_l_data));
  assign and_36_out = Address & {5{Sel_l}};  // AND_Gate and_36, 5 bits wide
  assign or_28_out = ROM_k_data | or_25_out;  // OR_Gate or_28, 32 bits wide
  assign or_29_out = aROM_k_data | or_26_out;  // OR_Gate or_29, 32 bits wide
  assign or_30_out = bROM_k_data | or_27_out;  // OR_Gate or_30, 32 bits wide
  ROM #(.addrWidth(5), .dataWidth(32)) ROM_m (.addr(and_37_out), .data(ROM_m_data));
  assign and_37_out = Address & {5{Sel_m}};  // AND_Gate and_37, 5 bits wide
  assign or_31_out = ROM_l_data | or_28_out;  // OR_Gate or_31, 32 bits wide
  ROM #(.addrWidth(5), .dataWidth(32)) aROM_m (.addr(and_38_out), .data(aROM_m_data));
  assign and_38_out = Address & {5{Sel_m}};  // AND_Gate and_38, 5 bits wide
  assign or_32_out = aROM_l_data | or_29_out;  // OR_Gate or_32, 32 bits wide
  ROM #(.addrWidth(5), .dataWidth(32)) bROM_m (.addr(and_39_out), .data(bROM_m_data));
  assign and_39_out = Address & {5{Sel_m}};  // AND_Gate and_39, 5 bits wide
  assign or_33_out = bROM_l_data | or_30_out;  // OR_Gate or_33, 32 bits wide
  ROM #(.addrWidth(5), .dataWidth(32)) ROM_n (.addr(and_40_out), .data(ROM_n_data));
  assign and_40_out = Address & {5{Sel_n}};  // AND_Gate and_40, 5 bits wide
  assign or_34_out = ROM_m_data | or_31_out;  // OR_Gate or_34, 32 bits wide
  ROM #(.addrWidth(5), .dataWidth(32)) aROM_n (.addr(and_41_out), .data(aROM_n_data));
  assign and_41_out = Address & {5{Sel_n}};  // AND_Gate and_41, 5 bits wide
  assign or_35_out = aROM_m_data | or_32_out;  // OR_Gate or_35, 32 bits wide
  ROM #(.addrWidth(5), .dataWidth(32)) bROM_n (.addr(and_42_out), .data(bROM_n_data));
  assign and_42_out = Address & {5{Sel_n}};  // AND_Gate and_42, 5 bits wide
  assign or_36_out = bROM_m_data | or_33_out;  // OR_Gate or_36, 32 bits wide
  ROM #(.addrWidth(5), .dataWidth(32)) ROM_o (.addr(and_43_out), .data(ROM_o_data));
  assign and_43_out = Address & {5{Sel_o}};  // AND_Gate and_43, 5 bits wide
  assign or_37_out = ROM_n_data | or_34_out;  // OR_Gate or_37, 32 bits wide
  ROM #(.addrWidth(5), .dataWidth(32)) aROM_o (.addr(and_44_out), .data(aROM_o_data));
  assign and_44_out = Address & {5{Sel_o}};  // AND_Gate and_44, 5 bits wide
  assign or_38_out = aROM_n_data | or_35_out;  // OR_Gate or_38, 32 bits wide
  ROM #(.addrWidth(5), .dataWidth(32)) bROM_o (.addr(and_45_out), .data(bROM_o_data));
  assign and_45_out = Address & {5{Sel_o}};  // AND_Gate and_45, 5 bits wide
  assign or_39_out = bROM_n_data | or_36_out;  // OR_Gate or_39, 32 bits wide
  ROM #(.addrWidth(5), .dataWidth(32)) ROM_p (.addr(and_46_out), .data(ROM_p_data));
  assign and_46_out = Address & {5{Sel_p}};  // AND_Gate and_46, 5 bits wide
  ROM #(.addrWidth(5), .dataWidth(32)) aROM_p (.addr(and_47_out), .data(aROM_p_data));
  assign and_47_out = Address & {5{Sel_p}};  // AND_Gate and_47, 5 bits wide
  ROM #(.addrWidth(5), .dataWidth(32)) bROM_p (.addr(and_48_out), .data(bROM_p_data));
  assign and_48_out = Address & {5{Sel_p}};  // AND_Gate and_48, 5 bits wide
  assign or_40_out = ROM_o_data | or_37_out;  // OR_Gate or_40, 32 bits wide
  assign or_41_out = aROM_o_data | or_38_out;  // OR_Gate or_41, 32 bits wide
  assign or_42_out = bROM_o_data | or_39_out;  // OR_Gate or_42, 32 bits wide
  assign Lines = ROM_p_data | or_40_out;  // OR_Gate or_43, 32 bits wide
  assign Linesa = aROM_p_data | or_41_out;  // OR_Gate or_44, 32 bits wide
  assign Linesb = bROM_p_data | or_42_out;  // OR_Gate or_45, 32 bits wide

  // Notes on the sheet:
  //   contents of aROM_a (hex, n*v repeats v):
  //   0 10000000
  //   contents of bROM_a (hex, n*v repeats v):
  //   0 10000000
  //   contents of bROM_g (hex, n*v repeats v):
  //   0 1
  //   contents of ROM_i (hex, n*v repeats v):
  //   0 9000000 80000001
  //   contents of ROM_j (hex, n*v repeats v):
  //   0 9010000 80000001
endmodule

module Instructions8x (
  input  Sel_a,
  input  Sel_b,
  input  Sel_c,
  input  Sel_d,
  input  Sel_e,
  input  Sel_f,
  input  Sel_g,
  input  Sel_h,
  input  Sel_i,
  input  Sel_j,
  input  Sel_k,
  input  Sel_l,
  input  Sel_m,
  input  Sel_n,
  input  Sel_o,
  input  Sel_p,
  input  [4:0] Address,
  output [31:0] Lines,
  output [31:0] Linesa,
  output [31:0] Linesb
);

  wire [4:0] and_1_out, and_2_out, and_3_out, and_4_out, and_5_out, and_6_out, and_7_out, and_8_out,
       and_9_out, and_10_out, and_11_out, and_12_out, and_13_out, and_14_out, and_15_out, and_16_out,
       and_17_out, and_18_out, and_19_out, and_20_out, and_21_out, and_22_out, and_23_out, and_24_out,
       and_25_out, and_26_out, and_27_out, and_28_out, and_29_out, and_30_out, and_31_out, and_32_out,
       and_33_out, and_34_out, and_35_out, and_36_out, and_37_out, and_38_out, and_39_out, and_40_out,
       and_41_out, and_42_out, and_43_out, and_44_out, and_45_out, and_46_out, and_47_out, and_48_out;
  wire [31:0] aROM_a_data, aROM_b_data, aROM_c_data, aROM_d_data, aROM_e_data, aROM_f_data, aROM_g_data,
       aROM_h_data, aROM_i_data, aROM_j_data, aROM_k_data, aROM_l_data, aROM_m_data, aROM_n_data,
       aROM_o_data, aROM_p_data, bROM_a_data, bROM_b_data, bROM_c_data, bROM_d_data, bROM_e_data,
       bROM_f_data, bROM_g_data, bROM_h_data, bROM_i_data, bROM_j_data, bROM_k_data, bROM_l_data,
       bROM_m_data, bROM_n_data, bROM_o_data, bROM_p_data, or_1_out, or_2_out, or_3_out, or_4_out, or_5_out,
       or_6_out, or_7_out, or_8_out, or_9_out, or_10_out, or_11_out, or_12_out, or_13_out, or_14_out,
       or_15_out, or_16_out, or_17_out, or_18_out, or_19_out, or_20_out, or_21_out, or_22_out, or_23_out,
       or_24_out, or_25_out, or_26_out, or_27_out, or_28_out, or_29_out, or_30_out, or_31_out, or_32_out,
       or_33_out, or_34_out, or_35_out, or_36_out, or_37_out, or_38_out, or_39_out, or_40_out, or_41_out,
       or_42_out, ROM_a_data, ROM_b_data, ROM_c_data, ROM_d_data, ROM_e_data, ROM_f_data, ROM_g_data,
       ROM_h_data, ROM_i_data, ROM_j_data, ROM_k_data, ROM_l_data, ROM_m_data, ROM_n_data, ROM_o_data,
       ROM_p_data;

  ROM #(.addrWidth(5), .dataWidth(32)) ROM_a (.addr(and_1_out), .data(ROM_a_data));
  assign and_1_out = Address & {5{Sel_a}};  // AND_Gate and_1, 5 bits wide
  ROM #(.addrWidth(5), .dataWidth(32)) aROM_a (.addr(and_2_out), .data(aROM_a_data));
  assign and_2_out = Address & {5{Sel_a}};  // AND_Gate and_2, 5 bits wide
  ROM #(.addrWidth(5), .dataWidth(32)) bROM_a (.addr(and_3_out), .data(bROM_a_data));
  assign and_3_out = Address & {5{Sel_a}};  // AND_Gate and_3, 5 bits wide
  ROM #(.addrWidth(5), .dataWidth(32)) ROM_b (.addr(and_4_out), .data(ROM_b_data));
  assign and_4_out = Address & {5{Sel_b}};  // AND_Gate and_4, 5 bits wide
  ROM #(.addrWidth(5), .dataWidth(32)) aROM_b (.addr(and_5_out), .data(aROM_b_data));
  assign and_5_out = Address & {5{Sel_b}};  // AND_Gate and_5, 5 bits wide
  ROM #(.addrWidth(5), .dataWidth(32)) bROM_b (.addr(and_6_out), .data(bROM_b_data));
  assign and_6_out = Address & {5{Sel_b}};  // AND_Gate and_6, 5 bits wide
  ROM #(.addrWidth(5), .dataWidth(32)) ROM_c (.addr(and_7_out), .data(ROM_c_data));
  assign and_7_out = Address & {5{Sel_c}};  // AND_Gate and_7, 5 bits wide
  assign or_1_out = ROM_b_data | ROM_a_data;  // OR_Gate or_1, 32 bits wide
  ROM #(.addrWidth(5), .dataWidth(32)) aROM_c (.addr(and_8_out), .data(aROM_c_data));
  assign and_8_out = Address & {5{Sel_c}};  // AND_Gate and_8, 5 bits wide
  assign or_2_out = aROM_b_data | aROM_a_data;  // OR_Gate or_2, 32 bits wide
  ROM #(.addrWidth(5), .dataWidth(32)) bROM_c (.addr(and_9_out), .data(bROM_c_data));
  assign and_9_out = Address & {5{Sel_c}};  // AND_Gate and_9, 5 bits wide
  assign or_3_out = bROM_b_data | bROM_a_data;  // OR_Gate or_3, 32 bits wide
  ROM #(.addrWidth(5), .dataWidth(32)) ROM_d (.addr(and_10_out), .data(ROM_d_data));
  assign and_10_out = Address & {5{Sel_d}};  // AND_Gate and_10, 5 bits wide
  ROM #(.addrWidth(5), .dataWidth(32)) aROM_d (.addr(and_11_out), .data(aROM_d_data));
  assign and_11_out = Address & {5{Sel_d}};  // AND_Gate and_11, 5 bits wide
  ROM #(.addrWidth(5), .dataWidth(32)) bROM_d (.addr(and_12_out), .data(bROM_d_data));
  assign and_12_out = Address & {5{Sel_d}};  // AND_Gate and_12, 5 bits wide
  assign or_4_out = ROM_c_data | or_1_out;  // OR_Gate or_4, 32 bits wide
  assign or_5_out = aROM_c_data | or_2_out;  // OR_Gate or_5, 32 bits wide
  assign or_6_out = bROM_c_data | or_3_out;  // OR_Gate or_6, 32 bits wide
  ROM #(.addrWidth(5), .dataWidth(32)) ROM_e (.addr(and_13_out), .data(ROM_e_data));
  assign and_13_out = Address & {5{Sel_e}};  // AND_Gate and_13, 5 bits wide
  assign or_7_out = ROM_d_data | or_4_out;  // OR_Gate or_7, 32 bits wide
  ROM #(.addrWidth(5), .dataWidth(32)) aROM_e (.addr(and_14_out), .data(aROM_e_data));
  assign and_14_out = Address & {5{Sel_e}};  // AND_Gate and_14, 5 bits wide
  assign or_8_out = aROM_d_data | or_5_out;  // OR_Gate or_8, 32 bits wide
  ROM #(.addrWidth(5), .dataWidth(32)) bROM_e (.addr(and_15_out), .data(bROM_e_data));
  assign and_15_out = Address & {5{Sel_e}};  // AND_Gate and_15, 5 bits wide
  assign or_9_out = bROM_d_data | or_6_out;  // OR_Gate or_9, 32 bits wide
  ROM #(.addrWidth(5), .dataWidth(32)) ROM_f (.addr(and_16_out), .data(ROM_f_data));
  assign and_16_out = Address & {5{Sel_f}};  // AND_Gate and_16, 5 bits wide
  assign or_10_out = ROM_e_data | or_7_out;  // OR_Gate or_10, 32 bits wide
  ROM #(.addrWidth(5), .dataWidth(32)) aROM_f (.addr(and_17_out), .data(aROM_f_data));
  assign and_17_out = Address & {5{Sel_f}};  // AND_Gate and_17, 5 bits wide
  assign or_11_out = aROM_e_data | or_8_out;  // OR_Gate or_11, 32 bits wide
  ROM #(.addrWidth(5), .dataWidth(32)) bROM_f (.addr(and_18_out), .data(bROM_f_data));
  assign and_18_out = Address & {5{Sel_f}};  // AND_Gate and_18, 5 bits wide
  assign or_12_out = bROM_e_data | or_9_out;  // OR_Gate or_12, 32 bits wide
  ROM #(.addrWidth(5), .dataWidth(32)) ROM_g (.addr(and_19_out), .data(ROM_g_data));
  assign and_19_out = Address & {5{Sel_g}};  // AND_Gate and_19, 5 bits wide
  assign or_13_out = ROM_f_data | or_10_out;  // OR_Gate or_13, 32 bits wide
  ROM #(.addrWidth(5), .dataWidth(32)) aROM_g (.addr(and_20_out), .data(aROM_g_data));
  assign and_20_out = Address & {5{Sel_g}};  // AND_Gate and_20, 5 bits wide
  assign or_14_out = aROM_f_data | or_11_out;  // OR_Gate or_14, 32 bits wide
  ROM #(.addrWidth(5), .dataWidth(32)) bROM_g (.addr(and_21_out), .data(bROM_g_data));
  assign and_21_out = Address & {5{Sel_g}};  // AND_Gate and_21, 5 bits wide
  assign or_15_out = bROM_f_data | or_12_out;  // OR_Gate or_15, 32 bits wide
  ROM #(.addrWidth(5), .dataWidth(32)) ROM_h (.addr(and_22_out), .data(ROM_h_data));
  assign and_22_out = Address & {5{Sel_h}};  // AND_Gate and_22, 5 bits wide
  ROM #(.addrWidth(5), .dataWidth(32)) aROM_h (.addr(and_23_out), .data(aROM_h_data));
  assign and_23_out = Address & {5{Sel_h}};  // AND_Gate and_23, 5 bits wide
  ROM #(.addrWidth(5), .dataWidth(32)) bROM_h (.addr(and_24_out), .data(bROM_h_data));
  assign and_24_out = Address & {5{Sel_h}};  // AND_Gate and_24, 5 bits wide
  assign or_16_out = ROM_g_data | or_13_out;  // OR_Gate or_16, 32 bits wide
  assign or_17_out = aROM_g_data | or_14_out;  // OR_Gate or_17, 32 bits wide
  assign or_18_out = bROM_g_data | or_15_out;  // OR_Gate or_18, 32 bits wide
  ROM #(.addrWidth(5), .dataWidth(32)) ROM_i (.addr(and_25_out), .data(ROM_i_data));
  assign and_25_out = Address & {5{Sel_i}};  // AND_Gate and_25, 5 bits wide
  assign or_19_out = ROM_h_data | or_16_out;  // OR_Gate or_19, 32 bits wide
  ROM #(.addrWidth(5), .dataWidth(32)) aROM_i (.addr(and_26_out), .data(aROM_i_data));
  assign and_26_out = Address & {5{Sel_i}};  // AND_Gate and_26, 5 bits wide
  assign or_20_out = aROM_h_data | or_17_out;  // OR_Gate or_20, 32 bits wide
  ROM #(.addrWidth(5), .dataWidth(32)) bROM_i (.addr(and_27_out), .data(bROM_i_data));
  assign and_27_out = Address & {5{Sel_i}};  // AND_Gate and_27, 5 bits wide
  assign or_21_out = bROM_h_data | or_18_out;  // OR_Gate or_21, 32 bits wide
  ROM #(.addrWidth(5), .dataWidth(32)) ROM_j (.addr(and_28_out), .data(ROM_j_data));
  assign and_28_out = Address & {5{Sel_j}};  // AND_Gate and_28, 5 bits wide
  assign or_22_out = ROM_i_data | or_19_out;  // OR_Gate or_22, 32 bits wide
  ROM #(.addrWidth(5), .dataWidth(32)) aROM_j (.addr(and_29_out), .data(aROM_j_data));
  assign and_29_out = Address & {5{Sel_j}};  // AND_Gate and_29, 5 bits wide
  assign or_23_out = aROM_i_data | or_20_out;  // OR_Gate or_23, 32 bits wide
  ROM #(.addrWidth(5), .dataWidth(32)) bROM_j (.addr(and_30_out), .data(bROM_j_data));
  assign and_30_out = Address & {5{Sel_j}};  // AND_Gate and_30, 5 bits wide
  assign or_24_out = bROM_i_data | or_21_out;  // OR_Gate or_24, 32 bits wide
  ROM #(.addrWidth(5), .dataWidth(32)) ROM_k (.addr(and_31_out), .data(ROM_k_data));
  assign and_31_out = Address & {5{Sel_k}};  // AND_Gate and_31, 5 bits wide
  assign or_25_out = ROM_j_data | or_22_out;  // OR_Gate or_25, 32 bits wide
  ROM #(.addrWidth(5), .dataWidth(32)) aROM_k (.addr(and_32_out), .data(aROM_k_data));
  assign and_32_out = Address & {5{Sel_k}};  // AND_Gate and_32, 5 bits wide
  assign or_26_out = aROM_j_data | or_23_out;  // OR_Gate or_26, 32 bits wide
  ROM #(.addrWidth(5), .dataWidth(32)) bROM_k (.addr(and_33_out), .data(bROM_k_data));
  assign and_33_out = Address & {5{Sel_k}};  // AND_Gate and_33, 5 bits wide
  assign or_27_out = bROM_j_data | or_24_out;  // OR_Gate or_27, 32 bits wide
  ROM #(.addrWidth(5), .dataWidth(32)) ROM_l (.addr(and_34_out), .data(ROM_l_data));
  assign and_34_out = Address & {5{Sel_l}};  // AND_Gate and_34, 5 bits wide
  ROM #(.addrWidth(5), .dataWidth(32)) aROM_l (.addr(and_35_out), .data(aROM_l_data));
  assign and_35_out = Address & {5{Sel_l}};  // AND_Gate and_35, 5 bits wide
  ROM #(.addrWidth(5), .dataWidth(32)) bROM_l (.addr(and_36_out), .data(bROM_l_data));
  assign and_36_out = Address & {5{Sel_l}};  // AND_Gate and_36, 5 bits wide
  assign or_28_out = ROM_k_data | or_25_out;  // OR_Gate or_28, 32 bits wide
  assign or_29_out = aROM_k_data | or_26_out;  // OR_Gate or_29, 32 bits wide
  assign or_30_out = bROM_k_data | or_27_out;  // OR_Gate or_30, 32 bits wide
  ROM #(.addrWidth(5), .dataWidth(32)) ROM_m (.addr(and_37_out), .data(ROM_m_data));
  assign and_37_out = Address & {5{Sel_m}};  // AND_Gate and_37, 5 bits wide
  assign or_31_out = ROM_l_data | or_28_out;  // OR_Gate or_31, 32 bits wide
  ROM #(.addrWidth(5), .dataWidth(32)) aROM_m (.addr(and_38_out), .data(aROM_m_data));
  assign and_38_out = Address & {5{Sel_m}};  // AND_Gate and_38, 5 bits wide
  assign or_32_out = aROM_l_data | or_29_out;  // OR_Gate or_32, 32 bits wide
  ROM #(.addrWidth(5), .dataWidth(32)) bROM_m (.addr(and_39_out), .data(bROM_m_data));
  assign and_39_out = Address & {5{Sel_m}};  // AND_Gate and_39, 5 bits wide
  assign or_33_out = bROM_l_data | or_30_out;  // OR_Gate or_33, 32 bits wide
  ROM #(.addrWidth(5), .dataWidth(32)) ROM_n (.addr(and_40_out), .data(ROM_n_data));
  assign and_40_out = Address & {5{Sel_n}};  // AND_Gate and_40, 5 bits wide
  assign or_34_out = ROM_m_data | or_31_out;  // OR_Gate or_34, 32 bits wide
  ROM #(.addrWidth(5), .dataWidth(32)) aROM_n (.addr(and_41_out), .data(aROM_n_data));
  assign and_41_out = Address & {5{Sel_n}};  // AND_Gate and_41, 5 bits wide
  assign or_35_out = aROM_m_data | or_32_out;  // OR_Gate or_35, 32 bits wide
  ROM #(.addrWidth(5), .dataWidth(32)) bROM_n (.addr(and_42_out), .data(bROM_n_data));
  assign and_42_out = Address & {5{Sel_n}};  // AND_Gate and_42, 5 bits wide
  assign or_36_out = bROM_m_data | or_33_out;  // OR_Gate or_36, 32 bits wide
  ROM #(.addrWidth(5), .dataWidth(32)) ROM_o (.addr(and_43_out), .data(ROM_o_data));
  assign and_43_out = Address & {5{Sel_o}};  // AND_Gate and_43, 5 bits wide
  assign or_37_out = ROM_n_data | or_34_out;  // OR_Gate or_37, 32 bits wide
  ROM #(.addrWidth(5), .dataWidth(32)) aROM_o (.addr(and_44_out), .data(aROM_o_data));
  assign and_44_out = Address & {5{Sel_o}};  // AND_Gate and_44, 5 bits wide
  assign or_38_out = aROM_n_data | or_35_out;  // OR_Gate or_38, 32 bits wide
  ROM #(.addrWidth(5), .dataWidth(32)) bROM_o (.addr(and_45_out), .data(bROM_o_data));
  assign and_45_out = Address & {5{Sel_o}};  // AND_Gate and_45, 5 bits wide
  assign or_39_out = bROM_n_data | or_36_out;  // OR_Gate or_39, 32 bits wide
  ROM #(.addrWidth(5), .dataWidth(32)) ROM_p (.addr(and_46_out), .data(ROM_p_data));
  assign and_46_out = Address & {5{Sel_p}};  // AND_Gate and_46, 5 bits wide
  ROM #(.addrWidth(5), .dataWidth(32)) aROM_p (.addr(and_47_out), .data(aROM_p_data));
  assign and_47_out = Address & {5{Sel_p}};  // AND_Gate and_47, 5 bits wide
  ROM #(.addrWidth(5), .dataWidth(32)) bROM_p (.addr(and_48_out), .data(bROM_p_data));
  assign and_48_out = Address & {5{Sel_p}};  // AND_Gate and_48, 5 bits wide
  assign or_40_out = ROM_o_data | or_37_out;  // OR_Gate or_40, 32 bits wide
  assign or_41_out = aROM_o_data | or_38_out;  // OR_Gate or_41, 32 bits wide
  assign or_42_out = bROM_o_data | or_39_out;  // OR_Gate or_42, 32 bits wide
  assign Lines = ROM_p_data | or_40_out;  // OR_Gate or_43, 32 bits wide
  assign Linesa = aROM_p_data | or_41_out;  // OR_Gate or_44, 32 bits wide
  assign Linesb = bROM_p_data | or_42_out;  // OR_Gate or_45, 32 bits wide

  // Notes on the sheet:
  //   contents of ROM_a (hex, n*v repeats v):
  //   0 9000000 0 8000002 80000001
  //   contents of aROM_a (hex, n*v repeats v):
  //   0 0 2 40800100
endmodule

module Instructions9x (
  input  Sel_a,
  input  Sel_b,
  input  Sel_c,
  input  Sel_d,
  input  Sel_e,
  input  Sel_f,
  input  Sel_g,
  input  Sel_h,
  input  Sel_i,
  input  Sel_j,
  input  Sel_k,
  input  Sel_l,
  input  Sel_m,
  input  Sel_n,
  input  Sel_o,
  input  Sel_p,
  input  [4:0] Address,
  output [31:0] Lines,
  output [31:0] Linesa,
  output [31:0] Linesb
);

  wire [4:0] and_1_out, and_2_out, and_3_out, and_4_out, and_5_out, and_6_out, and_7_out, and_8_out,
       and_9_out, and_10_out, and_11_out, and_12_out, and_13_out, and_14_out, and_15_out, and_16_out,
       and_17_out, and_18_out, and_19_out, and_20_out, and_21_out, and_22_out, and_23_out, and_24_out,
       and_25_out, and_26_out, and_27_out, and_28_out, and_29_out, and_30_out, and_31_out, and_32_out,
       and_33_out, and_34_out, and_35_out, and_36_out, and_37_out, and_38_out, and_39_out, and_40_out,
       and_41_out, and_42_out, and_43_out, and_44_out, and_45_out, and_46_out, and_47_out, and_48_out;
  wire [31:0] aROM_a_data, aROM_b_data, aROM_c_data, aROM_d_data, aROM_e_data, aROM_f_data, aROM_g_data,
       aROM_h_data, aROM_i_data, aROM_j_data, aROM_k_data, aROM_l_data, aROM_m_data, aROM_n_data,
       aROM_o_data, aROM_p_data, bROM_a_data, bROM_b_data, bROM_c_data, bROM_d_data, bROM_e_data,
       bROM_f_data, bROM_g_data, bROM_h_data, bROM_i_data, bROM_j_data, bROM_k_data, bROM_l_data,
       bROM_m_data, bROM_n_data, bROM_o_data, bROM_p_data, or_1_out, or_2_out, or_3_out, or_4_out, or_5_out,
       or_6_out, or_7_out, or_8_out, or_9_out, or_10_out, or_11_out, or_12_out, or_13_out, or_14_out,
       or_15_out, or_16_out, or_17_out, or_18_out, or_19_out, or_20_out, or_21_out, or_22_out, or_23_out,
       or_24_out, or_25_out, or_26_out, or_27_out, or_28_out, or_29_out, or_30_out, or_31_out, or_32_out,
       or_33_out, or_34_out, or_35_out, or_36_out, or_37_out, or_38_out, or_39_out, or_40_out, or_41_out,
       or_42_out, ROM_a_data, ROM_b_data, ROM_c_data, ROM_d_data, ROM_e_data, ROM_f_data, ROM_g_data,
       ROM_h_data, ROM_i_data, ROM_j_data, ROM_k_data, ROM_l_data, ROM_m_data, ROM_n_data, ROM_o_data,
       ROM_p_data;

  ROM #(.addrWidth(5), .dataWidth(32)) ROM_a (.addr(and_1_out), .data(ROM_a_data));
  assign and_1_out = Address & {5{Sel_a}};  // AND_Gate and_1, 5 bits wide
  ROM #(.addrWidth(5), .dataWidth(32)) aROM_a (.addr(and_2_out), .data(aROM_a_data));
  assign and_2_out = Address & {5{Sel_a}};  // AND_Gate and_2, 5 bits wide
  ROM #(.addrWidth(5), .dataWidth(32)) bROM_a (.addr(and_3_out), .data(bROM_a_data));
  assign and_3_out = Address & {5{Sel_a}};  // AND_Gate and_3, 5 bits wide
  ROM #(.addrWidth(5), .dataWidth(32)) ROM_b (.addr(and_4_out), .data(ROM_b_data));
  assign and_4_out = Address & {5{Sel_b}};  // AND_Gate and_4, 5 bits wide
  ROM #(.addrWidth(5), .dataWidth(32)) aROM_b (.addr(and_5_out), .data(aROM_b_data));
  assign and_5_out = Address & {5{Sel_b}};  // AND_Gate and_5, 5 bits wide
  ROM #(.addrWidth(5), .dataWidth(32)) bROM_b (.addr(and_6_out), .data(bROM_b_data));
  assign and_6_out = Address & {5{Sel_b}};  // AND_Gate and_6, 5 bits wide
  ROM #(.addrWidth(5), .dataWidth(32)) ROM_c (.addr(and_7_out), .data(ROM_c_data));
  assign and_7_out = Address & {5{Sel_c}};  // AND_Gate and_7, 5 bits wide
  assign or_1_out = ROM_b_data | ROM_a_data;  // OR_Gate or_1, 32 bits wide
  ROM #(.addrWidth(5), .dataWidth(32)) aROM_c (.addr(and_8_out), .data(aROM_c_data));
  assign and_8_out = Address & {5{Sel_c}};  // AND_Gate and_8, 5 bits wide
  assign or_2_out = aROM_b_data | aROM_a_data;  // OR_Gate or_2, 32 bits wide
  ROM #(.addrWidth(5), .dataWidth(32)) bROM_c (.addr(and_9_out), .data(bROM_c_data));
  assign and_9_out = Address & {5{Sel_c}};  // AND_Gate and_9, 5 bits wide
  assign or_3_out = bROM_b_data | bROM_a_data;  // OR_Gate or_3, 32 bits wide
  ROM #(.addrWidth(5), .dataWidth(32)) ROM_d (.addr(and_10_out), .data(ROM_d_data));
  assign and_10_out = Address & {5{Sel_d}};  // AND_Gate and_10, 5 bits wide
  ROM #(.addrWidth(5), .dataWidth(32)) aROM_d (.addr(and_11_out), .data(aROM_d_data));
  assign and_11_out = Address & {5{Sel_d}};  // AND_Gate and_11, 5 bits wide
  ROM #(.addrWidth(5), .dataWidth(32)) bROM_d (.addr(and_12_out), .data(bROM_d_data));
  assign and_12_out = Address & {5{Sel_d}};  // AND_Gate and_12, 5 bits wide
  assign or_4_out = ROM_c_data | or_1_out;  // OR_Gate or_4, 32 bits wide
  assign or_5_out = aROM_c_data | or_2_out;  // OR_Gate or_5, 32 bits wide
  assign or_6_out = bROM_c_data | or_3_out;  // OR_Gate or_6, 32 bits wide
  ROM #(.addrWidth(5), .dataWidth(32)) ROM_e (.addr(and_13_out), .data(ROM_e_data));
  assign and_13_out = Address & {5{Sel_e}};  // AND_Gate and_13, 5 bits wide
  assign or_7_out = ROM_d_data | or_4_out;  // OR_Gate or_7, 32 bits wide
  ROM #(.addrWidth(5), .dataWidth(32)) aROM_e (.addr(and_14_out), .data(aROM_e_data));
  assign and_14_out = Address & {5{Sel_e}};  // AND_Gate and_14, 5 bits wide
  assign or_8_out = aROM_d_data | or_5_out;  // OR_Gate or_8, 32 bits wide
  ROM #(.addrWidth(5), .dataWidth(32)) bROM_e (.addr(and_15_out), .data(bROM_e_data));
  assign and_15_out = Address & {5{Sel_e}};  // AND_Gate and_15, 5 bits wide
  assign or_9_out = bROM_d_data | or_6_out;  // OR_Gate or_9, 32 bits wide
  ROM #(.addrWidth(5), .dataWidth(32)) ROM_f (.addr(and_16_out), .data(ROM_f_data));
  assign and_16_out = Address & {5{Sel_f}};  // AND_Gate and_16, 5 bits wide
  assign or_10_out = ROM_e_data | or_7_out;  // OR_Gate or_10, 32 bits wide
  ROM #(.addrWidth(5), .dataWidth(32)) aROM_f (.addr(and_17_out), .data(aROM_f_data));
  assign and_17_out = Address & {5{Sel_f}};  // AND_Gate and_17, 5 bits wide
  assign or_11_out = aROM_e_data | or_8_out;  // OR_Gate or_11, 32 bits wide
  ROM #(.addrWidth(5), .dataWidth(32)) bROM_f (.addr(and_18_out), .data(bROM_f_data));
  assign and_18_out = Address & {5{Sel_f}};  // AND_Gate and_18, 5 bits wide
  assign or_12_out = bROM_e_data | or_9_out;  // OR_Gate or_12, 32 bits wide
  ROM #(.addrWidth(5), .dataWidth(32)) ROM_g (.addr(and_19_out), .data(ROM_g_data));
  assign and_19_out = Address & {5{Sel_g}};  // AND_Gate and_19, 5 bits wide
  assign or_13_out = ROM_f_data | or_10_out;  // OR_Gate or_13, 32 bits wide
  ROM #(.addrWidth(5), .dataWidth(32)) aROM_g (.addr(and_20_out), .data(aROM_g_data));
  assign and_20_out = Address & {5{Sel_g}};  // AND_Gate and_20, 5 bits wide
  assign or_14_out = aROM_f_data | or_11_out;  // OR_Gate or_14, 32 bits wide
  ROM #(.addrWidth(5), .dataWidth(32)) bROM_g (.addr(and_21_out), .data(bROM_g_data));
  assign and_21_out = Address & {5{Sel_g}};  // AND_Gate and_21, 5 bits wide
  assign or_15_out = bROM_f_data | or_12_out;  // OR_Gate or_15, 32 bits wide
  ROM #(.addrWidth(5), .dataWidth(32)) ROM_h (.addr(and_22_out), .data(ROM_h_data));
  assign and_22_out = Address & {5{Sel_h}};  // AND_Gate and_22, 5 bits wide
  ROM #(.addrWidth(5), .dataWidth(32)) aROM_h (.addr(and_23_out), .data(aROM_h_data));
  assign and_23_out = Address & {5{Sel_h}};  // AND_Gate and_23, 5 bits wide
  ROM #(.addrWidth(5), .dataWidth(32)) bROM_h (.addr(and_24_out), .data(bROM_h_data));
  assign and_24_out = Address & {5{Sel_h}};  // AND_Gate and_24, 5 bits wide
  assign or_16_out = ROM_g_data | or_13_out;  // OR_Gate or_16, 32 bits wide
  assign or_17_out = aROM_g_data | or_14_out;  // OR_Gate or_17, 32 bits wide
  assign or_18_out = bROM_g_data | or_15_out;  // OR_Gate or_18, 32 bits wide
  ROM #(.addrWidth(5), .dataWidth(32)) ROM_i (.addr(and_25_out), .data(ROM_i_data));
  assign and_25_out = Address & {5{Sel_i}};  // AND_Gate and_25, 5 bits wide
  assign or_19_out = ROM_h_data | or_16_out;  // OR_Gate or_19, 32 bits wide
  ROM #(.addrWidth(5), .dataWidth(32)) aROM_i (.addr(and_26_out), .data(aROM_i_data));
  assign and_26_out = Address & {5{Sel_i}};  // AND_Gate and_26, 5 bits wide
  assign or_20_out = aROM_h_data | or_17_out;  // OR_Gate or_20, 32 bits wide
  ROM #(.addrWidth(5), .dataWidth(32)) bROM_i (.addr(and_27_out), .data(bROM_i_data));
  assign and_27_out = Address & {5{Sel_i}};  // AND_Gate and_27, 5 bits wide
  assign or_21_out = bROM_h_data | or_18_out;  // OR_Gate or_21, 32 bits wide
  ROM #(.addrWidth(5), .dataWidth(32)) ROM_j (.addr(and_28_out), .data(ROM_j_data));
  assign and_28_out = Address & {5{Sel_j}};  // AND_Gate and_28, 5 bits wide
  assign or_22_out = ROM_i_data | or_19_out;  // OR_Gate or_22, 32 bits wide
  ROM #(.addrWidth(5), .dataWidth(32)) aROM_j (.addr(and_29_out), .data(aROM_j_data));
  assign and_29_out = Address & {5{Sel_j}};  // AND_Gate and_29, 5 bits wide
  assign or_23_out = aROM_i_data | or_20_out;  // OR_Gate or_23, 32 bits wide
  ROM #(.addrWidth(5), .dataWidth(32)) bROM_j (.addr(and_30_out), .data(bROM_j_data));
  assign and_30_out = Address & {5{Sel_j}};  // AND_Gate and_30, 5 bits wide
  assign or_24_out = bROM_i_data | or_21_out;  // OR_Gate or_24, 32 bits wide
  ROM #(.addrWidth(5), .dataWidth(32)) ROM_k (.addr(and_31_out), .data(ROM_k_data));
  assign and_31_out = Address & {5{Sel_k}};  // AND_Gate and_31, 5 bits wide
  assign or_25_out = ROM_j_data | or_22_out;  // OR_Gate or_25, 32 bits wide
  ROM #(.addrWidth(5), .dataWidth(32)) aROM_k (.addr(and_32_out), .data(aROM_k_data));
  assign and_32_out = Address & {5{Sel_k}};  // AND_Gate and_32, 5 bits wide
  assign or_26_out = aROM_j_data | or_23_out;  // OR_Gate or_26, 32 bits wide
  ROM #(.addrWidth(5), .dataWidth(32)) bROM_k (.addr(and_33_out), .data(bROM_k_data));
  assign and_33_out = Address & {5{Sel_k}};  // AND_Gate and_33, 5 bits wide
  assign or_27_out = bROM_j_data | or_24_out;  // OR_Gate or_27, 32 bits wide
  ROM #(.addrWidth(5), .dataWidth(32)) ROM_l (.addr(and_34_out), .data(ROM_l_data));
  assign and_34_out = Address & {5{Sel_l}};  // AND_Gate and_34, 5 bits wide
  ROM #(.addrWidth(5), .dataWidth(32)) aROM_l (.addr(and_35_out), .data(aROM_l_data));
  assign and_35_out = Address & {5{Sel_l}};  // AND_Gate and_35, 5 bits wide
  ROM #(.addrWidth(5), .dataWidth(32)) bROM_l (.addr(and_36_out), .data(bROM_l_data));
  assign and_36_out = Address & {5{Sel_l}};  // AND_Gate and_36, 5 bits wide
  assign or_28_out = ROM_k_data | or_25_out;  // OR_Gate or_28, 32 bits wide
  assign or_29_out = aROM_k_data | or_26_out;  // OR_Gate or_29, 32 bits wide
  assign or_30_out = bROM_k_data | or_27_out;  // OR_Gate or_30, 32 bits wide
  ROM #(.addrWidth(5), .dataWidth(32)) ROM_m (.addr(and_37_out), .data(ROM_m_data));
  assign and_37_out = Address & {5{Sel_m}};  // AND_Gate and_37, 5 bits wide
  assign or_31_out = ROM_l_data | or_28_out;  // OR_Gate or_31, 32 bits wide
  ROM #(.addrWidth(5), .dataWidth(32)) aROM_m (.addr(and_38_out), .data(aROM_m_data));
  assign and_38_out = Address & {5{Sel_m}};  // AND_Gate and_38, 5 bits wide
  assign or_32_out = aROM_l_data | or_29_out;  // OR_Gate or_32, 32 bits wide
  ROM #(.addrWidth(5), .dataWidth(32)) bROM_m (.addr(and_39_out), .data(bROM_m_data));
  assign and_39_out = Address & {5{Sel_m}};  // AND_Gate and_39, 5 bits wide
  assign or_33_out = bROM_l_data | or_30_out;  // OR_Gate or_33, 32 bits wide
  ROM #(.addrWidth(5), .dataWidth(32)) ROM_n (.addr(and_40_out), .data(ROM_n_data));
  assign and_40_out = Address & {5{Sel_n}};  // AND_Gate and_40, 5 bits wide
  assign or_34_out = ROM_m_data | or_31_out;  // OR_Gate or_34, 32 bits wide
  ROM #(.addrWidth(5), .dataWidth(32)) aROM_n (.addr(and_41_out), .data(aROM_n_data));
  assign and_41_out = Address & {5{Sel_n}};  // AND_Gate and_41, 5 bits wide
  assign or_35_out = aROM_m_data | or_32_out;  // OR_Gate or_35, 32 bits wide
  ROM #(.addrWidth(5), .dataWidth(32)) bROM_n (.addr(and_42_out), .data(bROM_n_data));
  assign and_42_out = Address & {5{Sel_n}};  // AND_Gate and_42, 5 bits wide
  assign or_36_out = bROM_m_data | or_33_out;  // OR_Gate or_36, 32 bits wide
  ROM #(.addrWidth(5), .dataWidth(32)) ROM_o (.addr(and_43_out), .data(ROM_o_data));
  assign and_43_out = Address & {5{Sel_o}};  // AND_Gate and_43, 5 bits wide
  assign or_37_out = ROM_n_data | or_34_out;  // OR_Gate or_37, 32 bits wide
  ROM #(.addrWidth(5), .dataWidth(32)) aROM_o (.addr(and_44_out), .data(aROM_o_data));
  assign and_44_out = Address & {5{Sel_o}};  // AND_Gate and_44, 5 bits wide
  assign or_38_out = aROM_n_data | or_35_out;  // OR_Gate or_38, 32 bits wide
  ROM #(.addrWidth(5), .dataWidth(32)) bROM_o (.addr(and_45_out), .data(bROM_o_data));
  assign and_45_out = Address & {5{Sel_o}};  // AND_Gate and_45, 5 bits wide
  assign or_39_out = bROM_n_data | or_36_out;  // OR_Gate or_39, 32 bits wide
  ROM #(.addrWidth(5), .dataWidth(32)) ROM_p (.addr(and_46_out), .data(ROM_p_data));
  assign and_46_out = Address & {5{Sel_p}};  // AND_Gate and_46, 5 bits wide
  ROM #(.addrWidth(5), .dataWidth(32)) aROM_p (.addr(and_47_out), .data(aROM_p_data));
  assign and_47_out = Address & {5{Sel_p}};  // AND_Gate and_47, 5 bits wide
  ROM #(.addrWidth(5), .dataWidth(32)) bROM_p (.addr(and_48_out), .data(bROM_p_data));
  assign and_48_out = Address & {5{Sel_p}};  // AND_Gate and_48, 5 bits wide
  assign or_40_out = ROM_o_data | or_37_out;  // OR_Gate or_40, 32 bits wide
  assign or_41_out = aROM_o_data | or_38_out;  // OR_Gate or_41, 32 bits wide
  assign or_42_out = bROM_o_data | or_39_out;  // OR_Gate or_42, 32 bits wide
  assign Lines = ROM_p_data | or_40_out;  // OR_Gate or_43, 32 bits wide
  assign Linesa = aROM_p_data | or_41_out;  // OR_Gate or_44, 32 bits wide
  assign Linesb = bROM_p_data | or_42_out;  // OR_Gate or_45, 32 bits wide

  // Notes on the sheet:
  //   contents of aROM_a (hex, n*v repeats v):
  //   0 10000000
  //   contents of bROM_a (hex, n*v repeats v):
  //   0 10000000
endmodule
module Instructions10x (
  input  Sel_a,
  input  Sel_b,
  input  Sel_c,
  input  Sel_d,
  input  Sel_e,
  input  Sel_f,
  input  Sel_g,
  input  Sel_h,
  input  Sel_i,
  input  Sel_j,
  input  Sel_k,
  input  Sel_l,
  input  Sel_m,
  input  Sel_n,
  input  Sel_o,
  input  Sel_p,
  input  [4:0] Address,
  output [31:0] Lines,
  output [31:0] Linesa,
  output [31:0] Linesb
);

  wire [4:0] and_1_out, and_2_out, and_3_out, and_4_out, and_5_out, and_6_out, and_7_out, and_8_out,
       and_9_out, and_10_out, and_11_out, and_12_out, and_13_out, and_14_out, and_15_out, and_16_out,
       and_17_out, and_18_out, and_19_out, and_20_out, and_21_out, and_22_out, and_23_out, and_24_out,
       and_25_out, and_26_out, and_27_out, and_28_out, and_29_out, and_30_out, and_31_out, and_32_out,
       and_33_out, and_34_out, and_35_out, and_36_out, and_37_out, and_38_out, and_39_out, and_40_out,
       and_41_out, and_42_out, and_43_out, and_44_out, and_45_out, and_46_out, and_47_out, and_48_out;
  wire [31:0] aROM_a_data, aROM_b_data, aROM_c_data, aROM_d_data, aROM_e_data, aROM_f_data, aROM_g_data,
       aROM_h_data, aROM_i_data, aROM_j_data, aROM_k_data, aROM_l_data, aROM_m_data, aROM_n_data,
       aROM_o_data, aROM_p_data, bROM_a_data, bROM_b_data, bROM_c_data, bROM_d_data, bROM_e_data,
       bROM_f_data, bROM_g_data, bROM_h_data, bROM_i_data, bROM_j_data, bROM_k_data, bROM_l_data,
       bROM_m_data, bROM_n_data, bROM_o_data, bROM_p_data, or_1_out, or_2_out, or_3_out, or_4_out, or_5_out,
       or_6_out, or_7_out, or_8_out, or_9_out, or_10_out, or_11_out, or_12_out, or_13_out, or_14_out,
       or_15_out, or_16_out, or_17_out, or_18_out, or_19_out, or_20_out, or_21_out, or_22_out, or_23_out,
       or_24_out, or_25_out, or_26_out, or_27_out, or_28_out, or_29_out, or_30_out, or_31_out, or_32_out,
       or_33_out, or_34_out, or_35_out, or_36_out, or_37_out, or_38_out, or_39_out, or_40_out, or_41_out,
       or_42_out, ROM_a_data, ROM_b_data, ROM_c_data, ROM_d_data, ROM_e_data, ROM_f_data, ROM_g_data,
       ROM_h_data, ROM_i_data, ROM_j_data, ROM_k_data, ROM_l_data, ROM_m_data, ROM_n_data, ROM_o_data,
       ROM_p_data;

  ROM #(.addrWidth(5), .dataWidth(32)) ROM_a (.addr(and_1_out), .data(ROM_a_data));
  assign and_1_out = Address & {5{Sel_a}};  // AND_Gate and_1, 5 bits wide
  ROM #(.addrWidth(5), .dataWidth(32)) aROM_a (.addr(and_2_out), .data(aROM_a_data));
  assign and_2_out = Address & {5{Sel_a}};  // AND_Gate and_2, 5 bits wide
  ROM #(.addrWidth(5), .dataWidth(32)) bROM_a (.addr(and_3_out), .data(bROM_a_data));
  assign and_3_out = Address & {5{Sel_a}};  // AND_Gate and_3, 5 bits wide
  ROM #(.addrWidth(5), .dataWidth(32)) ROM_b (.addr(and_4_out), .data(ROM_b_data));
  assign and_4_out = Address & {5{Sel_b}};  // AND_Gate and_4, 5 bits wide
  ROM #(.addrWidth(5), .dataWidth(32)) aROM_b (.addr(and_5_out), .data(aROM_b_data));
  assign and_5_out = Address & {5{Sel_b}};  // AND_Gate and_5, 5 bits wide
  ROM #(.addrWidth(5), .dataWidth(32)) bROM_b (.addr(and_6_out), .data(bROM_b_data));
  assign and_6_out = Address & {5{Sel_b}};  // AND_Gate and_6, 5 bits wide
  ROM #(.addrWidth(5), .dataWidth(32)) ROM_c (.addr(and_7_out), .data(ROM_c_data));
  assign and_7_out = Address & {5{Sel_c}};  // AND_Gate and_7, 5 bits wide
  assign or_1_out = ROM_b_data | ROM_a_data;  // OR_Gate or_1, 32 bits wide
  ROM #(.addrWidth(5), .dataWidth(32)) aROM_c (.addr(and_8_out), .data(aROM_c_data));
  assign and_8_out = Address & {5{Sel_c}};  // AND_Gate and_8, 5 bits wide
  assign or_2_out = aROM_b_data | aROM_a_data;  // OR_Gate or_2, 32 bits wide
  ROM #(.addrWidth(5), .dataWidth(32)) bROM_c (.addr(and_9_out), .data(bROM_c_data));
  assign and_9_out = Address & {5{Sel_c}};  // AND_Gate and_9, 5 bits wide
  assign or_3_out = bROM_b_data | bROM_a_data;  // OR_Gate or_3, 32 bits wide
  ROM #(.addrWidth(5), .dataWidth(32)) ROM_d (.addr(and_10_out), .data(ROM_d_data));
  assign and_10_out = Address & {5{Sel_d}};  // AND_Gate and_10, 5 bits wide
  ROM #(.addrWidth(5), .dataWidth(32)) aROM_d (.addr(and_11_out), .data(aROM_d_data));
  assign and_11_out = Address & {5{Sel_d}};  // AND_Gate and_11, 5 bits wide
  ROM #(.addrWidth(5), .dataWidth(32)) bROM_d (.addr(and_12_out), .data(bROM_d_data));
  assign and_12_out = Address & {5{Sel_d}};  // AND_Gate and_12, 5 bits wide
  assign or_4_out = ROM_c_data | or_1_out;  // OR_Gate or_4, 32 bits wide
  assign or_5_out = aROM_c_data | or_2_out;  // OR_Gate or_5, 32 bits wide
  assign or_6_out = bROM_c_data | or_3_out;  // OR_Gate or_6, 32 bits wide
  ROM #(.addrWidth(5), .dataWidth(32)) ROM_e (.addr(and_13_out), .data(ROM_e_data));
  assign and_13_out = Address & {5{Sel_e}};  // AND_Gate and_13, 5 bits wide
  assign or_7_out = ROM_d_data | or_4_out;  // OR_Gate or_7, 32 bits wide
  ROM #(.addrWidth(5), .dataWidth(32)) aROM_e (.addr(and_14_out), .data(aROM_e_data));
  assign and_14_out = Address & {5{Sel_e}};  // AND_Gate and_14, 5 bits wide
  assign or_8_out = aROM_d_data | or_5_out;  // OR_Gate or_8, 32 bits wide
  ROM #(.addrWidth(5), .dataWidth(32)) bROM_e (.addr(and_15_out), .data(bROM_e_data));
  assign and_15_out = Address & {5{Sel_e}};  // AND_Gate and_15, 5 bits wide
  assign or_9_out = bROM_d_data | or_6_out;  // OR_Gate or_9, 32 bits wide
  ROM #(.addrWidth(5), .dataWidth(32)) ROM_f (.addr(and_16_out), .data(ROM_f_data));
  assign and_16_out = Address & {5{Sel_f}};  // AND_Gate and_16, 5 bits wide
  assign or_10_out = ROM_e_data | or_7_out;  // OR_Gate or_10, 32 bits wide
  ROM #(.addrWidth(5), .dataWidth(32)) aROM_f (.addr(and_17_out), .data(aROM_f_data));
  assign and_17_out = Address & {5{Sel_f}};  // AND_Gate and_17, 5 bits wide
  assign or_11_out = aROM_e_data | or_8_out;  // OR_Gate or_11, 32 bits wide
  ROM #(.addrWidth(5), .dataWidth(32)) bROM_f (.addr(and_18_out), .data(bROM_f_data));
  assign and_18_out = Address & {5{Sel_f}};  // AND_Gate and_18, 5 bits wide
  assign or_12_out = bROM_e_data | or_9_out;  // OR_Gate or_12, 32 bits wide
  ROM #(.addrWidth(5), .dataWidth(32)) ROM_g (.addr(and_19_out), .data(ROM_g_data));
  assign and_19_out = Address & {5{Sel_g}};  // AND_Gate and_19, 5 bits wide
  assign or_13_out = ROM_f_data | or_10_out;  // OR_Gate or_13, 32 bits wide
  ROM #(.addrWidth(5), .dataWidth(32)) aROM_g (.addr(and_20_out), .data(aROM_g_data));
  assign and_20_out = Address & {5{Sel_g}};  // AND_Gate and_20, 5 bits wide
  assign or_14_out = aROM_f_data | or_11_out;  // OR_Gate or_14, 32 bits wide
  ROM #(.addrWidth(5), .dataWidth(32)) bROM_g (.addr(and_21_out), .data(bROM_g_data));
  assign and_21_out = Address & {5{Sel_g}};  // AND_Gate and_21, 5 bits wide
  assign or_15_out = bROM_f_data | or_12_out;  // OR_Gate or_15, 32 bits wide
  ROM #(.addrWidth(5), .dataWidth(32)) ROM_h (.addr(and_22_out), .data(ROM_h_data));
  assign and_22_out = Address & {5{Sel_h}};  // AND_Gate and_22, 5 bits wide
  ROM #(.addrWidth(5), .dataWidth(32)) aROM_h (.addr(and_23_out), .data(aROM_h_data));
  assign and_23_out = Address & {5{Sel_h}};  // AND_Gate and_23, 5 bits wide
  ROM #(.addrWidth(5), .dataWidth(32)) bROM_h (.addr(and_24_out), .data(bROM_h_data));
  assign and_24_out = Address & {5{Sel_h}};  // AND_Gate and_24, 5 bits wide
  assign or_16_out = ROM_g_data | or_13_out;  // OR_Gate or_16, 32 bits wide
  assign or_17_out = aROM_g_data | or_14_out;  // OR_Gate or_17, 32 bits wide
  assign or_18_out = bROM_g_data | or_15_out;  // OR_Gate or_18, 32 bits wide
  ROM #(.addrWidth(5), .dataWidth(32)) ROM_i (.addr(and_25_out), .data(ROM_i_data));
  assign and_25_out = Address & {5{Sel_i}};  // AND_Gate and_25, 5 bits wide
  assign or_19_out = ROM_h_data | or_16_out;  // OR_Gate or_19, 32 bits wide
  ROM #(.addrWidth(5), .dataWidth(32)) aROM_i (.addr(and_26_out), .data(aROM_i_data));
  assign and_26_out = Address & {5{Sel_i}};  // AND_Gate and_26, 5 bits wide
  assign or_20_out = aROM_h_data | or_17_out;  // OR_Gate or_20, 32 bits wide
  ROM #(.addrWidth(5), .dataWidth(32)) bROM_i (.addr(and_27_out), .data(bROM_i_data));
  assign and_27_out = Address & {5{Sel_i}};  // AND_Gate and_27, 5 bits wide
  assign or_21_out = bROM_h_data | or_18_out;  // OR_Gate or_21, 32 bits wide
  ROM #(.addrWidth(5), .dataWidth(32)) ROM_j (.addr(and_28_out), .data(ROM_j_data));
  assign and_28_out = Address & {5{Sel_j}};  // AND_Gate and_28, 5 bits wide
  assign or_22_out = ROM_i_data | or_19_out;  // OR_Gate or_22, 32 bits wide
  ROM #(.addrWidth(5), .dataWidth(32)) aROM_j (.addr(and_29_out), .data(aROM_j_data));
  assign and_29_out = Address & {5{Sel_j}};  // AND_Gate and_29, 5 bits wide
  assign or_23_out = aROM_i_data | or_20_out;  // OR_Gate or_23, 32 bits wide
  ROM #(.addrWidth(5), .dataWidth(32)) bROM_j (.addr(and_30_out), .data(bROM_j_data));
  assign and_30_out = Address & {5{Sel_j}};  // AND_Gate and_30, 5 bits wide
  assign or_24_out = bROM_i_data | or_21_out;  // OR_Gate or_24, 32 bits wide
  ROM #(.addrWidth(5), .dataWidth(32)) ROM_k (.addr(and_31_out), .data(ROM_k_data));
  assign and_31_out = Address & {5{Sel_k}};  // AND_Gate and_31, 5 bits wide
  assign or_25_out = ROM_j_data | or_22_out;  // OR_Gate or_25, 32 bits wide
  ROM #(.addrWidth(5), .dataWidth(32)) aROM_k (.addr(and_32_out), .data(aROM_k_data));
  assign and_32_out = Address & {5{Sel_k}};  // AND_Gate and_32, 5 bits wide
  assign or_26_out = aROM_j_data | or_23_out;  // OR_Gate or_26, 32 bits wide
  ROM #(.addrWidth(5), .dataWidth(32)) bROM_k (.addr(and_33_out), .data(bROM_k_data));
  assign and_33_out = Address & {5{Sel_k}};  // AND_Gate and_33, 5 bits wide
  assign or_27_out = bROM_j_data | or_24_out;  // OR_Gate or_27, 32 bits wide
  ROM #(.addrWidth(5), .dataWidth(32)) ROM_l (.addr(and_34_out), .data(ROM_l_data));
  assign and_34_out = Address & {5{Sel_l}};  // AND_Gate and_34, 5 bits wide
  ROM #(.addrWidth(5), .dataWidth(32)) aROM_l (.addr(and_35_out), .data(aROM_l_data));
  assign and_35_out = Address & {5{Sel_l}};  // AND_Gate and_35, 5 bits wide
  ROM #(.addrWidth(5), .dataWidth(32)) bROM_l (.addr(and_36_out), .data(bROM_l_data));
  assign and_36_out = Address & {5{Sel_l}};  // AND_Gate and_36, 5 bits wide
  assign or_28_out = ROM_k_data | or_25_out;  // OR_Gate or_28, 32 bits wide
  assign or_29_out = aROM_k_data | or_26_out;  // OR_Gate or_29, 32 bits wide
  assign or_30_out = bROM_k_data | or_27_out;  // OR_Gate or_30, 32 bits wide
  ROM #(.addrWidth(5), .dataWidth(32)) ROM_m (.addr(and_37_out), .data(ROM_m_data));
  assign and_37_out = Address & {5{Sel_m}};  // AND_Gate and_37, 5 bits wide
  assign or_31_out = ROM_l_data | or_28_out;  // OR_Gate or_31, 32 bits wide
  ROM #(.addrWidth(5), .dataWidth(32)) aROM_m (.addr(and_38_out), .data(aROM_m_data));
  assign and_38_out = Address & {5{Sel_m}};  // AND_Gate and_38, 5 bits wide
  assign or_32_out = aROM_l_data | or_29_out;  // OR_Gate or_32, 32 bits wide
  ROM #(.addrWidth(5), .dataWidth(32)) bROM_m (.addr(and_39_out), .data(bROM_m_data));
  assign and_39_out = Address & {5{Sel_m}};  // AND_Gate and_39, 5 bits wide
  assign or_33_out = bROM_l_data | or_30_out;  // OR_Gate or_33, 32 bits wide
  ROM #(.addrWidth(5), .dataWidth(32)) ROM_n (.addr(and_40_out), .data(ROM_n_data));
  assign and_40_out = Address & {5{Sel_n}};  // AND_Gate and_40, 5 bits wide
  assign or_34_out = ROM_m_data | or_31_out;  // OR_Gate or_34, 32 bits wide
  ROM #(.addrWidth(5), .dataWidth(32)) aROM_n (.addr(and_41_out), .data(aROM_n_data));
  assign and_41_out = Address & {5{Sel_n}};  // AND_Gate and_41, 5 bits wide
  assign or_35_out = aROM_m_data | or_32_out;  // OR_Gate or_35, 32 bits wide
  ROM #(.addrWidth(5), .dataWidth(32)) bROM_n (.addr(and_42_out), .data(bROM_n_data));
  assign and_42_out = Address & {5{Sel_n}};  // AND_Gate and_42, 5 bits wide
  assign or_36_out = bROM_m_data | or_33_out;  // OR_Gate or_36, 32 bits wide
  ROM #(.addrWidth(5), .dataWidth(32)) ROM_o (.addr(and_43_out), .data(ROM_o_data));
  assign and_43_out = Address & {5{Sel_o}};  // AND_Gate and_43, 5 bits wide
  assign or_37_out = ROM_n_data | or_34_out;  // OR_Gate or_37, 32 bits wide
  ROM #(.addrWidth(5), .dataWidth(32)) aROM_o (.addr(and_44_out), .data(aROM_o_data));
  assign and_44_out = Address & {5{Sel_o}};  // AND_Gate and_44, 5 bits wide
  assign or_38_out = aROM_n_data | or_35_out;  // OR_Gate or_38, 32 bits wide
  ROM #(.addrWidth(5), .dataWidth(32)) bROM_o (.addr(and_45_out), .data(bROM_o_data));
  assign and_45_out = Address & {5{Sel_o}};  // AND_Gate and_45, 5 bits wide
  assign or_39_out = bROM_n_data | or_36_out;  // OR_Gate or_39, 32 bits wide
  ROM #(.addrWidth(5), .dataWidth(32)) ROM_p (.addr(and_46_out), .data(ROM_p_data));
  assign and_46_out = Address & {5{Sel_p}};  // AND_Gate and_46, 5 bits wide
  ROM #(.addrWidth(5), .dataWidth(32)) aROM_p (.addr(and_47_out), .data(aROM_p_data));
  assign and_47_out = Address & {5{Sel_p}};  // AND_Gate and_47, 5 bits wide
  ROM #(.addrWidth(5), .dataWidth(32)) bROM_p (.addr(and_48_out), .data(bROM_p_data));
  assign and_48_out = Address & {5{Sel_p}};  // AND_Gate and_48, 5 bits wide
  assign or_40_out = ROM_o_data | or_37_out;  // OR_Gate or_40, 32 bits wide
  assign or_41_out = aROM_o_data | or_38_out;  // OR_Gate or_41, 32 bits wide
  assign or_42_out = bROM_o_data | or_39_out;  // OR_Gate or_42, 32 bits wide
  assign Lines = ROM_p_data | or_40_out;  // OR_Gate or_43, 32 bits wide
  assign Linesa = aROM_p_data | or_41_out;  // OR_Gate or_44, 32 bits wide
  assign Linesb = bROM_p_data | or_42_out;  // OR_Gate or_45, 32 bits wide

  // Notes on the sheet:
  //   contents of aROM_a (hex, n*v repeats v):
  //   0 10000000
  //   contents of bROM_a (hex, n*v repeats v):
  //   0 10000000
endmodule

module Instructions11x (
  input  Sel_a,
  input  Sel_b,
  input  Sel_c,
  input  Sel_d,
  input  Sel_e,
  input  Sel_f,
  input  Sel_g,
  input  Sel_h,
  input  Sel_i,
  input  Sel_j,
  input  Sel_k,
  input  Sel_l,
  input  Sel_m,
  input  Sel_n,
  input  Sel_o,
  input  Sel_p,
  input  [4:0] Address,
  output [31:0] Lines,
  output [31:0] Linesa,
  output [31:0] Linesb
);

  wire [4:0] and_1_out, and_2_out, and_3_out, and_4_out, and_5_out, and_6_out, and_7_out, and_8_out,
       and_9_out, and_10_out, and_11_out, and_12_out, and_13_out, and_14_out, and_15_out, and_16_out,
       and_17_out, and_18_out, and_19_out, and_20_out, and_21_out, and_22_out, and_23_out, and_24_out,
       and_25_out, and_26_out, and_27_out, and_28_out, and_29_out, and_30_out, and_31_out, and_32_out,
       and_33_out, and_34_out, and_35_out, and_36_out, and_37_out, and_38_out, and_39_out, and_40_out,
       and_41_out, and_42_out, and_43_out, and_44_out, and_45_out, and_46_out, and_47_out, and_48_out;
  wire [31:0] aROM_a_data, aROM_b_data, aROM_c_data, aROM_d_data, aROM_e_data, aROM_f_data, aROM_g_data,
       aROM_h_data, aROM_i_data, aROM_j_data, aROM_k_data, aROM_l_data, aROM_m_data, aROM_n_data,
       aROM_o_data, aROM_p_data, bROM_a_data, bROM_b_data, bROM_c_data, bROM_d_data, bROM_e_data,
       bROM_f_data, bROM_g_data, bROM_h_data, bROM_i_data, bROM_j_data, bROM_k_data, bROM_l_data,
       bROM_m_data, bROM_n_data, bROM_o_data, bROM_p_data, or_1_out, or_2_out, or_3_out, or_4_out, or_5_out,
       or_6_out, or_7_out, or_8_out, or_9_out, or_10_out, or_11_out, or_12_out, or_13_out, or_14_out,
       or_15_out, or_16_out, or_17_out, or_18_out, or_19_out, or_20_out, or_21_out, or_22_out, or_23_out,
       or_24_out, or_25_out, or_26_out, or_27_out, or_28_out, or_29_out, or_30_out, or_31_out, or_32_out,
       or_33_out, or_34_out, or_35_out, or_36_out, or_37_out, or_38_out, or_39_out, or_40_out, or_41_out,
       or_42_out, ROM_a_data, ROM_b_data, ROM_c_data, ROM_d_data, ROM_e_data, ROM_f_data, ROM_g_data,
       ROM_h_data, ROM_i_data, ROM_j_data, ROM_k_data, ROM_l_data, ROM_m_data, ROM_n_data, ROM_o_data,
       ROM_p_data;

  ROM #(.addrWidth(5), .dataWidth(32)) ROM_a (.addr(and_1_out), .data(ROM_a_data));
  assign and_1_out = Address & {5{Sel_a}};  // AND_Gate and_1, 5 bits wide
  ROM #(.addrWidth(5), .dataWidth(32)) aROM_a (.addr(and_2_out), .data(aROM_a_data));
  assign and_2_out = Address & {5{Sel_a}};  // AND_Gate and_2, 5 bits wide
  ROM #(.addrWidth(5), .dataWidth(32)) bROM_a (.addr(and_3_out), .data(bROM_a_data));
  assign and_3_out = Address & {5{Sel_a}};  // AND_Gate and_3, 5 bits wide
  ROM #(.addrWidth(5), .dataWidth(32)) ROM_b (.addr(and_4_out), .data(ROM_b_data));
  assign and_4_out = Address & {5{Sel_b}};  // AND_Gate and_4, 5 bits wide
  ROM #(.addrWidth(5), .dataWidth(32)) aROM_b (.addr(and_5_out), .data(aROM_b_data));
  assign and_5_out = Address & {5{Sel_b}};  // AND_Gate and_5, 5 bits wide
  ROM #(.addrWidth(5), .dataWidth(32)) bROM_b (.addr(and_6_out), .data(bROM_b_data));
  assign and_6_out = Address & {5{Sel_b}};  // AND_Gate and_6, 5 bits wide
  ROM #(.addrWidth(5), .dataWidth(32)) ROM_c (.addr(and_7_out), .data(ROM_c_data));
  assign and_7_out = Address & {5{Sel_c}};  // AND_Gate and_7, 5 bits wide
  assign or_1_out = ROM_b_data | ROM_a_data;  // OR_Gate or_1, 32 bits wide
  ROM #(.addrWidth(5), .dataWidth(32)) aROM_c (.addr(and_8_out), .data(aROM_c_data));
  assign and_8_out = Address & {5{Sel_c}};  // AND_Gate and_8, 5 bits wide
  assign or_2_out = aROM_b_data | aROM_a_data;  // OR_Gate or_2, 32 bits wide
  ROM #(.addrWidth(5), .dataWidth(32)) bROM_c (.addr(and_9_out), .data(bROM_c_data));
  assign and_9_out = Address & {5{Sel_c}};  // AND_Gate and_9, 5 bits wide
  assign or_3_out = bROM_b_data | bROM_a_data;  // OR_Gate or_3, 32 bits wide
  ROM #(.addrWidth(5), .dataWidth(32)) ROM_d (.addr(and_10_out), .data(ROM_d_data));
  assign and_10_out = Address & {5{Sel_d}};  // AND_Gate and_10, 5 bits wide
  ROM #(.addrWidth(5), .dataWidth(32)) aROM_d (.addr(and_11_out), .data(aROM_d_data));
  assign and_11_out = Address & {5{Sel_d}};  // AND_Gate and_11, 5 bits wide
  ROM #(.addrWidth(5), .dataWidth(32)) bROM_d (.addr(and_12_out), .data(bROM_d_data));
  assign and_12_out = Address & {5{Sel_d}};  // AND_Gate and_12, 5 bits wide
  assign or_4_out = ROM_c_data | or_1_out;  // OR_Gate or_4, 32 bits wide
  assign or_5_out = aROM_c_data | or_2_out;  // OR_Gate or_5, 32 bits wide
  assign or_6_out = bROM_c_data | or_3_out;  // OR_Gate or_6, 32 bits wide
  ROM #(.addrWidth(5), .dataWidth(32)) ROM_e (.addr(and_13_out), .data(ROM_e_data));
  assign and_13_out = Address & {5{Sel_e}};  // AND_Gate and_13, 5 bits wide
  assign or_7_out = ROM_d_data | or_4_out;  // OR_Gate or_7, 32 bits wide
  ROM #(.addrWidth(5), .dataWidth(32)) aROM_e (.addr(and_14_out), .data(aROM_e_data));
  assign and_14_out = Address & {5{Sel_e}};  // AND_Gate and_14, 5 bits wide
  assign or_8_out = aROM_d_data | or_5_out;  // OR_Gate or_8, 32 bits wide
  ROM #(.addrWidth(5), .dataWidth(32)) bROM_e (.addr(and_15_out), .data(bROM_e_data));
  assign and_15_out = Address & {5{Sel_e}};  // AND_Gate and_15, 5 bits wide
  assign or_9_out = bROM_d_data | or_6_out;  // OR_Gate or_9, 32 bits wide
  ROM #(.addrWidth(5), .dataWidth(32)) ROM_f (.addr(and_16_out), .data(ROM_f_data));
  assign and_16_out = Address & {5{Sel_f}};  // AND_Gate and_16, 5 bits wide
  assign or_10_out = ROM_e_data | or_7_out;  // OR_Gate or_10, 32 bits wide
  ROM #(.addrWidth(5), .dataWidth(32)) aROM_f (.addr(and_17_out), .data(aROM_f_data));
  assign and_17_out = Address & {5{Sel_f}};  // AND_Gate and_17, 5 bits wide
  assign or_11_out = aROM_e_data | or_8_out;  // OR_Gate or_11, 32 bits wide
  ROM #(.addrWidth(5), .dataWidth(32)) bROM_f (.addr(and_18_out), .data(bROM_f_data));
  assign and_18_out = Address & {5{Sel_f}};  // AND_Gate and_18, 5 bits wide
  assign or_12_out = bROM_e_data | or_9_out;  // OR_Gate or_12, 32 bits wide
  ROM #(.addrWidth(5), .dataWidth(32)) ROM_g (.addr(and_19_out), .data(ROM_g_data));
  assign and_19_out = Address & {5{Sel_g}};  // AND_Gate and_19, 5 bits wide
  assign or_13_out = ROM_f_data | or_10_out;  // OR_Gate or_13, 32 bits wide
  ROM #(.addrWidth(5), .dataWidth(32)) aROM_g (.addr(and_20_out), .data(aROM_g_data));
  assign and_20_out = Address & {5{Sel_g}};  // AND_Gate and_20, 5 bits wide
  assign or_14_out = aROM_f_data | or_11_out;  // OR_Gate or_14, 32 bits wide
  ROM #(.addrWidth(5), .dataWidth(32)) bROM_g (.addr(and_21_out), .data(bROM_g_data));
  assign and_21_out = Address & {5{Sel_g}};  // AND_Gate and_21, 5 bits wide
  assign or_15_out = bROM_f_data | or_12_out;  // OR_Gate or_15, 32 bits wide
  ROM #(.addrWidth(5), .dataWidth(32)) ROM_h (.addr(and_22_out), .data(ROM_h_data));
  assign and_22_out = Address & {5{Sel_h}};  // AND_Gate and_22, 5 bits wide
  ROM #(.addrWidth(5), .dataWidth(32)) aROM_h (.addr(and_23_out), .data(aROM_h_data));
  assign and_23_out = Address & {5{Sel_h}};  // AND_Gate and_23, 5 bits wide
  ROM #(.addrWidth(5), .dataWidth(32)) bROM_h (.addr(and_24_out), .data(bROM_h_data));
  assign and_24_out = Address & {5{Sel_h}};  // AND_Gate and_24, 5 bits wide
  assign or_16_out = ROM_g_data | or_13_out;  // OR_Gate or_16, 32 bits wide
  assign or_17_out = aROM_g_data | or_14_out;  // OR_Gate or_17, 32 bits wide
  assign or_18_out = bROM_g_data | or_15_out;  // OR_Gate or_18, 32 bits wide
  ROM #(.addrWidth(5), .dataWidth(32)) ROM_i (.addr(and_25_out), .data(ROM_i_data));
  assign and_25_out = Address & {5{Sel_i}};  // AND_Gate and_25, 5 bits wide
  assign or_19_out = ROM_h_data | or_16_out;  // OR_Gate or_19, 32 bits wide
  ROM #(.addrWidth(5), .dataWidth(32)) aROM_i (.addr(and_26_out), .data(aROM_i_data));
  assign and_26_out = Address & {5{Sel_i}};  // AND_Gate and_26, 5 bits wide
  assign or_20_out = aROM_h_data | or_17_out;  // OR_Gate or_20, 32 bits wide
  ROM #(.addrWidth(5), .dataWidth(32)) bROM_i (.addr(and_27_out), .data(bROM_i_data));
  assign and_27_out = Address & {5{Sel_i}};  // AND_Gate and_27, 5 bits wide
  assign or_21_out = bROM_h_data | or_18_out;  // OR_Gate or_21, 32 bits wide
  ROM #(.addrWidth(5), .dataWidth(32)) ROM_j (.addr(and_28_out), .data(ROM_j_data));
  assign and_28_out = Address & {5{Sel_j}};  // AND_Gate and_28, 5 bits wide
  assign or_22_out = ROM_i_data | or_19_out;  // OR_Gate or_22, 32 bits wide
  ROM #(.addrWidth(5), .dataWidth(32)) aROM_j (.addr(and_29_out), .data(aROM_j_data));
  assign and_29_out = Address & {5{Sel_j}};  // AND_Gate and_29, 5 bits wide
  assign or_23_out = aROM_i_data | or_20_out;  // OR_Gate or_23, 32 bits wide
  ROM #(.addrWidth(5), .dataWidth(32)) bROM_j (.addr(and_30_out), .data(bROM_j_data));
  assign and_30_out = Address & {5{Sel_j}};  // AND_Gate and_30, 5 bits wide
  assign or_24_out = bROM_i_data | or_21_out;  // OR_Gate or_24, 32 bits wide
  ROM #(.addrWidth(5), .dataWidth(32)) ROM_k (.addr(and_31_out), .data(ROM_k_data));
  assign and_31_out = Address & {5{Sel_k}};  // AND_Gate and_31, 5 bits wide
  assign or_25_out = ROM_j_data | or_22_out;  // OR_Gate or_25, 32 bits wide
  ROM #(.addrWidth(5), .dataWidth(32)) aROM_k (.addr(and_32_out), .data(aROM_k_data));
  assign and_32_out = Address & {5{Sel_k}};  // AND_Gate and_32, 5 bits wide
  assign or_26_out = aROM_j_data | or_23_out;  // OR_Gate or_26, 32 bits wide
  ROM #(.addrWidth(5), .dataWidth(32)) bROM_k (.addr(and_33_out), .data(bROM_k_data));
  assign and_33_out = Address & {5{Sel_k}};  // AND_Gate and_33, 5 bits wide
  assign or_27_out = bROM_j_data | or_24_out;  // OR_Gate or_27, 32 bits wide
  ROM #(.addrWidth(5), .dataWidth(32)) ROM_l (.addr(and_34_out), .data(ROM_l_data));
  assign and_34_out = Address & {5{Sel_l}};  // AND_Gate and_34, 5 bits wide
  ROM #(.addrWidth(5), .dataWidth(32)) aROM_l (.addr(and_35_out), .data(aROM_l_data));
  assign and_35_out = Address & {5{Sel_l}};  // AND_Gate and_35, 5 bits wide
  ROM #(.addrWidth(5), .dataWidth(32)) bROM_l (.addr(and_36_out), .data(bROM_l_data));
  assign and_36_out = Address & {5{Sel_l}};  // AND_Gate and_36, 5 bits wide
  assign or_28_out = ROM_k_data | or_25_out;  // OR_Gate or_28, 32 bits wide
  assign or_29_out = aROM_k_data | or_26_out;  // OR_Gate or_29, 32 bits wide
  assign or_30_out = bROM_k_data | or_27_out;  // OR_Gate or_30, 32 bits wide
  ROM #(.addrWidth(5), .dataWidth(32)) ROM_m (.addr(and_37_out), .data(ROM_m_data));
  assign and_37_out = Address & {5{Sel_m}};  // AND_Gate and_37, 5 bits wide
  assign or_31_out = ROM_l_data | or_28_out;  // OR_Gate or_31, 32 bits wide
  ROM #(.addrWidth(5), .dataWidth(32)) aROM_m (.addr(and_38_out), .data(aROM_m_data));
  assign and_38_out = Address & {5{Sel_m}};  // AND_Gate and_38, 5 bits wide
  assign or_32_out = aROM_l_data | or_29_out;  // OR_Gate or_32, 32 bits wide
  ROM #(.addrWidth(5), .dataWidth(32)) bROM_m (.addr(and_39_out), .data(bROM_m_data));
  assign and_39_out = Address & {5{Sel_m}};  // AND_Gate and_39, 5 bits wide
  assign or_33_out = bROM_l_data | or_30_out;  // OR_Gate or_33, 32 bits wide
  ROM #(.addrWidth(5), .dataWidth(32)) ROM_n (.addr(and_40_out), .data(ROM_n_data));
  assign and_40_out = Address & {5{Sel_n}};  // AND_Gate and_40, 5 bits wide
  assign or_34_out = ROM_m_data | or_31_out;  // OR_Gate or_34, 32 bits wide
  ROM #(.addrWidth(5), .dataWidth(32)) aROM_n (.addr(and_41_out), .data(aROM_n_data));
  assign and_41_out = Address & {5{Sel_n}};  // AND_Gate and_41, 5 bits wide
  assign or_35_out = aROM_m_data | or_32_out;  // OR_Gate or_35, 32 bits wide
  ROM #(.addrWidth(5), .dataWidth(32)) bROM_n (.addr(and_42_out), .data(bROM_n_data));
  assign and_42_out = Address & {5{Sel_n}};  // AND_Gate and_42, 5 bits wide
  assign or_36_out = bROM_m_data | or_33_out;  // OR_Gate or_36, 32 bits wide
  ROM #(.addrWidth(5), .dataWidth(32)) ROM_o (.addr(and_43_out), .data(ROM_o_data));
  assign and_43_out = Address & {5{Sel_o}};  // AND_Gate and_43, 5 bits wide
  assign or_37_out = ROM_n_data | or_34_out;  // OR_Gate or_37, 32 bits wide
  ROM #(.addrWidth(5), .dataWidth(32)) aROM_o (.addr(and_44_out), .data(aROM_o_data));
  assign and_44_out = Address & {5{Sel_o}};  // AND_Gate and_44, 5 bits wide
  assign or_38_out = aROM_n_data | or_35_out;  // OR_Gate or_38, 32 bits wide
  ROM #(.addrWidth(5), .dataWidth(32)) bROM_o (.addr(and_45_out), .data(bROM_o_data));
  assign and_45_out = Address & {5{Sel_o}};  // AND_Gate and_45, 5 bits wide
  assign or_39_out = bROM_n_data | or_36_out;  // OR_Gate or_39, 32 bits wide
  ROM #(.addrWidth(5), .dataWidth(32)) ROM_p (.addr(and_46_out), .data(ROM_p_data));
  assign and_46_out = Address & {5{Sel_p}};  // AND_Gate and_46, 5 bits wide
  ROM #(.addrWidth(5), .dataWidth(32)) aROM_p (.addr(and_47_out), .data(aROM_p_data));
  assign and_47_out = Address & {5{Sel_p}};  // AND_Gate and_47, 5 bits wide
  ROM #(.addrWidth(5), .dataWidth(32)) bROM_p (.addr(and_48_out), .data(bROM_p_data));
  assign and_48_out = Address & {5{Sel_p}};  // AND_Gate and_48, 5 bits wide
  assign or_40_out = ROM_o_data | or_37_out;  // OR_Gate or_40, 32 bits wide
  assign or_41_out = aROM_o_data | or_38_out;  // OR_Gate or_41, 32 bits wide
  assign or_42_out = bROM_o_data | or_39_out;  // OR_Gate or_42, 32 bits wide
  assign Lines = ROM_p_data | or_40_out;  // OR_Gate or_43, 32 bits wide
  assign Linesa = aROM_p_data | or_41_out;  // OR_Gate or_44, 32 bits wide
  assign Linesb = bROM_p_data | or_42_out;  // OR_Gate or_45, 32 bits wide

  // Notes on the sheet:
  //   contents of aROM_a (hex, n*v repeats v):
  //   0 10000000
  //   contents of bROM_a (hex, n*v repeats v):
  //   0 10000000
endmodule

module Instructions12x (
  input  Sel_a,
  input  Sel_b,
  input  Sel_c,
  input  Sel_d,
  input  Sel_e,
  input  Sel_f,
  input  Sel_g,
  input  Sel_h,
  input  Sel_i,
  input  Sel_j,
  input  Sel_k,
  input  Sel_l,
  input  Sel_m,
  input  Sel_n,
  input  Sel_o,
  input  Sel_p,
  input  [4:0] Address,
  output [31:0] Lines,
  output [31:0] Linesa,
  output [31:0] Linesb
);

  wire [4:0] and_1_out, and_2_out, and_3_out, and_4_out, and_5_out, and_6_out, and_7_out, and_8_out,
       and_9_out, and_10_out, and_11_out, and_12_out, and_13_out, and_14_out, and_15_out, and_16_out,
       and_17_out, and_18_out, and_19_out, and_20_out, and_21_out, and_22_out, and_23_out, and_24_out,
       and_25_out, and_26_out, and_27_out, and_28_out, and_29_out, and_30_out, and_31_out, and_32_out,
       and_33_out, and_34_out, and_35_out, and_36_out, and_37_out, and_38_out, and_39_out, and_40_out,
       and_41_out, and_42_out, and_43_out, and_44_out, and_45_out, and_46_out, and_47_out, and_48_out;
  wire [31:0] aROM_a_data, aROM_b_data, aROM_c_data, aROM_d_data, aROM_e_data, aROM_f_data, aROM_g_data,
       aROM_h_data, aROM_i_data, aROM_j_data, aROM_k_data, aROM_l_data, aROM_m_data, aROM_n_data,
       aROM_o_data, aROM_p_data, bROM_a_data, bROM_b_data, bROM_c_data, bROM_d_data, bROM_e_data,
       bROM_f_data, bROM_g_data, bROM_h_data, bROM_i_data, bROM_j_data, bROM_k_data, bROM_l_data,
       bROM_m_data, bROM_n_data, bROM_o_data, bROM_p_data, or_1_out, or_2_out, or_3_out, or_4_out, or_5_out,
       or_6_out, or_7_out, or_8_out, or_9_out, or_10_out, or_11_out, or_12_out, or_13_out, or_14_out,
       or_15_out, or_16_out, or_17_out, or_18_out, or_19_out, or_20_out, or_21_out, or_22_out, or_23_out,
       or_24_out, or_25_out, or_26_out, or_27_out, or_28_out, or_29_out, or_30_out, or_31_out, or_32_out,
       or_33_out, or_34_out, or_35_out, or_36_out, or_37_out, or_38_out, or_39_out, or_40_out, or_41_out,
       or_42_out, ROM_a_data, ROM_b_data, ROM_c_data, ROM_d_data, ROM_e_data, ROM_f_data, ROM_g_data,
       ROM_h_data, ROM_i_data, ROM_j_data, ROM_k_data, ROM_l_data, ROM_m_data, ROM_n_data, ROM_o_data,
       ROM_p_data;

  ROM #(.addrWidth(5), .dataWidth(32)) ROM_a (.addr(and_1_out), .data(ROM_a_data));
  assign and_1_out = Address & {5{Sel_a}};  // AND_Gate and_1, 5 bits wide
  ROM #(.addrWidth(5), .dataWidth(32)) aROM_a (.addr(and_2_out), .data(aROM_a_data));
  assign and_2_out = Address & {5{Sel_a}};  // AND_Gate and_2, 5 bits wide
  ROM #(.addrWidth(5), .dataWidth(32)) bROM_a (.addr(and_3_out), .data(bROM_a_data));
  assign and_3_out = Address & {5{Sel_a}};  // AND_Gate and_3, 5 bits wide
  ROM #(.addrWidth(5), .dataWidth(32)) ROM_b (.addr(and_4_out), .data(ROM_b_data));
  assign and_4_out = Address & {5{Sel_b}};  // AND_Gate and_4, 5 bits wide
  ROM #(.addrWidth(5), .dataWidth(32)) aROM_b (.addr(and_5_out), .data(aROM_b_data));
  assign and_5_out = Address & {5{Sel_b}};  // AND_Gate and_5, 5 bits wide
  ROM #(.addrWidth(5), .dataWidth(32)) bROM_b (.addr(and_6_out), .data(bROM_b_data));
  assign and_6_out = Address & {5{Sel_b}};  // AND_Gate and_6, 5 bits wide
  ROM #(.addrWidth(5), .dataWidth(32)) ROM_c (.addr(and_7_out), .data(ROM_c_data));
  assign and_7_out = Address & {5{Sel_c}};  // AND_Gate and_7, 5 bits wide
  assign or_1_out = ROM_b_data | ROM_a_data;  // OR_Gate or_1, 32 bits wide
  ROM #(.addrWidth(5), .dataWidth(32)) aROM_c (.addr(and_8_out), .data(aROM_c_data));
  assign and_8_out = Address & {5{Sel_c}};  // AND_Gate and_8, 5 bits wide
  assign or_2_out = aROM_b_data | aROM_a_data;  // OR_Gate or_2, 32 bits wide
  ROM #(.addrWidth(5), .dataWidth(32)) bROM_c (.addr(and_9_out), .data(bROM_c_data));
  assign and_9_out = Address & {5{Sel_c}};  // AND_Gate and_9, 5 bits wide
  assign or_3_out = bROM_b_data | bROM_a_data;  // OR_Gate or_3, 32 bits wide
  ROM #(.addrWidth(5), .dataWidth(32)) ROM_d (.addr(and_10_out), .data(ROM_d_data));
  assign and_10_out = Address & {5{Sel_d}};  // AND_Gate and_10, 5 bits wide
  ROM #(.addrWidth(5), .dataWidth(32)) aROM_d (.addr(and_11_out), .data(aROM_d_data));
  assign and_11_out = Address & {5{Sel_d}};  // AND_Gate and_11, 5 bits wide
  ROM #(.addrWidth(5), .dataWidth(32)) bROM_d (.addr(and_12_out), .data(bROM_d_data));
  assign and_12_out = Address & {5{Sel_d}};  // AND_Gate and_12, 5 bits wide
  assign or_4_out = ROM_c_data | or_1_out;  // OR_Gate or_4, 32 bits wide
  assign or_5_out = aROM_c_data | or_2_out;  // OR_Gate or_5, 32 bits wide
  assign or_6_out = bROM_c_data | or_3_out;  // OR_Gate or_6, 32 bits wide
  ROM #(.addrWidth(5), .dataWidth(32)) ROM_e (.addr(and_13_out), .data(ROM_e_data));
  assign and_13_out = Address & {5{Sel_e}};  // AND_Gate and_13, 5 bits wide
  assign or_7_out = ROM_d_data | or_4_out;  // OR_Gate or_7, 32 bits wide
  ROM #(.addrWidth(5), .dataWidth(32)) aROM_e (.addr(and_14_out), .data(aROM_e_data));
  assign and_14_out = Address & {5{Sel_e}};  // AND_Gate and_14, 5 bits wide
  assign or_8_out = aROM_d_data | or_5_out;  // OR_Gate or_8, 32 bits wide
  ROM #(.addrWidth(5), .dataWidth(32)) bROM_e (.addr(and_15_out), .data(bROM_e_data));
  assign and_15_out = Address & {5{Sel_e}};  // AND_Gate and_15, 5 bits wide
  assign or_9_out = bROM_d_data | or_6_out;  // OR_Gate or_9, 32 bits wide
  ROM #(.addrWidth(5), .dataWidth(32)) ROM_f (.addr(and_16_out), .data(ROM_f_data));
  assign and_16_out = Address & {5{Sel_f}};  // AND_Gate and_16, 5 bits wide
  assign or_10_out = ROM_e_data | or_7_out;  // OR_Gate or_10, 32 bits wide
  ROM #(.addrWidth(5), .dataWidth(32)) aROM_f (.addr(and_17_out), .data(aROM_f_data));
  assign and_17_out = Address & {5{Sel_f}};  // AND_Gate and_17, 5 bits wide
  assign or_11_out = aROM_e_data | or_8_out;  // OR_Gate or_11, 32 bits wide
  ROM #(.addrWidth(5), .dataWidth(32)) bROM_f (.addr(and_18_out), .data(bROM_f_data));
  assign and_18_out = Address & {5{Sel_f}};  // AND_Gate and_18, 5 bits wide
  assign or_12_out = bROM_e_data | or_9_out;  // OR_Gate or_12, 32 bits wide
  ROM #(.addrWidth(5), .dataWidth(32)) ROM_g (.addr(and_19_out), .data(ROM_g_data));
  assign and_19_out = Address & {5{Sel_g}};  // AND_Gate and_19, 5 bits wide
  assign or_13_out = ROM_f_data | or_10_out;  // OR_Gate or_13, 32 bits wide
  ROM #(.addrWidth(5), .dataWidth(32)) aROM_g (.addr(and_20_out), .data(aROM_g_data));
  assign and_20_out = Address & {5{Sel_g}};  // AND_Gate and_20, 5 bits wide
  assign or_14_out = aROM_f_data | or_11_out;  // OR_Gate or_14, 32 bits wide
  ROM #(.addrWidth(5), .dataWidth(32)) bROM_g (.addr(and_21_out), .data(bROM_g_data));
  assign and_21_out = Address & {5{Sel_g}};  // AND_Gate and_21, 5 bits wide
  assign or_15_out = bROM_f_data | or_12_out;  // OR_Gate or_15, 32 bits wide
  ROM #(.addrWidth(5), .dataWidth(32)) ROM_h (.addr(and_22_out), .data(ROM_h_data));
  assign and_22_out = Address & {5{Sel_h}};  // AND_Gate and_22, 5 bits wide
  ROM #(.addrWidth(5), .dataWidth(32)) aROM_h (.addr(and_23_out), .data(aROM_h_data));
  assign and_23_out = Address & {5{Sel_h}};  // AND_Gate and_23, 5 bits wide
  ROM #(.addrWidth(5), .dataWidth(32)) bROM_h (.addr(and_24_out), .data(bROM_h_data));
  assign and_24_out = Address & {5{Sel_h}};  // AND_Gate and_24, 5 bits wide
  assign or_16_out = ROM_g_data | or_13_out;  // OR_Gate or_16, 32 bits wide
  assign or_17_out = aROM_g_data | or_14_out;  // OR_Gate or_17, 32 bits wide
  assign or_18_out = bROM_g_data | or_15_out;  // OR_Gate or_18, 32 bits wide
  ROM #(.addrWidth(5), .dataWidth(32)) ROM_i (.addr(and_25_out), .data(ROM_i_data));
  assign and_25_out = Address & {5{Sel_i}};  // AND_Gate and_25, 5 bits wide
  assign or_19_out = ROM_h_data | or_16_out;  // OR_Gate or_19, 32 bits wide
  ROM #(.addrWidth(5), .dataWidth(32)) aROM_i (.addr(and_26_out), .data(aROM_i_data));
  assign and_26_out = Address & {5{Sel_i}};  // AND_Gate and_26, 5 bits wide
  assign or_20_out = aROM_h_data | or_17_out;  // OR_Gate or_20, 32 bits wide
  ROM #(.addrWidth(5), .dataWidth(32)) bROM_i (.addr(and_27_out), .data(bROM_i_data));
  assign and_27_out = Address & {5{Sel_i}};  // AND_Gate and_27, 5 bits wide
  assign or_21_out = bROM_h_data | or_18_out;  // OR_Gate or_21, 32 bits wide
  ROM #(.addrWidth(5), .dataWidth(32)) ROM_j (.addr(and_28_out), .data(ROM_j_data));
  assign and_28_out = Address & {5{Sel_j}};  // AND_Gate and_28, 5 bits wide
  assign or_22_out = ROM_i_data | or_19_out;  // OR_Gate or_22, 32 bits wide
  ROM #(.addrWidth(5), .dataWidth(32)) aROM_j (.addr(and_29_out), .data(aROM_j_data));
  assign and_29_out = Address & {5{Sel_j}};  // AND_Gate and_29, 5 bits wide
  assign or_23_out = aROM_i_data | or_20_out;  // OR_Gate or_23, 32 bits wide
  ROM #(.addrWidth(5), .dataWidth(32)) bROM_j (.addr(and_30_out), .data(bROM_j_data));
  assign and_30_out = Address & {5{Sel_j}};  // AND_Gate and_30, 5 bits wide
  assign or_24_out = bROM_i_data | or_21_out;  // OR_Gate or_24, 32 bits wide
  ROM #(.addrWidth(5), .dataWidth(32)) ROM_k (.addr(and_31_out), .data(ROM_k_data));
  assign and_31_out = Address & {5{Sel_k}};  // AND_Gate and_31, 5 bits wide
  assign or_25_out = ROM_j_data | or_22_out;  // OR_Gate or_25, 32 bits wide
  ROM #(.addrWidth(5), .dataWidth(32)) aROM_k (.addr(and_32_out), .data(aROM_k_data));
  assign and_32_out = Address & {5{Sel_k}};  // AND_Gate and_32, 5 bits wide
  assign or_26_out = aROM_j_data | or_23_out;  // OR_Gate or_26, 32 bits wide
  ROM #(.addrWidth(5), .dataWidth(32)) bROM_k (.addr(and_33_out), .data(bROM_k_data));
  assign and_33_out = Address & {5{Sel_k}};  // AND_Gate and_33, 5 bits wide
  assign or_27_out = bROM_j_data | or_24_out;  // OR_Gate or_27, 32 bits wide
  ROM #(.addrWidth(5), .dataWidth(32)) ROM_l (.addr(and_34_out), .data(ROM_l_data));
  assign and_34_out = Address & {5{Sel_l}};  // AND_Gate and_34, 5 bits wide
  ROM #(.addrWidth(5), .dataWidth(32)) aROM_l (.addr(and_35_out), .data(aROM_l_data));
  assign and_35_out = Address & {5{Sel_l}};  // AND_Gate and_35, 5 bits wide
  ROM #(.addrWidth(5), .dataWidth(32)) bROM_l (.addr(and_36_out), .data(bROM_l_data));
  assign and_36_out = Address & {5{Sel_l}};  // AND_Gate and_36, 5 bits wide
  assign or_28_out = ROM_k_data | or_25_out;  // OR_Gate or_28, 32 bits wide
  assign or_29_out = aROM_k_data | or_26_out;  // OR_Gate or_29, 32 bits wide
  assign or_30_out = bROM_k_data | or_27_out;  // OR_Gate or_30, 32 bits wide
  ROM #(.addrWidth(5), .dataWidth(32)) ROM_m (.addr(and_37_out), .data(ROM_m_data));
  assign and_37_out = Address & {5{Sel_m}};  // AND_Gate and_37, 5 bits wide
  assign or_31_out = ROM_l_data | or_28_out;  // OR_Gate or_31, 32 bits wide
  ROM #(.addrWidth(5), .dataWidth(32)) aROM_m (.addr(and_38_out), .data(aROM_m_data));
  assign and_38_out = Address & {5{Sel_m}};  // AND_Gate and_38, 5 bits wide
  assign or_32_out = aROM_l_data | or_29_out;  // OR_Gate or_32, 32 bits wide
  ROM #(.addrWidth(5), .dataWidth(32)) bROM_m (.addr(and_39_out), .data(bROM_m_data));
  assign and_39_out = Address & {5{Sel_m}};  // AND_Gate and_39, 5 bits wide
  assign or_33_out = bROM_l_data | or_30_out;  // OR_Gate or_33, 32 bits wide
  ROM #(.addrWidth(5), .dataWidth(32)) ROM_n (.addr(and_40_out), .data(ROM_n_data));
  assign and_40_out = Address & {5{Sel_n}};  // AND_Gate and_40, 5 bits wide
  assign or_34_out = ROM_m_data | or_31_out;  // OR_Gate or_34, 32 bits wide
  ROM #(.addrWidth(5), .dataWidth(32)) aROM_n (.addr(and_41_out), .data(aROM_n_data));
  assign and_41_out = Address & {5{Sel_n}};  // AND_Gate and_41, 5 bits wide
  assign or_35_out = aROM_m_data | or_32_out;  // OR_Gate or_35, 32 bits wide
  ROM #(.addrWidth(5), .dataWidth(32)) bROM_n (.addr(and_42_out), .data(bROM_n_data));
  assign and_42_out = Address & {5{Sel_n}};  // AND_Gate and_42, 5 bits wide
  assign or_36_out = bROM_m_data | or_33_out;  // OR_Gate or_36, 32 bits wide
  ROM #(.addrWidth(5), .dataWidth(32)) ROM_o (.addr(and_43_out), .data(ROM_o_data));
  assign and_43_out = Address & {5{Sel_o}};  // AND_Gate and_43, 5 bits wide
  assign or_37_out = ROM_n_data | or_34_out;  // OR_Gate or_37, 32 bits wide
  ROM #(.addrWidth(5), .dataWidth(32)) aROM_o (.addr(and_44_out), .data(aROM_o_data));
  assign and_44_out = Address & {5{Sel_o}};  // AND_Gate and_44, 5 bits wide
  assign or_38_out = aROM_n_data | or_35_out;  // OR_Gate or_38, 32 bits wide
  ROM #(.addrWidth(5), .dataWidth(32)) bROM_o (.addr(and_45_out), .data(bROM_o_data));
  assign and_45_out = Address & {5{Sel_o}};  // AND_Gate and_45, 5 bits wide
  assign or_39_out = bROM_n_data | or_36_out;  // OR_Gate or_39, 32 bits wide
  ROM #(.addrWidth(5), .dataWidth(32)) ROM_p (.addr(and_46_out), .data(ROM_p_data));
  assign and_46_out = Address & {5{Sel_p}};  // AND_Gate and_46, 5 bits wide
  ROM #(.addrWidth(5), .dataWidth(32)) aROM_p (.addr(and_47_out), .data(aROM_p_data));
  assign and_47_out = Address & {5{Sel_p}};  // AND_Gate and_47, 5 bits wide
  ROM #(.addrWidth(5), .dataWidth(32)) bROM_p (.addr(and_48_out), .data(bROM_p_data));
  assign and_48_out = Address & {5{Sel_p}};  // AND_Gate and_48, 5 bits wide
  assign or_40_out = ROM_o_data | or_37_out;  // OR_Gate or_40, 32 bits wide
  assign or_41_out = aROM_o_data | or_38_out;  // OR_Gate or_41, 32 bits wide
  assign or_42_out = bROM_o_data | or_39_out;  // OR_Gate or_42, 32 bits wide
  assign Lines = ROM_p_data | or_40_out;  // OR_Gate or_43, 32 bits wide
  assign Linesa = aROM_p_data | or_41_out;  // OR_Gate or_44, 32 bits wide
  assign Linesb = bROM_p_data | or_42_out;  // OR_Gate or_45, 32 bits wide

  // Notes on the sheet:
  //   contents of aROM_a (hex, n*v repeats v):
  //   0 10000000
  //   contents of bROM_a (hex, n*v repeats v):
  //   0 10000000
  //   contents of ROM_d (hex, n*v repeats v):
  //   0 10000000 20000000 0 8000000 4050000 10000000 20000000 0 8000000 4040000 11008010 40000000
  //   contents of bROM_d (hex, n*v repeats v):
  //   0 2000000 0 0 1000000 0 2000000 0 0 1000000
endmodule

module Instructions13x (
  input  Sel_a,
  input  Sel_b,
  input  Sel_c,
  input  Sel_d,
  input  Sel_e,
  input  Sel_f,
  input  Sel_g,
  input  Sel_h,
  input  Sel_i,
  input  Sel_j,
  input  Sel_k,
  input  Sel_l,
  input  Sel_m,
  input  Sel_n,
  input  Sel_o,
  input  Sel_p,
  input  [4:0] Address,
  output [31:0] Lines,
  output [31:0] Linesa,
  output [31:0] Linesb
);

  wire [4:0] and_1_out, and_2_out, and_3_out, and_4_out, and_5_out, and_6_out, and_7_out, and_8_out,
       and_9_out, and_10_out, and_11_out, and_12_out, and_13_out, and_14_out, and_15_out, and_16_out,
       and_17_out, and_18_out, and_19_out, and_20_out, and_21_out, and_22_out, and_23_out, and_24_out,
       and_25_out, and_26_out, and_27_out, and_28_out, and_29_out, and_30_out, and_31_out, and_32_out,
       and_33_out, and_34_out, and_35_out, and_36_out, and_37_out, and_38_out, and_39_out, and_40_out,
       and_41_out, and_42_out, and_43_out, and_44_out, and_45_out, and_46_out, and_47_out, and_48_out;
  wire [31:0] aROM_a_data, aROM_b_data, aROM_c_data, aROM_d_data, aROM_e_data, aROM_f_data, aROM_g_data,
       aROM_h_data, aROM_i_data, aROM_j_data, aROM_k_data, aROM_l_data, aROM_m_data, aROM_n_data,
       aROM_o_data, aROM_p_data, bROM_a_data, bROM_b_data, bROM_c_data, bROM_d_data, bROM_e_data,
       bROM_f_data, bROM_g_data, bROM_h_data, bROM_i_data, bROM_j_data, bROM_k_data, bROM_l_data,
       bROM_m_data, bROM_n_data, bROM_o_data, bROM_p_data, or_1_out, or_2_out, or_3_out, or_4_out, or_5_out,
       or_6_out, or_7_out, or_8_out, or_9_out, or_10_out, or_11_out, or_12_out, or_13_out, or_14_out,
       or_15_out, or_16_out, or_17_out, or_18_out, or_19_out, or_20_out, or_21_out, or_22_out, or_23_out,
       or_24_out, or_25_out, or_26_out, or_27_out, or_28_out, or_29_out, or_30_out, or_31_out, or_32_out,
       or_33_out, or_34_out, or_35_out, or_36_out, or_37_out, or_38_out, or_39_out, or_40_out, or_41_out,
       or_42_out, ROM_a_data, ROM_b_data, ROM_c_data, ROM_d_data, ROM_e_data, ROM_f_data, ROM_g_data,
       ROM_h_data, ROM_i_data, ROM_j_data, ROM_k_data, ROM_l_data, ROM_m_data, ROM_n_data, ROM_o_data,
       ROM_p_data;

  ROM #(.addrWidth(5), .dataWidth(32)) ROM_a (.addr(and_1_out), .data(ROM_a_data));
  assign and_1_out = Address & {5{Sel_a}};  // AND_Gate and_1, 5 bits wide
  ROM #(.addrWidth(5), .dataWidth(32)) aROM_a (.addr(and_2_out), .data(aROM_a_data));
  assign and_2_out = Address & {5{Sel_a}};  // AND_Gate and_2, 5 bits wide
  ROM #(.addrWidth(5), .dataWidth(32)) bROM_a (.addr(and_3_out), .data(bROM_a_data));
  assign and_3_out = Address & {5{Sel_a}};  // AND_Gate and_3, 5 bits wide
  ROM #(.addrWidth(5), .dataWidth(32)) ROM_b (.addr(and_4_out), .data(ROM_b_data));
  assign and_4_out = Address & {5{Sel_b}};  // AND_Gate and_4, 5 bits wide
  ROM #(.addrWidth(5), .dataWidth(32)) aROM_b (.addr(and_5_out), .data(aROM_b_data));
  assign and_5_out = Address & {5{Sel_b}};  // AND_Gate and_5, 5 bits wide
  ROM #(.addrWidth(5), .dataWidth(32)) bROM_b (.addr(and_6_out), .data(bROM_b_data));
  assign and_6_out = Address & {5{Sel_b}};  // AND_Gate and_6, 5 bits wide
  ROM #(.addrWidth(5), .dataWidth(32)) ROM_c (.addr(and_7_out), .data(ROM_c_data));
  assign and_7_out = Address & {5{Sel_c}};  // AND_Gate and_7, 5 bits wide
  assign or_1_out = ROM_b_data | ROM_a_data;  // OR_Gate or_1, 32 bits wide
  ROM #(.addrWidth(5), .dataWidth(32)) aROM_c (.addr(and_8_out), .data(aROM_c_data));
  assign and_8_out = Address & {5{Sel_c}};  // AND_Gate and_8, 5 bits wide
  assign or_2_out = aROM_b_data | aROM_a_data;  // OR_Gate or_2, 32 bits wide
  ROM #(.addrWidth(5), .dataWidth(32)) bROM_c (.addr(and_9_out), .data(bROM_c_data));
  assign and_9_out = Address & {5{Sel_c}};  // AND_Gate and_9, 5 bits wide
  assign or_3_out = bROM_b_data | bROM_a_data;  // OR_Gate or_3, 32 bits wide
  ROM #(.addrWidth(5), .dataWidth(32)) ROM_d (.addr(and_10_out), .data(ROM_d_data));
  assign and_10_out = Address & {5{Sel_d}};  // AND_Gate and_10, 5 bits wide
  ROM #(.addrWidth(5), .dataWidth(32)) aROM_d (.addr(and_11_out), .data(aROM_d_data));
  assign and_11_out = Address & {5{Sel_d}};  // AND_Gate and_11, 5 bits wide
  ROM #(.addrWidth(5), .dataWidth(32)) bROM_d (.addr(and_12_out), .data(bROM_d_data));
  assign and_12_out = Address & {5{Sel_d}};  // AND_Gate and_12, 5 bits wide
  assign or_4_out = ROM_c_data | or_1_out;  // OR_Gate or_4, 32 bits wide
  assign or_5_out = aROM_c_data | or_2_out;  // OR_Gate or_5, 32 bits wide
  assign or_6_out = bROM_c_data | or_3_out;  // OR_Gate or_6, 32 bits wide
  ROM #(.addrWidth(5), .dataWidth(32)) ROM_e (.addr(and_13_out), .data(ROM_e_data));
  assign and_13_out = Address & {5{Sel_e}};  // AND_Gate and_13, 5 bits wide
  assign or_7_out = ROM_d_data | or_4_out;  // OR_Gate or_7, 32 bits wide
  ROM #(.addrWidth(5), .dataWidth(32)) aROM_e (.addr(and_14_out), .data(aROM_e_data));
  assign and_14_out = Address & {5{Sel_e}};  // AND_Gate and_14, 5 bits wide
  assign or_8_out = aROM_d_data | or_5_out;  // OR_Gate or_8, 32 bits wide
  ROM #(.addrWidth(5), .dataWidth(32)) bROM_e (.addr(and_15_out), .data(bROM_e_data));
  assign and_15_out = Address & {5{Sel_e}};  // AND_Gate and_15, 5 bits wide
  assign or_9_out = bROM_d_data | or_6_out;  // OR_Gate or_9, 32 bits wide
  ROM #(.addrWidth(5), .dataWidth(32)) ROM_f (.addr(and_16_out), .data(ROM_f_data));
  assign and_16_out = Address & {5{Sel_f}};  // AND_Gate and_16, 5 bits wide
  assign or_10_out = ROM_e_data | or_7_out;  // OR_Gate or_10, 32 bits wide
  ROM #(.addrWidth(5), .dataWidth(32)) aROM_f (.addr(and_17_out), .data(aROM_f_data));
  assign and_17_out = Address & {5{Sel_f}};  // AND_Gate and_17, 5 bits wide
  assign or_11_out = aROM_e_data | or_8_out;  // OR_Gate or_11, 32 bits wide
  ROM #(.addrWidth(5), .dataWidth(32)) bROM_f (.addr(and_18_out), .data(bROM_f_data));
  assign and_18_out = Address & {5{Sel_f}};  // AND_Gate and_18, 5 bits wide
  assign or_12_out = bROM_e_data | or_9_out;  // OR_Gate or_12, 32 bits wide
  ROM #(.addrWidth(5), .dataWidth(32)) ROM_g (.addr(and_19_out), .data(ROM_g_data));
  assign and_19_out = Address & {5{Sel_g}};  // AND_Gate and_19, 5 bits wide
  assign or_13_out = ROM_f_data | or_10_out;  // OR_Gate or_13, 32 bits wide
  ROM #(.addrWidth(5), .dataWidth(32)) aROM_g (.addr(and_20_out), .data(aROM_g_data));
  assign and_20_out = Address & {5{Sel_g}};  // AND_Gate and_20, 5 bits wide
  assign or_14_out = aROM_f_data | or_11_out;  // OR_Gate or_14, 32 bits wide
  ROM #(.addrWidth(5), .dataWidth(32)) bROM_g (.addr(and_21_out), .data(bROM_g_data));
  assign and_21_out = Address & {5{Sel_g}};  // AND_Gate and_21, 5 bits wide
  assign or_15_out = bROM_f_data | or_12_out;  // OR_Gate or_15, 32 bits wide
  ROM #(.addrWidth(5), .dataWidth(32)) ROM_h (.addr(and_22_out), .data(ROM_h_data));
  assign and_22_out = Address & {5{Sel_h}};  // AND_Gate and_22, 5 bits wide
  ROM #(.addrWidth(5), .dataWidth(32)) aROM_h (.addr(and_23_out), .data(aROM_h_data));
  assign and_23_out = Address & {5{Sel_h}};  // AND_Gate and_23, 5 bits wide
  ROM #(.addrWidth(5), .dataWidth(32)) bROM_h (.addr(and_24_out), .data(bROM_h_data));
  assign and_24_out = Address & {5{Sel_h}};  // AND_Gate and_24, 5 bits wide
  assign or_16_out = ROM_g_data | or_13_out;  // OR_Gate or_16, 32 bits wide
  assign or_17_out = aROM_g_data | or_14_out;  // OR_Gate or_17, 32 bits wide
  assign or_18_out = bROM_g_data | or_15_out;  // OR_Gate or_18, 32 bits wide
  ROM #(.addrWidth(5), .dataWidth(32)) ROM_i (.addr(and_25_out), .data(ROM_i_data));
  assign and_25_out = Address & {5{Sel_i}};  // AND_Gate and_25, 5 bits wide
  assign or_19_out = ROM_h_data | or_16_out;  // OR_Gate or_19, 32 bits wide
  ROM #(.addrWidth(5), .dataWidth(32)) aROM_i (.addr(and_26_out), .data(aROM_i_data));
  assign and_26_out = Address & {5{Sel_i}};  // AND_Gate and_26, 5 bits wide
  assign or_20_out = aROM_h_data | or_17_out;  // OR_Gate or_20, 32 bits wide
  ROM #(.addrWidth(5), .dataWidth(32)) bROM_i (.addr(and_27_out), .data(bROM_i_data));
  assign and_27_out = Address & {5{Sel_i}};  // AND_Gate and_27, 5 bits wide
  assign or_21_out = bROM_h_data | or_18_out;  // OR_Gate or_21, 32 bits wide
  ROM #(.addrWidth(5), .dataWidth(32)) ROM_j (.addr(and_28_out), .data(ROM_j_data));
  assign and_28_out = Address & {5{Sel_j}};  // AND_Gate and_28, 5 bits wide
  assign or_22_out = ROM_i_data | or_19_out;  // OR_Gate or_22, 32 bits wide
  ROM #(.addrWidth(5), .dataWidth(32)) aROM_j (.addr(and_29_out), .data(aROM_j_data));
  assign and_29_out = Address & {5{Sel_j}};  // AND_Gate and_29, 5 bits wide
  assign or_23_out = aROM_i_data | or_20_out;  // OR_Gate or_23, 32 bits wide
  ROM #(.addrWidth(5), .dataWidth(32)) bROM_j (.addr(and_30_out), .data(bROM_j_data));
  assign and_30_out = Address & {5{Sel_j}};  // AND_Gate and_30, 5 bits wide
  assign or_24_out = bROM_i_data | or_21_out;  // OR_Gate or_24, 32 bits wide
  ROM #(.addrWidth(5), .dataWidth(32)) ROM_k (.addr(and_31_out), .data(ROM_k_data));
  assign and_31_out = Address & {5{Sel_k}};  // AND_Gate and_31, 5 bits wide
  assign or_25_out = ROM_j_data | or_22_out;  // OR_Gate or_25, 32 bits wide
  ROM #(.addrWidth(5), .dataWidth(32)) aROM_k (.addr(and_32_out), .data(aROM_k_data));
  assign and_32_out = Address & {5{Sel_k}};  // AND_Gate and_32, 5 bits wide
  assign or_26_out = aROM_j_data | or_23_out;  // OR_Gate or_26, 32 bits wide
  ROM #(.addrWidth(5), .dataWidth(32)) bROM_k (.addr(and_33_out), .data(bROM_k_data));
  assign and_33_out = Address & {5{Sel_k}};  // AND_Gate and_33, 5 bits wide
  assign or_27_out = bROM_j_data | or_24_out;  // OR_Gate or_27, 32 bits wide
  ROM #(.addrWidth(5), .dataWidth(32)) ROM_l (.addr(and_34_out), .data(ROM_l_data));
  assign and_34_out = Address & {5{Sel_l}};  // AND_Gate and_34, 5 bits wide
  ROM #(.addrWidth(5), .dataWidth(32)) aROM_l (.addr(and_35_out), .data(aROM_l_data));
  assign and_35_out = Address & {5{Sel_l}};  // AND_Gate and_35, 5 bits wide
  ROM #(.addrWidth(5), .dataWidth(32)) bROM_l (.addr(and_36_out), .data(bROM_l_data));
  assign and_36_out = Address & {5{Sel_l}};  // AND_Gate and_36, 5 bits wide
  assign or_28_out = ROM_k_data | or_25_out;  // OR_Gate or_28, 32 bits wide
  assign or_29_out = aROM_k_data | or_26_out;  // OR_Gate or_29, 32 bits wide
  assign or_30_out = bROM_k_data | or_27_out;  // OR_Gate or_30, 32 bits wide
  ROM #(.addrWidth(5), .dataWidth(32)) ROM_m (.addr(and_37_out), .data(ROM_m_data));
  assign and_37_out = Address & {5{Sel_m}};  // AND_Gate and_37, 5 bits wide
  assign or_31_out = ROM_l_data | or_28_out;  // OR_Gate or_31, 32 bits wide
  ROM #(.addrWidth(5), .dataWidth(32)) aROM_m (.addr(and_38_out), .data(aROM_m_data));
  assign and_38_out = Address & {5{Sel_m}};  // AND_Gate and_38, 5 bits wide
  assign or_32_out = aROM_l_data | or_29_out;  // OR_Gate or_32, 32 bits wide
  ROM #(.addrWidth(5), .dataWidth(32)) bROM_m (.addr(and_39_out), .data(bROM_m_data));
  assign and_39_out = Address & {5{Sel_m}};  // AND_Gate and_39, 5 bits wide
  assign or_33_out = bROM_l_data | or_30_out;  // OR_Gate or_33, 32 bits wide
  ROM #(.addrWidth(5), .dataWidth(32)) ROM_n (.addr(and_40_out), .data(ROM_n_data));
  assign and_40_out = Address & {5{Sel_n}};  // AND_Gate and_40, 5 bits wide
  assign or_34_out = ROM_m_data | or_31_out;  // OR_Gate or_34, 32 bits wide
  ROM #(.addrWidth(5), .dataWidth(32)) aROM_n (.addr(and_41_out), .data(aROM_n_data));
  assign and_41_out = Address & {5{Sel_n}};  // AND_Gate and_41, 5 bits wide
  assign or_35_out = aROM_m_data | or_32_out;  // OR_Gate or_35, 32 bits wide
  ROM #(.addrWidth(5), .dataWidth(32)) bROM_n (.addr(and_42_out), .data(bROM_n_data));
  assign and_42_out = Address & {5{Sel_n}};  // AND_Gate and_42, 5 bits wide
  assign or_36_out = bROM_m_data | or_33_out;  // OR_Gate or_36, 32 bits wide
  ROM #(.addrWidth(5), .dataWidth(32)) ROM_o (.addr(and_43_out), .data(ROM_o_data));
  assign and_43_out = Address & {5{Sel_o}};  // AND_Gate and_43, 5 bits wide
  assign or_37_out = ROM_n_data | or_34_out;  // OR_Gate or_37, 32 bits wide
  ROM #(.addrWidth(5), .dataWidth(32)) aROM_o (.addr(and_44_out), .data(aROM_o_data));
  assign and_44_out = Address & {5{Sel_o}};  // AND_Gate and_44, 5 bits wide
  assign or_38_out = aROM_n_data | or_35_out;  // OR_Gate or_38, 32 bits wide
  ROM #(.addrWidth(5), .dataWidth(32)) bROM_o (.addr(and_45_out), .data(bROM_o_data));
  assign and_45_out = Address & {5{Sel_o}};  // AND_Gate and_45, 5 bits wide
  assign or_39_out = bROM_n_data | or_36_out;  // OR_Gate or_39, 32 bits wide
  ROM #(.addrWidth(5), .dataWidth(32)) ROM_p (.addr(and_46_out), .data(ROM_p_data));
  assign and_46_out = Address & {5{Sel_p}};  // AND_Gate and_46, 5 bits wide
  ROM #(.addrWidth(5), .dataWidth(32)) aROM_p (.addr(and_47_out), .data(aROM_p_data));
  assign and_47_out = Address & {5{Sel_p}};  // AND_Gate and_47, 5 bits wide
  ROM #(.addrWidth(5), .dataWidth(32)) bROM_p (.addr(and_48_out), .data(bROM_p_data));
  assign and_48_out = Address & {5{Sel_p}};  // AND_Gate and_48, 5 bits wide
  assign or_40_out = ROM_o_data | or_37_out;  // OR_Gate or_40, 32 bits wide
  assign or_41_out = aROM_o_data | or_38_out;  // OR_Gate or_41, 32 bits wide
  assign or_42_out = bROM_o_data | or_39_out;  // OR_Gate or_42, 32 bits wide
  assign Lines = ROM_p_data | or_40_out;  // OR_Gate or_43, 32 bits wide
  assign Linesa = aROM_p_data | or_41_out;  // OR_Gate or_44, 32 bits wide
  assign Linesb = bROM_p_data | or_42_out;  // OR_Gate or_45, 32 bits wide

  // Notes on the sheet:
  //   contents of aROM_a (hex, n*v repeats v):
  //   0 10000000
  //   contents of bROM_a (hex, n*v repeats v):
  //   0 10000000
  //   contents of ROM_d (hex, n*v repeats v):
  //   0 10000000 20000000 0 8000000 4050000 23008010 8000000 80000000
  //   contents of bROM_d (hex, n*v repeats v):
  //   0 2000000 0 0 1000000 0 0 4000000 8100000
  //   contents of ROM_l (hex, n*v repeats v):
  //   0 10000000 20000000 0 8000000 4050000 23008010 8000000 80000001
  //   contents of bROM_l (hex, n*v repeats v):
  //   0 2000000 0 0 1000000 0 0 1100000
endmodule

module Instructions14x (
  input  Sel_a,
  input  Sel_b,
  input  Sel_c,
  input  Sel_d,
  input  Sel_e,
  input  Sel_f,
  input  Sel_g,
  input  Sel_h,
  input  Sel_i,
  input  Sel_j,
  input  Sel_k,
  input  Sel_l,
  input  Sel_m,
  input  Sel_n,
  input  Sel_o,
  input  Sel_p,
  input  [4:0] Address,
  output [31:0] Lines,
  output [31:0] Linesa,
  output [31:0] Linesb
);

  wire [4:0] and_1_out, and_2_out, and_3_out, and_4_out, and_5_out, and_6_out, and_7_out, and_8_out,
       and_9_out, and_10_out, and_11_out, and_12_out, and_13_out, and_14_out, and_15_out, and_16_out,
       and_17_out, and_18_out, and_19_out, and_20_out, and_21_out, and_22_out, and_23_out, and_24_out,
       and_25_out, and_26_out, and_27_out, and_28_out, and_29_out, and_30_out, and_31_out, and_32_out,
       and_33_out, and_34_out, and_35_out, and_36_out, and_37_out, and_38_out, and_39_out, and_40_out,
       and_41_out, and_42_out, and_43_out, and_44_out, and_45_out, and_46_out, and_47_out, and_48_out;
  wire [31:0] aROM_a_data, aROM_b_data, aROM_c_data, aROM_d_data, aROM_e_data, aROM_f_data, aROM_g_data,
       aROM_h_data, aROM_i_data, aROM_j_data, aROM_k_data, aROM_l_data, aROM_m_data, aROM_n_data,
       aROM_o_data, aROM_p_data, bROM_a_data, bROM_b_data, bROM_c_data, bROM_d_data, bROM_e_data,
       bROM_f_data, bROM_g_data, bROM_h_data, bROM_i_data, bROM_j_data, bROM_k_data, bROM_l_data,
       bROM_m_data, bROM_n_data, bROM_o_data, bROM_p_data, or_1_out, or_2_out, or_3_out, or_4_out, or_5_out,
       or_6_out, or_7_out, or_8_out, or_9_out, or_10_out, or_11_out, or_12_out, or_13_out, or_14_out,
       or_15_out, or_16_out, or_17_out, or_18_out, or_19_out, or_20_out, or_21_out, or_22_out, or_23_out,
       or_24_out, or_25_out, or_26_out, or_27_out, or_28_out, or_29_out, or_30_out, or_31_out, or_32_out,
       or_33_out, or_34_out, or_35_out, or_36_out, or_37_out, or_38_out, or_39_out, or_40_out, or_41_out,
       or_42_out, ROM_a_data, ROM_b_data, ROM_c_data, ROM_d_data, ROM_e_data, ROM_f_data, ROM_g_data,
       ROM_h_data, ROM_i_data, ROM_j_data, ROM_k_data, ROM_l_data, ROM_m_data, ROM_n_data, ROM_o_data,
       ROM_p_data;

  ROM #(.addrWidth(5), .dataWidth(32)) ROM_a (.addr(and_1_out), .data(ROM_a_data));
  assign and_1_out = Address & {5{Sel_a}};  // AND_Gate and_1, 5 bits wide
  ROM #(.addrWidth(5), .dataWidth(32)) aROM_a (.addr(and_2_out), .data(aROM_a_data));
  assign and_2_out = Address & {5{Sel_a}};  // AND_Gate and_2, 5 bits wide
  ROM #(.addrWidth(5), .dataWidth(32)) bROM_a (.addr(and_3_out), .data(bROM_a_data));
  assign and_3_out = Address & {5{Sel_a}};  // AND_Gate and_3, 5 bits wide
  ROM #(.addrWidth(5), .dataWidth(32)) ROM_b (.addr(and_4_out), .data(ROM_b_data));
  assign and_4_out = Address & {5{Sel_b}};  // AND_Gate and_4, 5 bits wide
  ROM #(.addrWidth(5), .dataWidth(32)) aROM_b (.addr(and_5_out), .data(aROM_b_data));
  assign and_5_out = Address & {5{Sel_b}};  // AND_Gate and_5, 5 bits wide
  ROM #(.addrWidth(5), .dataWidth(32)) bROM_b (.addr(and_6_out), .data(bROM_b_data));
  assign and_6_out = Address & {5{Sel_b}};  // AND_Gate and_6, 5 bits wide
  ROM #(.addrWidth(5), .dataWidth(32)) ROM_c (.addr(and_7_out), .data(ROM_c_data));
  assign and_7_out = Address & {5{Sel_c}};  // AND_Gate and_7, 5 bits wide
  assign or_1_out = ROM_b_data | ROM_a_data;  // OR_Gate or_1, 32 bits wide
  ROM #(.addrWidth(5), .dataWidth(32)) aROM_c (.addr(and_8_out), .data(aROM_c_data));
  assign and_8_out = Address & {5{Sel_c}};  // AND_Gate and_8, 5 bits wide
  assign or_2_out = aROM_b_data | aROM_a_data;  // OR_Gate or_2, 32 bits wide
  ROM #(.addrWidth(5), .dataWidth(32)) bROM_c (.addr(and_9_out), .data(bROM_c_data));
  assign and_9_out = Address & {5{Sel_c}};  // AND_Gate and_9, 5 bits wide
  assign or_3_out = bROM_b_data | bROM_a_data;  // OR_Gate or_3, 32 bits wide
  ROM #(.addrWidth(5), .dataWidth(32)) ROM_d (.addr(and_10_out), .data(ROM_d_data));
  assign and_10_out = Address & {5{Sel_d}};  // AND_Gate and_10, 5 bits wide
  ROM #(.addrWidth(5), .dataWidth(32)) aROM_d (.addr(and_11_out), .data(aROM_d_data));
  assign and_11_out = Address & {5{Sel_d}};  // AND_Gate and_11, 5 bits wide
  ROM #(.addrWidth(5), .dataWidth(32)) bROM_d (.addr(and_12_out), .data(bROM_d_data));
  assign and_12_out = Address & {5{Sel_d}};  // AND_Gate and_12, 5 bits wide
  assign or_4_out = ROM_c_data | or_1_out;  // OR_Gate or_4, 32 bits wide
  assign or_5_out = aROM_c_data | or_2_out;  // OR_Gate or_5, 32 bits wide
  assign or_6_out = bROM_c_data | or_3_out;  // OR_Gate or_6, 32 bits wide
  ROM #(.addrWidth(5), .dataWidth(32)) ROM_e (.addr(and_13_out), .data(ROM_e_data));
  assign and_13_out = Address & {5{Sel_e}};  // AND_Gate and_13, 5 bits wide
  assign or_7_out = ROM_d_data | or_4_out;  // OR_Gate or_7, 32 bits wide
  ROM #(.addrWidth(5), .dataWidth(32)) aROM_e (.addr(and_14_out), .data(aROM_e_data));
  assign and_14_out = Address & {5{Sel_e}};  // AND_Gate and_14, 5 bits wide
  assign or_8_out = aROM_d_data | or_5_out;  // OR_Gate or_8, 32 bits wide
  ROM #(.addrWidth(5), .dataWidth(32)) bROM_e (.addr(and_15_out), .data(bROM_e_data));
  assign and_15_out = Address & {5{Sel_e}};  // AND_Gate and_15, 5 bits wide
  assign or_9_out = bROM_d_data | or_6_out;  // OR_Gate or_9, 32 bits wide
  ROM #(.addrWidth(5), .dataWidth(32)) ROM_f (.addr(and_16_out), .data(ROM_f_data));
  assign and_16_out = Address & {5{Sel_f}};  // AND_Gate and_16, 5 bits wide
  assign or_10_out = ROM_e_data | or_7_out;  // OR_Gate or_10, 32 bits wide
  ROM #(.addrWidth(5), .dataWidth(32)) aROM_f (.addr(and_17_out), .data(aROM_f_data));
  assign and_17_out = Address & {5{Sel_f}};  // AND_Gate and_17, 5 bits wide
  assign or_11_out = aROM_e_data | or_8_out;  // OR_Gate or_11, 32 bits wide
  ROM #(.addrWidth(5), .dataWidth(32)) bROM_f (.addr(and_18_out), .data(bROM_f_data));
  assign and_18_out = Address & {5{Sel_f}};  // AND_Gate and_18, 5 bits wide
  assign or_12_out = bROM_e_data | or_9_out;  // OR_Gate or_12, 32 bits wide
  ROM #(.addrWidth(5), .dataWidth(32)) ROM_g (.addr(and_19_out), .data(ROM_g_data));
  assign and_19_out = Address & {5{Sel_g}};  // AND_Gate and_19, 5 bits wide
  assign or_13_out = ROM_f_data | or_10_out;  // OR_Gate or_13, 32 bits wide
  ROM #(.addrWidth(5), .dataWidth(32)) aROM_g (.addr(and_20_out), .data(aROM_g_data));
  assign and_20_out = Address & {5{Sel_g}};  // AND_Gate and_20, 5 bits wide
  assign or_14_out = aROM_f_data | or_11_out;  // OR_Gate or_14, 32 bits wide
  ROM #(.addrWidth(5), .dataWidth(32)) bROM_g (.addr(and_21_out), .data(bROM_g_data));
  assign and_21_out = Address & {5{Sel_g}};  // AND_Gate and_21, 5 bits wide
  assign or_15_out = bROM_f_data | or_12_out;  // OR_Gate or_15, 32 bits wide
  ROM #(.addrWidth(5), .dataWidth(32)) ROM_h (.addr(and_22_out), .data(ROM_h_data));
  assign and_22_out = Address & {5{Sel_h}};  // AND_Gate and_22, 5 bits wide
  ROM #(.addrWidth(5), .dataWidth(32)) aROM_h (.addr(and_23_out), .data(aROM_h_data));
  assign and_23_out = Address & {5{Sel_h}};  // AND_Gate and_23, 5 bits wide
  ROM #(.addrWidth(5), .dataWidth(32)) bROM_h (.addr(and_24_out), .data(bROM_h_data));
  assign and_24_out = Address & {5{Sel_h}};  // AND_Gate and_24, 5 bits wide
  assign or_16_out = ROM_g_data | or_13_out;  // OR_Gate or_16, 32 bits wide
  assign or_17_out = aROM_g_data | or_14_out;  // OR_Gate or_17, 32 bits wide
  assign or_18_out = bROM_g_data | or_15_out;  // OR_Gate or_18, 32 bits wide
  ROM #(.addrWidth(5), .dataWidth(32)) ROM_i (.addr(and_25_out), .data(ROM_i_data));
  assign and_25_out = Address & {5{Sel_i}};  // AND_Gate and_25, 5 bits wide
  assign or_19_out = ROM_h_data | or_16_out;  // OR_Gate or_19, 32 bits wide
  ROM #(.addrWidth(5), .dataWidth(32)) aROM_i (.addr(and_26_out), .data(aROM_i_data));
  assign and_26_out = Address & {5{Sel_i}};  // AND_Gate and_26, 5 bits wide
  assign or_20_out = aROM_h_data | or_17_out;  // OR_Gate or_20, 32 bits wide
  ROM #(.addrWidth(5), .dataWidth(32)) bROM_i (.addr(and_27_out), .data(bROM_i_data));
  assign and_27_out = Address & {5{Sel_i}};  // AND_Gate and_27, 5 bits wide
  assign or_21_out = bROM_h_data | or_18_out;  // OR_Gate or_21, 32 bits wide
  ROM #(.addrWidth(5), .dataWidth(32)) ROM_j (.addr(and_28_out), .data(ROM_j_data));
  assign and_28_out = Address & {5{Sel_j}};  // AND_Gate and_28, 5 bits wide
  assign or_22_out = ROM_i_data | or_19_out;  // OR_Gate or_22, 32 bits wide
  ROM #(.addrWidth(5), .dataWidth(32)) aROM_j (.addr(and_29_out), .data(aROM_j_data));
  assign and_29_out = Address & {5{Sel_j}};  // AND_Gate and_29, 5 bits wide
  assign or_23_out = aROM_i_data | or_20_out;  // OR_Gate or_23, 32 bits wide
  ROM #(.addrWidth(5), .dataWidth(32)) bROM_j (.addr(and_30_out), .data(bROM_j_data));
  assign and_30_out = Address & {5{Sel_j}};  // AND_Gate and_30, 5 bits wide
  assign or_24_out = bROM_i_data | or_21_out;  // OR_Gate or_24, 32 bits wide
  ROM #(.addrWidth(5), .dataWidth(32)) ROM_k (.addr(and_31_out), .data(ROM_k_data));
  assign and_31_out = Address & {5{Sel_k}};  // AND_Gate and_31, 5 bits wide
  assign or_25_out = ROM_j_data | or_22_out;  // OR_Gate or_25, 32 bits wide
  ROM #(.addrWidth(5), .dataWidth(32)) aROM_k (.addr(and_32_out), .data(aROM_k_data));
  assign and_32_out = Address & {5{Sel_k}};  // AND_Gate and_32, 5 bits wide
  assign or_26_out = aROM_j_data | or_23_out;  // OR_Gate or_26, 32 bits wide
  ROM #(.addrWidth(5), .dataWidth(32)) bROM_k (.addr(and_33_out), .data(bROM_k_data));
  assign and_33_out = Address & {5{Sel_k}};  // AND_Gate and_33, 5 bits wide
  assign or_27_out = bROM_j_data | or_24_out;  // OR_Gate or_27, 32 bits wide
  ROM #(.addrWidth(5), .dataWidth(32)) ROM_l (.addr(and_34_out), .data(ROM_l_data));
  assign and_34_out = Address & {5{Sel_l}};  // AND_Gate and_34, 5 bits wide
  ROM #(.addrWidth(5), .dataWidth(32)) aROM_l (.addr(and_35_out), .data(aROM_l_data));
  assign and_35_out = Address & {5{Sel_l}};  // AND_Gate and_35, 5 bits wide
  ROM #(.addrWidth(5), .dataWidth(32)) bROM_l (.addr(and_36_out), .data(bROM_l_data));
  assign and_36_out = Address & {5{Sel_l}};  // AND_Gate and_36, 5 bits wide
  assign or_28_out = ROM_k_data | or_25_out;  // OR_Gate or_28, 32 bits wide
  assign or_29_out = aROM_k_data | or_26_out;  // OR_Gate or_29, 32 bits wide
  assign or_30_out = bROM_k_data | or_27_out;  // OR_Gate or_30, 32 bits wide
  ROM #(.addrWidth(5), .dataWidth(32)) ROM_m (.addr(and_37_out), .data(ROM_m_data));
  assign and_37_out = Address & {5{Sel_m}};  // AND_Gate and_37, 5 bits wide
  assign or_31_out = ROM_l_data | or_28_out;  // OR_Gate or_31, 32 bits wide
  ROM #(.addrWidth(5), .dataWidth(32)) aROM_m (.addr(and_38_out), .data(aROM_m_data));
  assign and_38_out = Address & {5{Sel_m}};  // AND_Gate and_38, 5 bits wide
  assign or_32_out = aROM_l_data | or_29_out;  // OR_Gate or_32, 32 bits wide
  ROM #(.addrWidth(5), .dataWidth(32)) bROM_m (.addr(and_39_out), .data(bROM_m_data));
  assign and_39_out = Address & {5{Sel_m}};  // AND_Gate and_39, 5 bits wide
  assign or_33_out = bROM_l_data | or_30_out;  // OR_Gate or_33, 32 bits wide
  ROM #(.addrWidth(5), .dataWidth(32)) ROM_n (.addr(and_40_out), .data(ROM_n_data));
  assign and_40_out = Address & {5{Sel_n}};  // AND_Gate and_40, 5 bits wide
  assign or_34_out = ROM_m_data | or_31_out;  // OR_Gate or_34, 32 bits wide
  ROM #(.addrWidth(5), .dataWidth(32)) aROM_n (.addr(and_41_out), .data(aROM_n_data));
  assign and_41_out = Address & {5{Sel_n}};  // AND_Gate and_41, 5 bits wide
  assign or_35_out = aROM_m_data | or_32_out;  // OR_Gate or_35, 32 bits wide
  ROM #(.addrWidth(5), .dataWidth(32)) bROM_n (.addr(and_42_out), .data(bROM_n_data));
  assign and_42_out = Address & {5{Sel_n}};  // AND_Gate and_42, 5 bits wide
  assign or_36_out = bROM_m_data | or_33_out;  // OR_Gate or_36, 32 bits wide
  ROM #(.addrWidth(5), .dataWidth(32)) ROM_o (.addr(and_43_out), .data(ROM_o_data));
  assign and_43_out = Address & {5{Sel_o}};  // AND_Gate and_43, 5 bits wide
  assign or_37_out = ROM_n_data | or_34_out;  // OR_Gate or_37, 32 bits wide
  ROM #(.addrWidth(5), .dataWidth(32)) aROM_o (.addr(and_44_out), .data(aROM_o_data));
  assign and_44_out = Address & {5{Sel_o}};  // AND_Gate and_44, 5 bits wide
  assign or_38_out = aROM_n_data | or_35_out;  // OR_Gate or_38, 32 bits wide
  ROM #(.addrWidth(5), .dataWidth(32)) bROM_o (.addr(and_45_out), .data(bROM_o_data));
  assign and_45_out = Address & {5{Sel_o}};  // AND_Gate and_45, 5 bits wide
  assign or_39_out = bROM_n_data | or_36_out;  // OR_Gate or_39, 32 bits wide
  ROM #(.addrWidth(5), .dataWidth(32)) ROM_p (.addr(and_46_out), .data(ROM_p_data));
  assign and_46_out = Address & {5{Sel_p}};  // AND_Gate and_46, 5 bits wide
  ROM #(.addrWidth(5), .dataWidth(32)) aROM_p (.addr(and_47_out), .data(aROM_p_data));
  assign and_47_out = Address & {5{Sel_p}};  // AND_Gate and_47, 5 bits wide
  ROM #(.addrWidth(5), .dataWidth(32)) bROM_p (.addr(and_48_out), .data(bROM_p_data));
  assign and_48_out = Address & {5{Sel_p}};  // AND_Gate and_48, 5 bits wide
  assign or_40_out = ROM_o_data | or_37_out;  // OR_Gate or_40, 32 bits wide
  assign or_41_out = aROM_o_data | or_38_out;  // OR_Gate or_41, 32 bits wide
  assign or_42_out = bROM_o_data | or_39_out;  // OR_Gate or_42, 32 bits wide
  assign Lines = ROM_p_data | or_40_out;  // OR_Gate or_43, 32 bits wide
  assign Linesa = aROM_p_data | or_41_out;  // OR_Gate or_44, 32 bits wide
  assign Linesb = bROM_p_data | or_42_out;  // OR_Gate or_45, 32 bits wide

  // Notes on the sheet:
  //   contents of aROM_a (hex, n*v repeats v):
  //   0 10000000
  //   contents of bROM_a (hex, n*v repeats v):
  //   0 10000000
  //   contents of ROM_k (hex, n*v repeats v):
  //   0 0 8000004 1 0 10000000 20000000 0 8000000 4050000 10000000 20000000 0 8000000 4040000 11008010
  //   40000000
  //   contents of aROM_k (hex, n*v repeats v):
  //   0 1 0 0 1000
  //   contents of bROM_k (hex, n*v repeats v):
  //   4*0 800000 2000000 0 0 1000000 0 2000000 0 0 1000000
endmodule

module Instructions15x (
  input  Sel_a,
  input  Sel_b,
  input  Sel_c,
  input  Sel_d,
  input  Sel_e,
  input  Sel_f,
  input  Sel_g,
  input  Sel_h,
  input  Sel_i,
  input  Sel_j,
  input  Sel_k,
  input  Sel_l,
  input  Sel_m,
  input  Sel_n,
  input  Sel_o,
  input  Sel_p,
  input  [4:0] Address,
  output [31:0] Lines,
  output [31:0] Linesa,
  output [31:0] Linesb
);

  wire [4:0] and_1_out, and_2_out, and_3_out, and_4_out, and_5_out, and_6_out, and_7_out, and_8_out,
       and_9_out, and_10_out, and_11_out, and_12_out, and_13_out, and_14_out, and_15_out, and_16_out,
       and_17_out, and_18_out, and_19_out, and_20_out, and_21_out, and_22_out, and_23_out, and_24_out,
       and_25_out, and_26_out, and_27_out, and_28_out, and_29_out, and_30_out, and_31_out, and_32_out,
       and_33_out, and_34_out, and_35_out, and_36_out, and_37_out, and_38_out, and_39_out, and_40_out,
       and_41_out, and_42_out, and_43_out, and_44_out, and_45_out, and_46_out, and_47_out, and_48_out;
  wire [31:0] aROM_a_data, aROM_b_data, aROM_c_data, aROM_d_data, aROM_e_data, aROM_f_data, aROM_g_data,
       aROM_h_data, aROM_i_data, aROM_j_data, aROM_k_data, aROM_l_data, aROM_m_data, aROM_n_data,
       aROM_o_data, aROM_p_data, bROM_a_data, bROM_b_data, bROM_c_data, bROM_d_data, bROM_e_data,
       bROM_f_data, bROM_g_data, bROM_h_data, bROM_i_data, bROM_j_data, bROM_k_data, bROM_l_data,
       bROM_m_data, bROM_n_data, bROM_o_data, bROM_p_data, or_1_out, or_2_out, or_3_out, or_4_out, or_5_out,
       or_6_out, or_7_out, or_8_out, or_9_out, or_10_out, or_11_out, or_12_out, or_13_out, or_14_out,
       or_15_out, or_16_out, or_17_out, or_18_out, or_19_out, or_20_out, or_21_out, or_22_out, or_23_out,
       or_24_out, or_25_out, or_26_out, or_27_out, or_28_out, or_29_out, or_30_out, or_31_out, or_32_out,
       or_33_out, or_34_out, or_35_out, or_36_out, or_37_out, or_38_out, or_39_out, or_40_out, or_41_out,
       or_42_out, ROM_a_data, ROM_b_data, ROM_c_data, ROM_d_data, ROM_e_data, ROM_f_data, ROM_g_data,
       ROM_h_data, ROM_i_data, ROM_j_data, ROM_k_data, ROM_l_data, ROM_m_data, ROM_n_data, ROM_o_data,
       ROM_p_data;

  ROM #(.addrWidth(5), .dataWidth(32)) ROM_a (.addr(and_1_out), .data(ROM_a_data));
  assign and_1_out = Address & {5{Sel_a}};  // AND_Gate and_1, 5 bits wide
  ROM #(.addrWidth(5), .dataWidth(32)) aROM_a (.addr(and_2_out), .data(aROM_a_data));
  assign and_2_out = Address & {5{Sel_a}};  // AND_Gate and_2, 5 bits wide
  ROM #(.addrWidth(5), .dataWidth(32)) bROM_a (.addr(and_3_out), .data(bROM_a_data));
  assign and_3_out = Address & {5{Sel_a}};  // AND_Gate and_3, 5 bits wide
  ROM #(.addrWidth(5), .dataWidth(32)) ROM_b (.addr(and_4_out), .data(ROM_b_data));
  assign and_4_out = Address & {5{Sel_b}};  // AND_Gate and_4, 5 bits wide
  ROM #(.addrWidth(5), .dataWidth(32)) aROM_b (.addr(and_5_out), .data(aROM_b_data));
  assign and_5_out = Address & {5{Sel_b}};  // AND_Gate and_5, 5 bits wide
  ROM #(.addrWidth(5), .dataWidth(32)) bROM_b (.addr(and_6_out), .data(bROM_b_data));
  assign and_6_out = Address & {5{Sel_b}};  // AND_Gate and_6, 5 bits wide
  ROM #(.addrWidth(5), .dataWidth(32)) ROM_c (.addr(and_7_out), .data(ROM_c_data));
  assign and_7_out = Address & {5{Sel_c}};  // AND_Gate and_7, 5 bits wide
  assign or_1_out = ROM_b_data | ROM_a_data;  // OR_Gate or_1, 32 bits wide
  ROM #(.addrWidth(5), .dataWidth(32)) aROM_c (.addr(and_8_out), .data(aROM_c_data));
  assign and_8_out = Address & {5{Sel_c}};  // AND_Gate and_8, 5 bits wide
  assign or_2_out = aROM_b_data | aROM_a_data;  // OR_Gate or_2, 32 bits wide
  ROM #(.addrWidth(5), .dataWidth(32)) bROM_c (.addr(and_9_out), .data(bROM_c_data));
  assign and_9_out = Address & {5{Sel_c}};  // AND_Gate and_9, 5 bits wide
  assign or_3_out = bROM_b_data | bROM_a_data;  // OR_Gate or_3, 32 bits wide
  ROM #(.addrWidth(5), .dataWidth(32)) ROM_d (.addr(and_10_out), .data(ROM_d_data));
  assign and_10_out = Address & {5{Sel_d}};  // AND_Gate and_10, 5 bits wide
  ROM #(.addrWidth(5), .dataWidth(32)) aROM_d (.addr(and_11_out), .data(aROM_d_data));
  assign and_11_out = Address & {5{Sel_d}};  // AND_Gate and_11, 5 bits wide
  ROM #(.addrWidth(5), .dataWidth(32)) bROM_d (.addr(and_12_out), .data(bROM_d_data));
  assign and_12_out = Address & {5{Sel_d}};  // AND_Gate and_12, 5 bits wide
  assign or_4_out = ROM_c_data | or_1_out;  // OR_Gate or_4, 32 bits wide
  assign or_5_out = aROM_c_data | or_2_out;  // OR_Gate or_5, 32 bits wide
  assign or_6_out = bROM_c_data | or_3_out;  // OR_Gate or_6, 32 bits wide
  ROM #(.addrWidth(5), .dataWidth(32)) ROM_e (.addr(and_13_out), .data(ROM_e_data));
  assign and_13_out = Address & {5{Sel_e}};  // AND_Gate and_13, 5 bits wide
  assign or_7_out = ROM_d_data | or_4_out;  // OR_Gate or_7, 32 bits wide
  ROM #(.addrWidth(5), .dataWidth(32)) aROM_e (.addr(and_14_out), .data(aROM_e_data));
  assign and_14_out = Address & {5{Sel_e}};  // AND_Gate and_14, 5 bits wide
  assign or_8_out = aROM_d_data | or_5_out;  // OR_Gate or_8, 32 bits wide
  ROM #(.addrWidth(5), .dataWidth(32)) bROM_e (.addr(and_15_out), .data(bROM_e_data));
  assign and_15_out = Address & {5{Sel_e}};  // AND_Gate and_15, 5 bits wide
  assign or_9_out = bROM_d_data | or_6_out;  // OR_Gate or_9, 32 bits wide
  ROM #(.addrWidth(5), .dataWidth(32)) ROM_f (.addr(and_16_out), .data(ROM_f_data));
  assign and_16_out = Address & {5{Sel_f}};  // AND_Gate and_16, 5 bits wide
  assign or_10_out = ROM_e_data | or_7_out;  // OR_Gate or_10, 32 bits wide
  ROM #(.addrWidth(5), .dataWidth(32)) aROM_f (.addr(and_17_out), .data(aROM_f_data));
  assign and_17_out = Address & {5{Sel_f}};  // AND_Gate and_17, 5 bits wide
  assign or_11_out = aROM_e_data | or_8_out;  // OR_Gate or_11, 32 bits wide
  ROM #(.addrWidth(5), .dataWidth(32)) bROM_f (.addr(and_18_out), .data(bROM_f_data));
  assign and_18_out = Address & {5{Sel_f}};  // AND_Gate and_18, 5 bits wide
  assign or_12_out = bROM_e_data | or_9_out;  // OR_Gate or_12, 32 bits wide
  ROM #(.addrWidth(5), .dataWidth(32)) ROM_g (.addr(and_19_out), .data(ROM_g_data));
  assign and_19_out = Address & {5{Sel_g}};  // AND_Gate and_19, 5 bits wide
  assign or_13_out = ROM_f_data | or_10_out;  // OR_Gate or_13, 32 bits wide
  ROM #(.addrWidth(5), .dataWidth(32)) aROM_g (.addr(and_20_out), .data(aROM_g_data));
  assign and_20_out = Address & {5{Sel_g}};  // AND_Gate and_20, 5 bits wide
  assign or_14_out = aROM_f_data | or_11_out;  // OR_Gate or_14, 32 bits wide
  ROM #(.addrWidth(5), .dataWidth(32)) bROM_g (.addr(and_21_out), .data(bROM_g_data));
  assign and_21_out = Address & {5{Sel_g}};  // AND_Gate and_21, 5 bits wide
  assign or_15_out = bROM_f_data | or_12_out;  // OR_Gate or_15, 32 bits wide
  ROM #(.addrWidth(5), .dataWidth(32)) ROM_h (.addr(and_22_out), .data(ROM_h_data));
  assign and_22_out = Address & {5{Sel_h}};  // AND_Gate and_22, 5 bits wide
  ROM #(.addrWidth(5), .dataWidth(32)) aROM_h (.addr(and_23_out), .data(aROM_h_data));
  assign and_23_out = Address & {5{Sel_h}};  // AND_Gate and_23, 5 bits wide
  ROM #(.addrWidth(5), .dataWidth(32)) bROM_h (.addr(and_24_out), .data(bROM_h_data));
  assign and_24_out = Address & {5{Sel_h}};  // AND_Gate and_24, 5 bits wide
  assign or_16_out = ROM_g_data | or_13_out;  // OR_Gate or_16, 32 bits wide
  assign or_17_out = aROM_g_data | or_14_out;  // OR_Gate or_17, 32 bits wide
  assign or_18_out = bROM_g_data | or_15_out;  // OR_Gate or_18, 32 bits wide
  ROM #(.addrWidth(5), .dataWidth(32)) ROM_i (.addr(and_25_out), .data(ROM_i_data));
  assign and_25_out = Address & {5{Sel_i}};  // AND_Gate and_25, 5 bits wide
  assign or_19_out = ROM_h_data | or_16_out;  // OR_Gate or_19, 32 bits wide
  ROM #(.addrWidth(5), .dataWidth(32)) aROM_i (.addr(and_26_out), .data(aROM_i_data));
  assign and_26_out = Address & {5{Sel_i}};  // AND_Gate and_26, 5 bits wide
  assign or_20_out = aROM_h_data | or_17_out;  // OR_Gate or_20, 32 bits wide
  ROM #(.addrWidth(5), .dataWidth(32)) bROM_i (.addr(and_27_out), .data(bROM_i_data));
  assign and_27_out = Address & {5{Sel_i}};  // AND_Gate and_27, 5 bits wide
  assign or_21_out = bROM_h_data | or_18_out;  // OR_Gate or_21, 32 bits wide
  ROM #(.addrWidth(5), .dataWidth(32)) ROM_j (.addr(and_28_out), .data(ROM_j_data));
  assign and_28_out = Address & {5{Sel_j}};  // AND_Gate and_28, 5 bits wide
  assign or_22_out = ROM_i_data | or_19_out;  // OR_Gate or_22, 32 bits wide
  ROM #(.addrWidth(5), .dataWidth(32)) aROM_j (.addr(and_29_out), .data(aROM_j_data));
  assign and_29_out = Address & {5{Sel_j}};  // AND_Gate and_29, 5 bits wide
  assign or_23_out = aROM_i_data | or_20_out;  // OR_Gate or_23, 32 bits wide
  ROM #(.addrWidth(5), .dataWidth(32)) bROM_j (.addr(and_30_out), .data(bROM_j_data));
  assign and_30_out = Address & {5{Sel_j}};  // AND_Gate and_30, 5 bits wide
  assign or_24_out = bROM_i_data | or_21_out;  // OR_Gate or_24, 32 bits wide
  ROM #(.addrWidth(5), .dataWidth(32)) ROM_k (.addr(and_31_out), .data(ROM_k_data));
  assign and_31_out = Address & {5{Sel_k}};  // AND_Gate and_31, 5 bits wide
  assign or_25_out = ROM_j_data | or_22_out;  // OR_Gate or_25, 32 bits wide
  ROM #(.addrWidth(5), .dataWidth(32)) aROM_k (.addr(and_32_out), .data(aROM_k_data));
  assign and_32_out = Address & {5{Sel_k}};  // AND_Gate and_32, 5 bits wide
  assign or_26_out = aROM_j_data | or_23_out;  // OR_Gate or_26, 32 bits wide
  ROM #(.addrWidth(5), .dataWidth(32)) bROM_k (.addr(and_33_out), .data(bROM_k_data));
  assign and_33_out = Address & {5{Sel_k}};  // AND_Gate and_33, 5 bits wide
  assign or_27_out = bROM_j_data | or_24_out;  // OR_Gate or_27, 32 bits wide
  ROM #(.addrWidth(5), .dataWidth(32)) ROM_l (.addr(and_34_out), .data(ROM_l_data));
  assign and_34_out = Address & {5{Sel_l}};  // AND_Gate and_34, 5 bits wide
  ROM #(.addrWidth(5), .dataWidth(32)) aROM_l (.addr(and_35_out), .data(aROM_l_data));
  assign and_35_out = Address & {5{Sel_l}};  // AND_Gate and_35, 5 bits wide
  ROM #(.addrWidth(5), .dataWidth(32)) bROM_l (.addr(and_36_out), .data(bROM_l_data));
  assign and_36_out = Address & {5{Sel_l}};  // AND_Gate and_36, 5 bits wide
  assign or_28_out = ROM_k_data | or_25_out;  // OR_Gate or_28, 32 bits wide
  assign or_29_out = aROM_k_data | or_26_out;  // OR_Gate or_29, 32 bits wide
  assign or_30_out = bROM_k_data | or_27_out;  // OR_Gate or_30, 32 bits wide
  ROM #(.addrWidth(5), .dataWidth(32)) ROM_m (.addr(and_37_out), .data(ROM_m_data));
  assign and_37_out = Address & {5{Sel_m}};  // AND_Gate and_37, 5 bits wide
  assign or_31_out = ROM_l_data | or_28_out;  // OR_Gate or_31, 32 bits wide
  ROM #(.addrWidth(5), .dataWidth(32)) aROM_m (.addr(and_38_out), .data(aROM_m_data));
  assign and_38_out = Address & {5{Sel_m}};  // AND_Gate and_38, 5 bits wide
  assign or_32_out = aROM_l_data | or_29_out;  // OR_Gate or_32, 32 bits wide
  ROM #(.addrWidth(5), .dataWidth(32)) bROM_m (.addr(and_39_out), .data(bROM_m_data));
  assign and_39_out = Address & {5{Sel_m}};  // AND_Gate and_39, 5 bits wide
  assign or_33_out = bROM_l_data | or_30_out;  // OR_Gate or_33, 32 bits wide
  ROM #(.addrWidth(5), .dataWidth(32)) ROM_n (.addr(and_40_out), .data(ROM_n_data));
  assign and_40_out = Address & {5{Sel_n}};  // AND_Gate and_40, 5 bits wide
  assign or_34_out = ROM_m_data | or_31_out;  // OR_Gate or_34, 32 bits wide
  ROM #(.addrWidth(5), .dataWidth(32)) aROM_n (.addr(and_41_out), .data(aROM_n_data));
  assign and_41_out = Address & {5{Sel_n}};  // AND_Gate and_41, 5 bits wide
  assign or_35_out = aROM_m_data | or_32_out;  // OR_Gate or_35, 32 bits wide
  ROM #(.addrWidth(5), .dataWidth(32)) bROM_n (.addr(and_42_out), .data(bROM_n_data));
  assign and_42_out = Address & {5{Sel_n}};  // AND_Gate and_42, 5 bits wide
  assign or_36_out = bROM_m_data | or_33_out;  // OR_Gate or_36, 32 bits wide
  ROM #(.addrWidth(5), .dataWidth(32)) ROM_o (.addr(and_43_out), .data(ROM_o_data));
  assign and_43_out = Address & {5{Sel_o}};  // AND_Gate and_43, 5 bits wide
  assign or_37_out = ROM_n_data | or_34_out;  // OR_Gate or_37, 32 bits wide
  ROM #(.addrWidth(5), .dataWidth(32)) aROM_o (.addr(and_44_out), .data(aROM_o_data));
  assign and_44_out = Address & {5{Sel_o}};  // AND_Gate and_44, 5 bits wide
  assign or_38_out = aROM_n_data | or_35_out;  // OR_Gate or_38, 32 bits wide
  ROM #(.addrWidth(5), .dataWidth(32)) bROM_o (.addr(and_45_out), .data(bROM_o_data));
  assign and_45_out = Address & {5{Sel_o}};  // AND_Gate and_45, 5 bits wide
  assign or_39_out = bROM_n_data | or_36_out;  // OR_Gate or_39, 32 bits wide
  ROM #(.addrWidth(5), .dataWidth(32)) ROM_p (.addr(and_46_out), .data(ROM_p_data));
  assign and_46_out = Address & {5{Sel_p}};  // AND_Gate and_46, 5 bits wide
  ROM #(.addrWidth(5), .dataWidth(32)) aROM_p (.addr(and_47_out), .data(aROM_p_data));
  assign and_47_out = Address & {5{Sel_p}};  // AND_Gate and_47, 5 bits wide
  ROM #(.addrWidth(5), .dataWidth(32)) bROM_p (.addr(and_48_out), .data(bROM_p_data));
  assign and_48_out = Address & {5{Sel_p}};  // AND_Gate and_48, 5 bits wide
  assign or_40_out = ROM_o_data | or_37_out;  // OR_Gate or_40, 32 bits wide
  assign or_41_out = aROM_o_data | or_38_out;  // OR_Gate or_41, 32 bits wide
  assign or_42_out = bROM_o_data | or_39_out;  // OR_Gate or_42, 32 bits wide
  assign Lines = ROM_p_data | or_40_out;  // OR_Gate or_43, 32 bits wide
  assign Linesa = aROM_p_data | or_41_out;  // OR_Gate or_44, 32 bits wide
  assign Linesb = bROM_p_data | or_42_out;  // OR_Gate or_45, 32 bits wide

  // Notes on the sheet:
  //   contents of aROM_a (hex, n*v repeats v):
  //   0 10000000
  //   contents of bROM_a (hex, n*v repeats v):
  //   0 10000000
endmodule
